// Logisim project 3 trabalho.circ as structural Verilog: 7 circuits, main circuit SUM COMPLETO
// SOMA
module SUM_COMPLETO (
  input  A,
  input  B,
  input  TE,
  output Saida,
  output Ts
);

  wire and_1_out, and_2_out, and_3_out, and_4_out, and_5_out, and_6_out, and_7_out;

  and and_1 (and_1_out, A, B);
  and and_2 (and_2_out, A, TE);
  and and_3 (and_3_out, B, TE);
  and and_4 (and_4_out, ~A, ~B, TE);  // AND_Gate
  and and_5 (and_5_out, ~A, B, ~TE);  // AND_Gate
  and and_6 (and_6_out, A, ~B, ~TE);  // AND_Gate
  and and_7 (and_7_out, A, B, TE);
  or or_1 (Ts, and_1_out, and_2_out, and_3_out);
  or or_2 (Saida, and_4_out, and_5_out, and_6_out, and_7_out);
endmodule

// SUB
module SUB_COMPLETO (
  input  A,
  input  B,
  input  TE,
  output Saida,
  output Ts
);

  wire and_1_out, and_2_out, and_3_out, and_4_out, and_5_out, and_6_out, and_7_out;

  and and_1 (and_1_out, ~A, B);  // AND_Gate
  and and_2 (and_2_out, ~A, TE);  // AND_Gate
  and and_3 (and_3_out, B, TE);
  and and_4 (and_4_out, ~A, ~B, TE);  // AND_Gate
  and and_5 (and_5_out, ~A, B, ~TE);  // AND_Gate
  and and_6 (and_6_out, A, ~B, ~TE);  // AND_Gate
  and and_7 (and_7_out, A, B, TE);
  or or_1 (Ts, and_1_out, and_2_out, and_3_out);
  or or_2 (Saida, and_4_out, and_5_out, and_6_out, and_7_out);
endmodule

// SOMA
module SOMA_4BIT (
  input  n1_1,
  input  n2_1,
  input  n1_2,
  input  n2_2,
  input  n1_3,
  input  n2_3,
  input  n1_4,
  input  n2_4,
  output TS,
  output saida4,
  output saida3,
  output saida2,
  output saida1
);

  wire sum_completo_1_ts, sum_completo_2_ts, sum_completo_3_ts;

  SUM_COMPLETO sum_completo_1 (.Saida(saida1), .Ts(sum_completo_1_ts), .A(n1_1), .B(n2_1), .TE(1'b0));
  SUM_COMPLETO sum_completo_2 (.Saida(saida2), .Ts(sum_completo_2_ts), .A(n1_2), .B(n2_2), .TE(sum_completo_1_ts));
  SUM_COMPLETO sum_completo_3 (.Saida(saida3), .Ts(sum_completo_3_ts), .A(n1_3), .B(n2_3), .TE(sum_completo_2_ts));
  SUM_COMPLETO sum_completo_4 (.Saida(saida4), .Ts(TS), .A(n1_4), .B(n2_4), .TE(sum_completo_3_ts));
endmodule

// SUBTRAÇÃO
module SUB_4BIT (
  input  n1_1,
  input  n2_1,
  input  n1_2,
  input  n2_2,
  input  n1_3,
  input  n2_3,
  input  n1_4,
  input  n2_4,
  output TS,
  output saida4,
  output saida3,
  output saida2,
  output saida1
);

  wire sub_completo_1_ts, sub_completo_2_ts, sub_completo_3_ts;

  SUB_COMPLETO sub_completo_1 (.Saida(saida1), .Ts(sub_completo_1_ts), .A(n1_1), .B(n2_1), .TE(1'b0));
  SUB_COMPLETO sub_completo_2 (.Saida(saida2), .Ts(sub_completo_2_ts), .A(n1_2), .B(n2_2), .TE(sub_completo_1_ts));
  SUB_COMPLETO sub_completo_3 (.Saida(saida3), .Ts(sub_completo_3_ts), .A(n1_3), .B(n2_3), .TE(sub_completo_2_ts));
  SUB_COMPLETO sub_completo_4 (.Saida(saida4), .Ts(TS), .A(n1_4), .B(n2_4), .TE(sub_completo_3_ts));
endmodule

module deslocamento (
  input  a1,
  input  a2,
  input  a3,
  input  a4,
  input  b1,
  input  b2,
  input  b3,
  input  b4,
  output a4_2,
  output a3_2,
  output a2_2,
  output a1_2
);

  Multiplexer multiplexer_1 (.in0(1'b0), .in1(a3), .out(a4_2), .sel(b4));  // open: en
  Multiplexer multiplexer_2 (.in0(a4), .in1(a2), .out(a3_2), .sel(b4));  // open: en
  Multiplexer multiplexer_3 (.in0(a3), .in1(a1), .out(a2_2), .sel(b4));  // open: en
  Multiplexer multiplexer_4 (.in0(a2), .in1(1'b0), .out(a1_2), .sel(b4));  // open: en

  assign b2 = b1;
  assign b3 = b1;
  // also tied to GND on the sheet: b1
endmodule

// compador
module comparador (
  input  a1,
  input  a2,
  input  a3,
  input  a4,
  input  b1,
  input  b2,
  input  b3,
  input  b4,
  output s4,
  output s3,
  output s2,
  output s1
);

  wire xnor_1_out, xnor_2_out, xnor_3_out, xnor_4_out;

  xnor xnor_1 (xnor_1_out, a4, b4);
  xnor xnor_2 (xnor_2_out, a3, b3);
  xnor xnor_3 (xnor_3_out, a2, b2);
  xnor xnor_4 (xnor_4_out, a1, b1);
  and and_1 (s4, xnor_1_out, xnor_2_out, xnor_3_out, xnor_4_out);

  assign s1 = 1'b0;
  assign s2 = 1'b0;
  assign s3 = 1'b0;
endmodule

module projetoCompleto (
  input  a1,
  input  a2,
  input  a3,
  input  a4,
  input  [1:0] in_5,
  input  b1,
  input  b2,
  input  b3,
  input  b4,
  output overflow,
  output s4,
  output s3,
  output s2,
  output s1
);

  wire comparador_1_s1, comparador_1_s2, comparador_1_s3, comparador_1_s4, deslocamento_1_a1_2,
       deslocamento_1_a2_2, deslocamento_1_a3_2, deslocamento_1_a4_2, soma_4bit_1_saida1, soma_4bit_1_saida2,
       soma_4bit_1_saida3, soma_4bit_1_saida4, soma_4bit_1_ts, sub_4bit_1_saida1, sub_4bit_1_saida2,
       sub_4bit_1_saida3, sub_4bit_1_saida4, sub_4bit_1_ts;

  SOMA_4BIT soma_4bit_1 (
    .TS(soma_4bit_1_ts), .saida4(soma_4bit_1_saida4), .saida3(soma_4bit_1_saida3),
    .saida2(soma_4bit_1_saida2), .saida1(soma_4bit_1_saida1), .n1_1(a4), .n1_3(a2), .n2_1(b4), .n2_3(b2),
    .n1_2(a3), .n1_4(a1), .n2_2(b3), .n2_4(b1));
  SUB_4BIT sub_4bit_1 (
    .TS(sub_4bit_1_ts), .saida4(sub_4bit_1_saida4), .saida3(sub_4bit_1_saida3), .saida2(sub_4bit_1_saida2),
    .saida1(sub_4bit_1_saida1), .n1_1(a4), .n1_3(a2), .n2_1(b4), .n2_3(b2), .n1_2(a3), .n1_4(a1), .n2_2(b3),
    .n2_4(b1));
  deslocamento deslocamento_1 (
    .a4_2(deslocamento_1_a4_2), .a3_2(deslocamento_1_a3_2), .a2_2(deslocamento_1_a2_2),
    .a1_2(deslocamento_1_a1_2), .b1(b1), .a1(a1), .b2(b2), .a2(a2), .b3(b3), .a3(a3), .b4(b4), .a4(a4));
  comparador comparador_1 (
    .s4(comparador_1_s4), .s3(comparador_1_s3), .s2(comparador_1_s2), .s1(comparador_1_s1), .a1(a1), .a2(a2),
    .a3(a3), .a4(a4), .b1(b1), .b2(b2), .b3(b3), .b4(b4));
  Multiplexer #(.select(2)) multiplexer_1 (
    .in0(soma_4bit_1_ts), .in1(sub_4bit_1_ts), .in2(1'b0), .in3(1'b0), .out(overflow), .sel(in_5));  // open: en
  Multiplexer #(.select(2)) multiplexer_2 (
    .in0(soma_4bit_1_saida4), .in1(sub_4bit_1_saida4), .in2(deslocamento_1_a4_2), .in3(comparador_1_s4),
    .out(s4), .sel(in_5));  // open: en
  Multiplexer #(.select(2)) multiplexer_3 (
    .in0(soma_4bit_1_saida3), .in1(sub_4bit_1_saida3), .in2(deslocamento_1_a3_2), .in3(comparador_1_s3),
    .out(s3), .sel(in_5));  // open: en
  Multiplexer #(.select(2)) multiplexer_4 (
    .in0(soma_4bit_1_saida2), .in1(sub_4bit_1_saida2), .in2(deslocamento_1_a2_2), .in3(comparador_1_s2),
    .out(s2), .sel(in_5));  // open: en
  Multiplexer #(.select(2)) multiplexer_5 (
    .in0(soma_4bit_1_saida1), .in1(sub_4bit_1_saida1), .in2(deslocamento_1_a1_2), .in3(comparador_1_s1),
    .out(s1), .sel(in_5));  // open: en

  // Notes on the sheet:
  //   0.0 == sum
  //   0.1 == sub
  //   1.0 == deslocamento
  //   1.1 == comparador
endmodule
