// Logisim project 4 tarefa.circ as structural Verilog: 2 circuits, main circuit saidaLetras
module saidaLetras (
  input  A,
  input  B,
  input  C,
  output a_2,
  output b_2,
  output c_2,
  output d,
  output e,
  output f,
  output g
);

  wire and_1_out, and_2_out, and_3_out, and_4_out, and_5_out, and_6_out, and_7_out, and_8_out, and_9_out,
       and_10_out, and_11_out, not_1_out, not_2_out, not_3_out, not_4_out, not_5_out, not_6_out, not_7_out,
       not_8_out, not_9_out, not_10_out, not_11_out, not_12_out, not_13_out, not_14_out, not_15_out,
       not_16_out, not_17_out, not_18_out, not_19_out, not_20_out, not_21_out, not_22_out;

  not not_1 (not_1_out, A);
  not not_2 (not_2_out, C);
  not not_3 (not_3_out, B);
  not not_4 (not_4_out, A);
  not not_5 (not_5_out, B);
  not not_6 (not_6_out, A);
  not not_7 (not_7_out, C);
  not not_8 (not_8_out, B);
  not not_9 (not_9_out, A);
  not not_10 (not_10_out, C);
  not not_11 (not_11_out, B);
  not not_12 (not_12_out, C);
  not not_13 (not_13_out, A);
  not not_14 (not_14_out, B);
  not not_15 (not_15_out, B);
  not not_16 (not_16_out, C);
  not not_17 (not_17_out, A);
  not not_18 (not_18_out, B);
  not not_19 (not_19_out, A);
  not not_20 (not_20_out, C);
  and and_1 (and_1_out, not_1_out, B, not_2_out);
  and and_2 (and_2_out, A, not_3_out);
  and and_3 (and_3_out, not_4_out, not_5_out, C);
  and and_4 (and_4_out, not_6_out, B, not_7_out);
  and and_5 (and_5_out, not_8_out, C);
  and and_6 (and_6_out, not_9_out, B, not_10_out);
  and and_7 (and_7_out, not_11_out, not_12_out);
  and and_8 (and_8_out, not_13_out, B, C);
  and and_9 (and_9_out, A, not_14_out);
  not not_21 (not_21_out, A);
  and and_10 (and_10_out, not_15_out, not_16_out);
  or or_1 (f, not_17_out, not_18_out);
  and and_11 (and_11_out, not_19_out, not_20_out);
  not not_22 (not_22_out, B);
  or or_2 (a_2, and_1_out, and_2_out);
  or or_3 (b_2, and_3_out, and_4_out);
  or or_4 (c_2, and_5_out, and_6_out);
  or or_5 (d, and_7_out, and_8_out, and_9_out);
  or or_6 (e, not_21_out, and_10_out);
  or or_7 (g, and_11_out, not_22_out);
endmodule

module display (
  input  A,
  input  B,
  input  C
);

  wire saidaletras_1_a_2, saidaletras_1_b_2, saidaletras_1_c_2, saidaletras_1_d, saidaletras_1_e,
       saidaletras_1_f, saidaletras_1_g;

  saidaLetras saidaletras_1 (
    .A(A), .B(B), .C(C), .a_2(saidaletras_1_a_2), .b_2(saidaletras_1_b_2), .c_2(saidaletras_1_c_2),
    .d(saidaletras_1_d), .e(saidaletras_1_e), .f(saidaletras_1_f), .g(saidaletras_1_g));
  _7_Segment_Display u_7_segment_display_1 (
    .g(saidaletras_1_g), .f(saidaletras_1_f), .a(saidaletras_1_a_2), .b(saidaletras_1_b_2),
    .e(saidaletras_1_e), .d(saidaletras_1_d), .c(saidaletras_1_c_2));  // open: dp

  // Notes on the sheet:
  //   000-T, 001-H , 010-A,011-L,100-E,101-S
endmodule
