// Logisim project C1.circ as structural Verilog: 1 circuit, main circuit main
module main (
  input  X,
  input  Y,
  input  Z,
  output out_4
);

  wire not_1_out, or_1_out;

  not not_1 (not_1_out, Z);
  or or_1 (or_1_out, Y, not_1_out);
  and and_1 (out_4, X, or_1_out);
endmodule
