// Logisim project C3.circ as structural Verilog: 3 circuits, main circuit main
module main (
  input  Sel,
  input  in_2,
  input  in_3,
  input  A,
  input  B,
  input  in_6,
  input  in_7,
  input  in_8,
  input  in_9,
  input  [1:0] in_10,
  input  in_11,
  output S,
  output out_13,
  output S_2,
  output out_15
);

  Multiplexer multiplexer_1 (.in0(A), .in1(B), .out(S), .sel(Sel));  // open: en
  n_sesi n_sesi_1 (.Sel(Sel), .A(A), .B(B), .S(S_2));
  muxhel4 muxhel4_1 (.A(in_6), .B(in_7), .C(in_8), .D(in_9), .Sel1(in_2), .Sel2(in_3), .S(out_13));
  Multiplexer #(.select(2)) multiplexer_2 (
    .in0(in_6), .in1(in_7), .in2(in_8), .in3(in_9), .out(out_15), .sel(in_10), .en(in_11));
endmodule

module n_sesi (
  input  Sel,
  input  A,
  input  B,
  output S
);

  wire and_1_out, and_2_out, not_1_out;

  not not_1 (not_1_out, Sel);
  and and_1 (and_1_out, not_1_out, A);
  and and_2 (and_2_out, Sel, B);
  or or_1 (S, and_1_out, and_2_out);
endmodule

module muxhel4 (
  input  Sel1,
  input  Sel2,
  input  A,
  input  B,
  input  C,
  input  D,
  output S
);

  wire and_1_out, and_2_out, and_3_out, and_4_out, and_5_out, and_6_out, and_7_out, and_8_out, not_1_out,
       not_2_out, not_3_out, not_4_out;

  not not_1 (not_1_out, Sel1);
  not not_2 (not_2_out, Sel1);
  not not_3 (not_3_out, Sel2);
  not not_4 (not_4_out, Sel1);
  and and_1 (and_1_out, not_1_out, not_2_out);
  and and_2 (and_2_out, Sel1, not_3_out);
  and and_3 (and_3_out, not_4_out, Sel2);
  and and_4 (and_4_out, Sel1, Sel2);
  and and_5 (and_5_out, and_1_out, A);
  and and_6 (and_6_out, and_2_out, B);
  and and_7 (and_7_out, and_3_out, C);
  and and_8 (and_8_out, and_4_out, D);
  or or_1 (S, and_5_out, and_6_out, and_7_out, and_8_out);
endmodule
