// Logisim project CLOCK.circ as structural Verilog: 7 circuits, main circuit main
module main (
  input  PR,
  input  J,
  input  CLOCK,
  input  K,
  input  CLR,
  output Q,
  output Q_
);

  wire clock_1_out, nand_1_out, nand_2_out, nand_3_out, nand_4_out, nand_5_out, nand_6_out, not_1_out;

  Clock clock_1 (.out(clock_1_out));
  nand nand_1 (nand_1_out, J, clock_1_out, Q_);
  nand nand_2 (nand_2_out, Q, clock_1_out, K);
  not not_1 (not_1_out, clock_1_out);
  nand nand_3 (nand_3_out, nand_1_out, PR, nand_4_out);
  nand nand_4 (nand_4_out, nand_3_out, CLR, nand_2_out);
  nand nand_5 (nand_5_out, nand_3_out, not_1_out);
  nand nand_6 (nand_6_out, nand_4_out, not_1_out);
  nand nand_7 (Q, nand_5_out, PR, Q_);
  nand nand_8 (Q_, Q, CLR, nand_6_out);
endmodule

module flip_flop_m_s (
  input  J,
  input  CLOCK,
  input  K,
  output Q,
  output Q_
);

  wire nand_1_out, nand_2_out, nand_3_out, nand_4_out, nand_5_out, nand_6_out, not_1_out;

  nand nand_1 (nand_1_out, J, CLOCK, Q_);
  nand nand_2 (nand_2_out, Q, CLOCK, K);
  nand nand_3 (nand_3_out, nand_1_out, nand_4_out);
  nand nand_4 (nand_4_out, nand_3_out, nand_2_out);
  not not_1 (not_1_out, CLOCK);
  nand nand_5 (nand_5_out, nand_3_out, not_1_out);
  nand nand_6 (nand_6_out, nand_4_out, not_1_out);
  nand nand_7 (Q, nand_5_out, Q_);
  nand nand_8 (Q_, Q, nand_6_out);
endmodule

module \and  (
  input  in_1,
  input  in_2,
  input  in_3,
  input  in_4,
  input  in_5,
  input  in_6,
  output out_7,
  output out_8,
  output out_9,
  output out_10,
  output out_11
);

  wire and_2_out, and_4_out, nand_2_out;

  and and_1 (out_7, in_1, in_3, in_5);
  and and_2 (and_2_out, in_1, in_3);
  and and_3 (out_9, and_2_out, in_5);
  nand nand_1 (out_8, in_2, in_4, in_6);
  nand nand_2 (nand_2_out, in_2, in_4);
  and and_4 (and_4_out, in_2, in_4);
  nand nand_3 (out_10, nand_2_out, in_6);
  nand nand_4 (out_11, and_4_out, in_6);

  // Notes on the sheet:
  //   __________________________________
  //   ________________________________________
endmodule

module ous (
  input  in_1,
  input  in_2,
  input  in_3,
  output out_4,
  output out_5
);

  wire xor_2_out;

  ExactlyOne xor_1 (.out(out_4), .in1(in_1), .in2(in_2), .in3(in_3));
  xor xor_2 (xor_2_out, in_1, in_2);
  xor xor_3 (out_5, xor_2_out, in_3);
endmodule

module clocka (
  input  PR,
  input  J,
  input  CLOCK,
  input  K,
  input  CLR,
  output Q,
  output Q_
);

  wire nand_1_out, nand_2_out, nand_3_out, nand_4_out, nand_5_out, nand_6_out, not_1_out;

  Clock u_clock ();  // open: out
  nand nand_1 (nand_1_out, J, CLOCK, Q_);
  nand nand_2 (nand_2_out, Q, CLOCK, K);
  not not_1 (not_1_out, CLOCK);
  nand nand_3 (nand_3_out, nand_1_out, PR, nand_4_out);
  nand nand_4 (nand_4_out, nand_3_out, CLR, nand_2_out);
  nand nand_5 (nand_5_out, nand_3_out, not_1_out);
  nand nand_6 (nand_6_out, nand_4_out, not_1_out);
  nand nand_7 (Q, nand_5_out, PR, Q_);
  nand nand_8 (Q_, Q, CLR, nand_6_out);
endmodule

module flip_flopT (
  input  in_1,
  input  in_2,
  input  in_3,
  input  in_4,
  input  in_5,
  input  in_6,
  input  in_7,
  input  in_8,
  input  in_9,
  input  in_10,
  input  in_11,
  input  in_12,
  output out_13,
  output out_14,
  output out_15,
  output out_16,
  output out_17,
  output out_18,
  output out_19,
  output out_20
);

  wire clock_1_out;

  Clock clock_1 (.out(clock_1_out));
  clocka clocka_1 (.PR(in_11), .J(in_6), .CLOCK(clock_1_out), .K(in_6), .CLR(in_12), .Q(out_17), .Q_(out_16));
  clocka clocka_2 (.PR(in_9), .J(in_3), .CLOCK(out_17), .K(in_3), .CLR(in_10), .Q(out_18), .Q_(out_15));
  clocka clocka_3 (.PR(in_7), .J(in_2), .CLOCK(out_18), .K(in_2), .CLR(in_8), .Q(out_19), .Q_(out_14));
  clocka clocka_4 (.PR(in_4), .J(in_1), .CLOCK(out_19), .K(in_1), .CLR(in_5), .Q(out_20), .Q_(out_13));
endmodule

module clockss (
  input  in_1,
  input  in_2,
  input  in_3,
  output out_4,
  output out_5
);

  wire clock_1_out, not_1_out;

  not not_1 (not_1_out, in_1);
  Clock clock_1 (.out(clock_1_out));
  clocka clocka_1 (.PR(in_2), .J(in_1), .CLOCK(clock_1_out), .K(not_1_out), .CLR(in_3), .Q(out_4), .Q_(out_5));
endmodule
