// Logisim project FAIL.circ as structural Verilog: 4 circuits, main circuit main
module main (
  input  in_1,
  input  in_2,
  input  in_3,
  input  in_4,
  input  in_5,
  input  in_6
);
endmodule

module SUB (
  input  A,
  input  B,
  output S,
  output Ts
);

  wire and_1_out, and_2_out, not_1_out, not_2_out, not_3_out;

  not not_1 (not_1_out, A);
  not not_2 (not_2_out, B);
  not not_3 (not_3_out, A);
  and and_1 (and_1_out, not_1_out, B);
  and and_2 (and_2_out, A, not_2_out);
  and and_3 (Ts, not_3_out, B);
  or or_1 (S, and_1_out, and_2_out);
endmodule

module SUB2 (
  input  A,
  input  B,
  input  Te,
  output S,
  output Te2
);

  wire and_1_out, and_2_out, and_3_out, and_4_out, and_5_out, and_6_out, and_7_out, and_8_out, and_9_out,
       and_10_out, and_11_out, not_1_out, not_2_out, not_3_out, not_4_out, not_5_out, not_6_out, not_7_out,
       not_8_out, or_1_out, or_2_out, or_3_out;

  not not_1 (not_1_out, A);
  not not_2 (not_2_out, B);
  not not_3 (not_3_out, A);
  not not_4 (not_4_out, B);
  not not_5 (not_5_out, A);
  not not_6 (not_6_out, A);
  and and_1 (and_1_out, not_1_out, not_2_out);
  and and_2 (and_2_out, not_3_out, B);
  not not_7 (not_7_out, Te);
  and and_3 (and_3_out, A, not_4_out);
  not not_8 (not_8_out, Te);
  and and_4 (and_4_out, A, B);
  and and_5 (and_5_out, not_5_out, Te);
  and and_6 (and_6_out, not_6_out, B);
  and and_7 (and_7_out, and_1_out, Te);
  and and_8 (and_8_out, and_2_out, not_7_out);
  and and_9 (and_9_out, and_3_out, not_8_out);
  and and_10 (and_10_out, and_4_out, Te);
  or or_1 (or_1_out, and_5_out, and_6_out);
  and and_11 (and_11_out, B, Te);
  or or_2 (or_2_out, and_7_out, and_8_out);
  or or_3 (or_3_out, and_9_out, and_10_out);
  or or_4 (Te2, or_1_out, and_11_out);
  or or_5 (S, or_2_out, or_3_out);
endmodule

module SUM (
  input  in_1,
  input  in_2,
  input  in_3,
  input  in_4
);
endmodule
