// Logisim project MAIN.circ as structural Verilog
module main (
  input  in_1,
  input  in_2,
  input  in_3,
  input  in_4,
  input  in_5,
  input  in_6,
  input  in_7,
  input  in_8,
  input  in_9,
  input  in_10,
  input  in_11,
  input  in_12,
  input  in_13,
  input  in_14,
  input  in_15,
  input  in_16,
  output out_17,
  output out_18,
  output out_19,
  output out_20,
  output out_21,
  output out_22,
  output out_23,
  output out_24,
  output out_25,
  output out_26
);

  wire seila_1_ts, seila_2_ts, seila_3_ts, sub2_1_te_2, sub2_2_te_2, sub_1_ts;

  seila seila_1 (.A(in_4), .B(in_12), .Te(1'b0), .S(out_17), .Ts(seila_1_ts));
  seila seila_2 (.A(seila_1_ts), .B(in_3), .Te(in_11), .S(out_19), .Ts(seila_2_ts));
  seila seila_3 (.A(seila_2_ts), .B(in_2), .Te(in_10), .S(out_21), .Ts(seila_3_ts));
  seila seila_4 (.A(seila_3_ts), .B(in_1), .Te(in_9), .S(out_23), .Ts(out_25));
  SUB sub_1 (.A(in_8), .B(in_16), .S(out_18), .Ts(sub_1_ts));
  SUB2 sub2_1 (.A(sub_1_ts), .B(in_7), .Te(in_15), .S(out_20), .Te_2(sub2_1_te_2));
  SUB2 sub2_2 (.A(sub2_1_te_2), .B(in_6), .Te(in_14), .S(out_22), .Te_2(sub2_2_te_2));
  SUB2 sub2_3 (.A(sub2_2_te_2), .B(in_5), .Te(in_13), .S(out_24), .Te_2(out_26));
endmodule

module OUT (
  input  A,
  input  B,
  output S,
  output Ts
);

  wire and_2_out, and_3_out, not_1_out, not_2_out;

  not not_1 (not_1_out, A);
  not not_2 (not_2_out, B);
  and and_1 (Ts, B, A);
  and and_2 (and_2_out, not_1_out, B);
  and and_3 (and_3_out, not_2_out, A);
  or or_1 (S, and_2_out, and_3_out);
endmodule

module circ1tent (
  input  A,
  input  B,
  output S,
  output Ts,
  output out_5
);

  wire and_2_out, and_3_out, not_1_out, not_2_out;

  not not_1 (not_1_out, A);
  not not_2 (not_2_out, B);
  and and_1 (Ts, B, A);
  xor xor_1 (out_5, A, B);
  and and_2 (and_2_out, not_1_out, B);
  and and_3 (and_3_out, not_2_out, A);
  or or_1 (S, and_2_out, and_3_out);
endmodule

module seila (
  input  A,
  input  B,
  input  Te,
  output S,
  output Ts
);

  wire and_1_out, and_2_out, and_3_out, and_4_out, and_5_out, and_6_out, and_7_out, and_8_out, and_9_out,
       and_10_out, and_11_out, not_1_out, not_2_out, not_3_out, not_4_out, not_5_out, not_6_out, or_1_out,
       or_3_out, or_4_out;

  not not_1 (not_1_out, A);
  not not_2 (not_2_out, B);
  not not_3 (not_3_out, A);
  not not_4 (not_4_out, B);
  and and_1 (and_1_out, B, Te);
  and and_2 (and_2_out, A, Te);
  and and_3 (and_3_out, not_1_out, not_2_out);
  and and_4 (and_4_out, not_3_out, B);
  not not_5 (not_5_out, Te);
  and and_5 (and_5_out, A, not_4_out);
  not not_6 (not_6_out, Te);
  and and_6 (and_6_out, A, B);
  or or_1 (or_1_out, and_1_out, and_2_out);
  and and_7 (and_7_out, A, B);
  and and_8 (and_8_out, and_3_out, Te);
  and and_9 (and_9_out, and_4_out, not_5_out);
  and and_10 (and_10_out, and_5_out, not_6_out);
  and and_11 (and_11_out, and_6_out, Te);
  or or_2 (Ts, or_1_out, and_7_out);
  or or_3 (or_3_out, and_8_out, and_9_out);
  or or_4 (or_4_out, and_10_out, and_11_out);
  or or_5 (S, or_3_out, or_4_out);
endmodule

module SUB (
  input  A,
  input  B,
  output S,
  output Ts
);

  wire and_1_out, and_2_out, not_1_out, not_2_out, not_3_out;

  not not_1 (not_1_out, A);
  not not_2 (not_2_out, B);
  not not_3 (not_3_out, A);
  and and_1 (and_1_out, not_1_out, B);
  and and_2 (and_2_out, A, not_2_out);
  and and_3 (Ts, not_3_out, B);
  or or_1 (S, and_1_out, and_2_out);
endmodule

module SUB2 (
  input  A,
  input  B,
  input  Te,
  output S,
  output Te_2
);

  wire and_1_out, and_2_out, and_3_out, and_4_out, and_5_out, and_6_out, and_7_out, and_8_out, and_9_out,
       and_10_out, and_11_out, not_1_out, not_2_out, not_3_out, not_4_out, not_5_out, not_6_out, not_7_out,
       not_8_out, or_1_out, or_2_out, or_3_out;

  not not_1 (not_1_out, A);
  not not_2 (not_2_out, B);
  not not_3 (not_3_out, A);
  not not_4 (not_4_out, B);
  not not_5 (not_5_out, A);
  not not_6 (not_6_out, A);
  and and_1 (and_1_out, not_1_out, not_2_out);
  and and_2 (and_2_out, not_3_out, B);
  not not_7 (not_7_out, Te);
  and and_3 (and_3_out, A, not_4_out);
  not not_8 (not_8_out, Te);
  and and_4 (and_4_out, A, B);
  and and_5 (and_5_out, not_5_out, Te);
  and and_6 (and_6_out, not_6_out, B);
  and and_7 (and_7_out, and_1_out, Te);
  and and_8 (and_8_out, and_2_out, not_7_out);
  and and_9 (and_9_out, and_3_out, not_8_out);
  and and_10 (and_10_out, and_4_out, Te);
  or or_1 (or_1_out, and_5_out, and_6_out);
  and and_11 (and_11_out, B, Te);
  or or_2 (or_2_out, and_7_out, and_8_out);
  or or_3 (or_3_out, and_9_out, and_10_out);
  or or_4 (Te_2, or_1_out, and_11_out);
  or or_5 (S, or_2_out, or_3_out);
endmodule
