// Logisim project MIC-1.circ as structural Verilog: 1 circuit, main circuit main
module main (
  input  in_1,
  input  [3:0] in_2,
  input  [1:0] ALU,
  input  AMUX,
  input  [3:0] B,
  input  [1:0] SH,
  input  [3:0] A,
  input  in_8,
  output N,
  output Z
);

  wire and_2_out, and_4_out, and_6_out, and_7_out, decoder_1_out0, decoder_1_out1, decoder_1_out2,
       decoder_1_out3, decoder_1_out4, decoder_1_out5, decoder_1_out6, decoder_1_out7, decoder_1_out8,
       decoder_1_out9, decoder_1_out10, decoder_1_out11, decoder_1_out12, decoder_1_out13, decoder_1_out14,
       decoder_1_out15, xnor_1_out;
  wire [3:0] _0_q, A_q, AC_q, adder_1_out, AMASK_q, and_1_out, and_5_out, B_q, C_q, D_q, E_q, F_q, IR_q,
       MBR_q, minus_1_q, multiplexer_1_out, multiplexer_2_out, multiplexer_3_out, multiplexer_4_out,
       multiplexer_5_out, multiplexer_6_out, not_1_out, PC_q, plus_1_q, SMASK_q, SP_q, TIR_q;

  Decoder #(.select(4), .enable("false")) decoder_1 (
    .out0(decoder_1_out0), .out1(decoder_1_out1), .out2(decoder_1_out2), .out3(decoder_1_out3),
    .out4(decoder_1_out4), .out5(decoder_1_out5), .out6(decoder_1_out6), .out7(decoder_1_out7),
    .out8(decoder_1_out8), .out9(decoder_1_out9), .out10(decoder_1_out10), .out11(decoder_1_out11),
    .out12(decoder_1_out12), .out13(decoder_1_out13), .out14(decoder_1_out14), .out15(decoder_1_out15));  // open: sel
  Register #(.width(4)) PC (.D(multiplexer_5_out), .en(decoder_1_out0), .Q(PC_q));  // open: clk, clr
  Register #(.width(4)) AC (.D(multiplexer_5_out), .en(decoder_1_out1), .Q(AC_q));  // open: clk, clr
  Register #(.width(4)) SP (.D(multiplexer_5_out), .en(decoder_1_out2), .Q(SP_q));  // open: clk, clr
  Register #(.width(4)) IR (.D(multiplexer_5_out), .en(decoder_1_out3), .Q(IR_q));  // open: clk, clr
  Register #(.width(4)) TIR (.D(multiplexer_5_out), .en(decoder_1_out4), .Q(TIR_q));  // open: clk, clr
  Register #(.width(4)) _0 (.D(multiplexer_5_out), .en(decoder_1_out5), .Q(_0_q), .clr(in_8));  // open: clk
  Register #(.width(4)) plus_1 (.D(multiplexer_5_out), .en(decoder_1_out6), .Q(plus_1_q));  // open: clk, clr
  Register #(.width(4)) minus_1 (.D(multiplexer_5_out), .en(decoder_1_out7), .Q(minus_1_q));  // open: clk, clr
  Register #(.width(4)) AMASK (.D(multiplexer_5_out), .en(decoder_1_out8), .Q(AMASK_q));  // open: clk, clr
  Register #(.width(4)) SMASK (.D(multiplexer_5_out), .en(decoder_1_out9), .Q(SMASK_q));  // open: clk, clr
  Register #(.width(4)) u_A (.D(multiplexer_5_out), .en(decoder_1_out10), .Q(A_q));  // open: clk, clr
  Register #(.width(4)) u_B (.D(multiplexer_5_out), .en(decoder_1_out11), .Q(B_q));  // open: clk, clr
  Register #(.width(4)) C (.D(multiplexer_5_out), .en(decoder_1_out12), .Q(C_q));  // open: clk, clr
  Register #(.width(4)) D (.D(multiplexer_5_out), .en(decoder_1_out13), .Q(D_q));  // open: clk, clr
  Register #(.width(4)) E (.D(multiplexer_5_out), .en(decoder_1_out14), .Q(E_q));  // open: clk, clr
  Register #(.width(4)) F (.D(multiplexer_5_out), .en(decoder_1_out15), .Q(F_q));  // open: clk, clr
  Multiplexer #(.select(4), .width(4), .enable("false")) multiplexer_1 (
    .in0(PC_q), .in1(AC_q), .in2(SP_q), .in3(IR_q), .in4(TIR_q), .in5(_0_q), .in6(plus_1_q), .in7(minus_1_q),
    .in8(AMASK_q), .in9(SMASK_q), .in10(A_q), .in11(B_q), .in12(C_q), .in13(D_q), .in14(E_q), .in15(F_q),
    .out(multiplexer_1_out), .sel(B));
  Multiplexer #(.select(4), .width(4), .enable("false")) multiplexer_2 (
    .in0(PC_q), .in1(AC_q), .in2(SP_q), .in3(IR_q), .in4(TIR_q), .in5(_0_q), .in6(plus_1_q), .in7(minus_1_q),
    .in8(AMASK_q), .in9(SMASK_q), .in10(A_q), .in11(B_q), .in12(C_q), .in13(D_q), .in14(E_q), .in15(F_q),
    .out(multiplexer_2_out), .sel(A));
  Register #(.width(3)) MAR (.D(multiplexer_1_out[2:0]));  // open: en, Q, clk, clr
  Register #(.width(4)) MBR (.D(multiplexer_3_out), .Q(MBR_q));  // open: en, clk, clr
  Multiplexer #(.width(4), .enable("false")) multiplexer_3 (.out(multiplexer_3_out));  // open: in0, in1, sel
  Adder #(.width(4)) adder_1 (
    .a(multiplexer_1_out), .b(multiplexer_4_out), .out(adder_1_out), .cin(in_1));  // open: cout
  Multiplexer #(.width(4), .enable("false")) multiplexer_4 (
    .in0(multiplexer_2_out), .in1(MBR_q), .out(multiplexer_4_out), .sel(AMUX));
  assign and_1_out = multiplexer_1_out & multiplexer_4_out;  // AND_Gate and_1, 4 bits wide
  assign not_1_out = ~multiplexer_4_out;  // NOT_Gate not_1, 4 bits wide
  and and_2 (and_2_out, multiplexer_6_out[3], SH[0]);
  xnor xnor_1 (xnor_1_out, SH[1], SH[0]);
  Multiplexer #(.width(4), .enable("false")) multiplexer_5 (
    .in0(and_5_out), .in1(multiplexer_6_out), .out(multiplexer_5_out), .sel(xnor_1_out));
  Multiplexer #(.select(2), .width(4), .enable("false")) multiplexer_6 (
    .in0(adder_1_out), .in1(and_1_out), .in2(multiplexer_4_out), .in3(not_1_out), .out(multiplexer_6_out),
    .sel(ALU));
  and and_3 (and_5_out[3], SH[1], multiplexer_6_out[2]);
  and and_4 (and_4_out, multiplexer_6_out[2], SH[0]);
  or or_1 (and_5_out[2], and_2_out, and_6_out);
  Comparator #(.width(4)) comparator_1 (.a(in_2), .b(multiplexer_6_out), .gt(N), .eq(Z));  // open: lt
  and and_5 (and_5_out[0], multiplexer_6_out[1], SH[0]);
  and and_6 (and_6_out, SH[1], multiplexer_6_out[1]);
  or or_2 (and_5_out[1], and_4_out, and_7_out);
  and and_7 (and_7_out, SH[1], multiplexer_6_out[0]);
endmodule
