// Logisim project Muxes.circ as structural Verilog: 6 circuits, main circuit main
module main (
  input  a,
  input  b,
  input  c,
  input  d,
  input  e,
  input  f,
  input  g,
  input  h,
  input  in_9,
  input  in_10,
  input  in_11,
  input  i,
  input  j,
  input  k,
  input  l,
  input  m,
  input  in_17,
  input  n,
  input  o,
  input  p,
  output S
);

  wire muxde8_1_1_s, muxde8_1_2_s;

  MuxDe8_1 muxde8_1_1 (
    .a(a), .b(b), .c(c), .d(d), .e(e), .f(f), .g(g), .h(h), .Sel1(in_9), .Sel2(in_10), .Sel3(in_11),
    .S(muxde8_1_1_s));
  MuxDe8_1 muxde8_1_2 (
    .a(i), .b(j), .c(k), .d(l), .e(m), .f(n), .g(o), .h(p), .Sel1(in_9), .Sel2(in_10), .Sel3(in_11),
    .S(muxde8_1_2_s));
  MuxDe8_1 muxde8_1_3 (
    .a(muxde8_1_1_s), .h(muxde8_1_2_s), .Sel1(in_17), .Sel2(in_17), .Sel3(in_17), .S(S));  // open: b, c, d, e, f, g
endmodule

module MuxDe2_1 (
  input  a,
  input  b,
  input  c,
  output S
);

  wire and_1_out, and_2_out, not_1_out;

  not not_1 (not_1_out, c);
  and and_1 (and_1_out, a, not_1_out);
  and and_2 (and_2_out, b, c);
  or or_1 (S, and_1_out, and_2_out);
endmodule

module MuxDe4_1 (
  input  a,
  input  b,
  input  c,
  input  d,
  input  Sel1,
  input  Sel2,
  output out_7
);

  wire and_1_out, and_2_out, and_3_out, and_4_out, not_1_out, not_2_out, not_3_out, not_4_out;

  not not_1 (not_1_out, Sel1);
  not not_2 (not_2_out, Sel2);
  not not_3 (not_3_out, Sel1);
  not not_4 (not_4_out, Sel2);
  and and_1 (and_1_out, a, not_1_out, not_2_out);
  and and_2 (and_2_out, b, not_3_out, Sel2);
  and and_3 (and_3_out, c, Sel1, not_4_out);
  and and_4 (and_4_out, d, Sel1, Sel2);
  or or_1 (out_7, and_1_out, and_2_out, and_3_out, and_4_out);
endmodule

// Mux 8:1
module MuxDe8_1 (
  input  a,
  input  b,
  input  c,
  input  d,
  input  e,
  input  f,
  input  g,
  input  h,
  input  Sel1,
  input  Sel2,
  input  Sel3,
  output S
);

  wire and_1_out, and_2_out, and_3_out, and_4_out, and_5_out, and_6_out, and_7_out, and_8_out, not_1_out,
       not_2_out, not_3_out, not_4_out, not_5_out, not_6_out, not_7_out, not_8_out, not_9_out, not_10_out,
       not_11_out, not_12_out;

  not not_1 (not_1_out, Sel1);
  not not_2 (not_2_out, Sel2);
  not not_3 (not_3_out, Sel3);
  not not_4 (not_4_out, Sel1);
  not not_5 (not_5_out, Sel2);
  not not_6 (not_6_out, Sel1);
  not not_7 (not_7_out, Sel3);
  not not_8 (not_8_out, Sel1);
  not not_9 (not_9_out, Sel2);
  not not_10 (not_10_out, Sel3);
  not not_11 (not_11_out, Sel2);
  not not_12 (not_12_out, Sel3);
  and and_1 (and_1_out, a, not_1_out, not_2_out, not_3_out);
  and and_2 (and_2_out, b, not_4_out, not_5_out, Sel3);
  and and_3 (and_3_out, c, not_6_out, Sel2, not_7_out);
  and and_4 (and_4_out, d, not_8_out, Sel2, Sel3);
  and and_5 (and_5_out, e, Sel1, not_9_out, not_10_out);
  and and_6 (and_6_out, f, Sel1, not_11_out, Sel3);
  and and_7 (and_7_out, g, Sel1, Sel2, not_12_out);
  and and_8 (and_8_out, h, Sel1, Sel2, Sel3);
  or or_1 (S, and_1_out, and_2_out, and_3_out, and_4_out, and_5_out, and_6_out, and_7_out, and_8_out);
endmodule

module MuxDe16_1_2x8_1 (
  input  a,
  input  b,
  input  c,
  input  d,
  input  e,
  input  f,
  input  g,
  input  h,
  input  in_9,
  input  in_10,
  input  in_11,
  input  in_12,
  input  i,
  input  j,
  input  k,
  input  l,
  input  m,
  input  n,
  input  o,
  input  p,
  output out_21
);

  wire and_1_out, and_2_out, muxde8_1_1_s, muxde8_1_2_s, not_1_out;

  MuxDe8_1 muxde8_1_1 (
    .a(a), .b(b), .c(c), .d(d), .e(e), .f(f), .g(g), .h(h), .Sel1(in_9), .Sel2(in_10), .Sel3(in_11),
    .S(muxde8_1_1_s));
  MuxDe8_1 muxde8_1_2 (
    .a(i), .b(j), .c(k), .d(l), .e(m), .f(n), .g(o), .h(p), .Sel1(in_9), .Sel2(in_10), .Sel3(in_11),
    .S(muxde8_1_2_s));
  not not_1 (not_1_out, in_12);
  and and_1 (and_1_out, muxde8_1_1_s, not_1_out);
  and and_2 (and_2_out, in_12, muxde8_1_2_s);
  or or_1 (out_21, and_1_out, and_2_out);
endmodule

module MuxDe16_1_3x8_1 (
  input  a,
  input  b,
  input  c,
  input  d,
  input  e,
  input  f,
  input  g,
  input  h,
  input  in_9,
  input  in_10,
  input  in_11,
  input  i,
  input  j,
  input  k,
  input  l,
  input  m,
  input  in_17,
  input  n,
  input  o,
  input  p,
  output S
);

  wire muxde8_1_1_s, muxde8_1_2_s;

  MuxDe8_1 muxde8_1_1 (
    .a(a), .b(b), .c(c), .d(d), .e(e), .f(f), .g(g), .h(h), .Sel1(in_9), .Sel2(in_10), .Sel3(in_11),
    .S(muxde8_1_1_s));
  MuxDe8_1 muxde8_1_2 (
    .a(i), .b(j), .c(k), .d(l), .e(m), .f(n), .g(o), .h(p), .Sel1(in_9), .Sel2(in_10), .Sel3(in_11),
    .S(muxde8_1_2_s));
  MuxDe8_1 muxde8_1_3 (
    .a(muxde8_1_1_s), .h(muxde8_1_2_s), .Sel1(in_17), .Sel2(in_17), .Sel3(in_17), .S(S));  // open: b, c, d, e, f, g
endmodule
