// Logisim project TRABALHO006.circ as structural Verilog: 1 circuit, main circuit main
module main (
  input  pin1,
  input  pin2,
  input  pin3,
  input  Sin,
  input  pin4,
  input  Sin_2,
  input  [1:0] in_7,
  input  clr,
  output s1,
  output s2,
  output s3,
  output s4
);

  wire clock_1_out, multiplexer_1_out, multiplexer_2_out, multiplexer_3_out, multiplexer_4_out;

  Clock clock_1 (.out(clock_1_out));
  D_Flip_Flop d_ff_1 (.clk(clock_1_out), .D(multiplexer_1_out), .Q(s1), .reset(clr));  // open: Qn, preset, en
  Multiplexer #(.select(2)) multiplexer_1 (
    .in0(s1), .in1(s2), .in2(Sin_2), .in3(pin1), .out(multiplexer_1_out), .sel(in_7));  // open: en
  Multiplexer #(.select(2)) multiplexer_2 (
    .in0(s2), .in1(s3), .in2(s1), .in3(pin2), .out(multiplexer_2_out), .sel(in_7));  // open: en
  D_Flip_Flop d_ff_2 (.clk(clock_1_out), .D(multiplexer_2_out), .Q(s2), .reset(clr));  // open: Qn, preset, en
  Multiplexer #(.select(2)) multiplexer_3 (
    .in0(s3), .in1(s4), .in2(s2), .in3(pin3), .out(multiplexer_3_out), .sel(in_7));  // open: en
  D_Flip_Flop d_ff_3 (.clk(clock_1_out), .D(multiplexer_3_out), .Q(s3), .reset(clr));  // open: Qn, preset, en
  Multiplexer #(.select(2)) multiplexer_4 (
    .in0(s4), .in1(Sin), .in2(s3), .in3(pin4), .out(multiplexer_4_out), .sel(in_7));  // open: en
  D_Flip_Flop d_ff_4 (.clk(clock_1_out), .D(multiplexer_4_out), .Q(s4), .reset(clr));  // open: Qn, preset, en
endmodule
