// Logisim project Tarefa01.circ as structural Verilog: 8 circuits, main circuit main
module main (
  input  Y_25,
  input  A_1,
  input  S_19,
  input  M_13,
  input  I_9,
  input  N_14,
  input  E_5,
  input  M133,
  input  Sel,
  output out_10,
  output out_11,
  output out_12,
  output out_13,
  output out_14
);

  SISTEMA_SUM_SUB sistema_sum_sub_1 (
    .Y_25(Y_25), .A_1(A_1), .S_19(S_19), .M_13(M_13), .I_9(I_9), .N_14(N_14), .E_5(E_5), .M133(M133),
    .Sel(Sel), .out_10(out_10), .out_11(out_11), .out_12(out_12), .out_13(out_13), .out_14(out_14));

  // Notes on the sheet:
  //   YASM INEM
  //   Lendo de baixo pra cima ^^
endmodule

module SUM (
  input  A,
  input  B,
  output S,
  output Ts
);

  wire and_2_out, and_3_out, not_1_out, not_2_out;

  not not_1 (not_1_out, A);
  not not_2 (not_2_out, B);
  and and_1 (Ts, A, B);
  and and_2 (and_2_out, not_1_out, B);
  and and_3 (and_3_out, A, not_2_out);
  or or_1 (S, and_2_out, and_3_out);
endmodule

module SUB (
  input  A,
  input  B,
  output S,
  output Ts
);

  wire and_1_out, and_2_out, not_1_out, not_2_out, not_3_out;

  not not_1 (not_1_out, A);
  not not_2 (not_2_out, B);
  not not_3 (not_3_out, A);
  and and_1 (and_1_out, not_1_out, B);
  and and_2 (and_2_out, A, not_2_out);
  and and_3 (Ts, not_3_out, B);
  or or_1 (S, and_1_out, and_2_out);
endmodule

module SUM2 (
  input  A,
  input  B,
  input  Te,
  output S,
  output Ts
);

  wire and_1_out, and_2_out, and_3_out, and_4_out, and_5_out, and_6_out, and_7_out, and_8_out, and_9_out,
       and_10_out, and_11_out, not_1_out, not_2_out, not_3_out, not_4_out, not_5_out, not_6_out, or_1_out,
       or_3_out, or_4_out;

  not not_1 (not_1_out, A);
  not not_2 (not_2_out, B);
  not not_3 (not_3_out, A);
  not not_4 (not_4_out, B);
  and and_1 (and_1_out, B, Te);
  and and_2 (and_2_out, A, Te);
  and and_3 (and_3_out, not_1_out, not_2_out);
  and and_4 (and_4_out, not_3_out, B);
  not not_5 (not_5_out, Te);
  and and_5 (and_5_out, A, not_4_out);
  not not_6 (not_6_out, Te);
  and and_6 (and_6_out, A, B);
  or or_1 (or_1_out, and_1_out, and_2_out);
  and and_7 (and_7_out, A, B);
  and and_8 (and_8_out, and_3_out, Te);
  and and_9 (and_9_out, and_4_out, not_5_out);
  and and_10 (and_10_out, and_5_out, not_6_out);
  and and_11 (and_11_out, and_6_out, Te);
  or or_2 (Ts, or_1_out, and_7_out);
  or or_3 (or_3_out, and_8_out, and_9_out);
  or or_4 (or_4_out, and_10_out, and_11_out);
  or or_5 (S, or_3_out, or_4_out);
endmodule

module SUB2 (
  input  A,
  input  B,
  input  Te,
  output S,
  output Te2
);

  wire and_1_out, and_2_out, and_3_out, and_4_out, and_5_out, and_6_out, and_7_out, and_8_out, and_9_out,
       and_10_out, and_11_out, not_1_out, not_2_out, not_3_out, not_4_out, not_5_out, not_6_out, not_7_out,
       not_8_out, or_1_out, or_2_out, or_3_out;

  not not_1 (not_1_out, A);
  not not_2 (not_2_out, B);
  not not_3 (not_3_out, A);
  not not_4 (not_4_out, B);
  not not_5 (not_5_out, A);
  not not_6 (not_6_out, A);
  and and_1 (and_1_out, not_1_out, not_2_out);
  and and_2 (and_2_out, not_3_out, B);
  not not_7 (not_7_out, Te);
  and and_3 (and_3_out, A, not_4_out);
  not not_8 (not_8_out, Te);
  and and_4 (and_4_out, A, B);
  and and_5 (and_5_out, not_5_out, Te);
  and and_6 (and_6_out, not_6_out, B);
  and and_7 (and_7_out, and_1_out, Te);
  and and_8 (and_8_out, and_2_out, not_7_out);
  and and_9 (and_9_out, and_3_out, not_8_out);
  and and_10 (and_10_out, and_4_out, Te);
  or or_1 (or_1_out, and_5_out, and_6_out);
  and and_11 (and_11_out, B, Te);
  or or_2 (or_2_out, and_7_out, and_8_out);
  or or_3 (or_3_out, and_9_out, and_10_out);
  or or_4 (Te2, or_1_out, and_11_out);
  or or_5 (S, or_2_out, or_3_out);
endmodule

module SOMA (
  input  Y_25,
  input  A_1,
  input  S_19,
  input  M_13,
  input  I_9,
  input  N_14,
  input  E_5,
  input  M133,
  output out_9,
  output out_10,
  output out_11,
  output out_12,
  output out_13
);

  wire sum2_1_ts, sum2_2_ts, sum_1_ts;

  SUM sum_1 (.A(M_13), .B(M133), .S(out_9), .Ts(sum_1_ts));
  SUM2 sum2_1 (.A(S_19), .B(E_5), .Te(sum_1_ts), .S(out_10), .Ts(sum2_1_ts));
  SUM2 sum2_2 (.A(A_1), .B(N_14), .Te(sum2_1_ts), .S(out_11), .Ts(sum2_2_ts));
  SUM2 sum2_3 (.A(Y_25), .B(I_9), .Te(sum2_2_ts), .S(out_12), .Ts(out_13));
endmodule

module SUBT (
  input  Y_25,
  input  A_1,
  input  S_19,
  input  M_13,
  input  I_9,
  input  N_14,
  input  E_5,
  input  M133,
  output out_9,
  output out_10,
  output out_11,
  output out_12,
  output out_13
);

  wire sub2_1_te2, sub2_2_te2, sub_1_ts;

  SUB sub_1 (.A(M_13), .B(M133), .S(out_9), .Ts(sub_1_ts));
  SUB2 sub2_1 (.A(S_19), .B(E_5), .Te(sub_1_ts), .S(out_10), .Te2(sub2_1_te2));
  SUB2 sub2_2 (.A(A_1), .B(N_14), .Te(sub2_1_te2), .S(out_11), .Te2(sub2_2_te2));
  SUB2 sub2_3 (.A(Y_25), .B(I_9), .Te(sub2_2_te2), .S(out_12), .Te2(out_13));
endmodule

// 0-SUM 1-SUB
module SISTEMA_SUM_SUB (
  input  Y_25,
  input  A_1,
  input  S_19,
  input  M_13,
  input  I_9,
  input  N_14,
  input  E_5,
  input  M133,
  input  Sel,
  output out_10,
  output out_11,
  output out_12,
  output out_13,
  output out_14
);

  wire soma_1_out_9, soma_1_out_10, soma_1_out_11, soma_1_out_12, soma_1_out_13, subt_1_out_9, subt_1_out_10,
       subt_1_out_11, subt_1_out_12, subt_1_out_13;

  SOMA soma_1 (
    .Y_25(Y_25), .A_1(A_1), .S_19(S_19), .M_13(M_13), .I_9(I_9), .N_14(N_14), .E_5(E_5), .M133(M133),
    .out_9(soma_1_out_9), .out_10(soma_1_out_10), .out_11(soma_1_out_11), .out_12(soma_1_out_12),
    .out_13(soma_1_out_13));
  SUBT subt_1 (
    .Y_25(Y_25), .A_1(A_1), .S_19(S_19), .M_13(M_13), .I_9(I_9), .N_14(N_14), .E_5(E_5), .M133(M133),
    .out_9(subt_1_out_9), .out_10(subt_1_out_10), .out_11(subt_1_out_11), .out_12(subt_1_out_12),
    .out_13(subt_1_out_13));
  Multiplexer multiplexer_1 (.in0(soma_1_out_9), .in1(subt_1_out_9), .out(out_10), .sel(Sel));  // open: en
  Multiplexer multiplexer_2 (.in0(soma_1_out_10), .in1(subt_1_out_10), .out(out_11), .sel(Sel));  // open: en
  Multiplexer multiplexer_3 (.in0(soma_1_out_11), .in1(subt_1_out_11), .out(out_12), .sel(Sel));  // open: en
  Multiplexer multiplexer_4 (.in0(soma_1_out_12), .in1(subt_1_out_12), .out(out_13), .sel(Sel));  // open: en
  Multiplexer multiplexer_5 (.in0(soma_1_out_13), .in1(subt_1_out_13), .out(out_14), .sel(Sel));  // open: en
endmodule
