// Logisim project bin_2_7seg.circ as structural Verilog: 3 circuits, main circuit main
module main (
  input  a0,
  input  a1,
  output a,
  output b,
  output c,
  output d,
  output e,
  output f,
  output g
);

  not not_1 (a, a1);
  not not_2 (d, a1);
  not not_3 (e, a1);
  not not_4 (f, a1);

  assign b = 1'b1;
  assign c = 1'b1;
  assign g = 1'b0;
endmodule

module bin27seg (
  input  a0,
  input  a1,
  output a,
  output b,
  output c,
  output d,
  output e,
  output f,
  output g
);

  or or_1 (b, a1, a0);
  or or_2 (c, a1, a0);

  assign a = a0;
  assign d = a0;
  assign e = a0;
  assign f = a0;
  assign g = 1'b0;
endmodule

module IN_2_OUT (
  input  in_1,
  input  in_2,
  input  in_3,
  input  in_4
);

  wire bin27seg_1_a, bin27seg_1_b, bin27seg_1_c, bin27seg_1_d, bin27seg_1_e, bin27seg_1_f, bin27seg_1_g,
       main_1_a, main_1_b, main_1_c, main_1_d, main_1_e, main_1_f, main_1_g;

  bin27seg bin27seg_1 (
    .a0(in_1), .a1(in_2), .a(bin27seg_1_a), .b(bin27seg_1_b), .c(bin27seg_1_c), .d(bin27seg_1_d),
    .e(bin27seg_1_e), .f(bin27seg_1_f), .g(bin27seg_1_g));
  main main_1 (
    .a0(in_3), .a1(in_4), .a(main_1_a), .b(main_1_b), .c(main_1_c), .d(main_1_d), .e(main_1_e), .f(main_1_f),
    .g(main_1_g));
  _7_Segment_Display u_7_segment_display_1 (
    .g(bin27seg_1_g), .f(bin27seg_1_f), .a(bin27seg_1_a), .b(bin27seg_1_b), .e(bin27seg_1_e),
    .d(bin27seg_1_d), .c(bin27seg_1_c));  // open: dp
  _7_Segment_Display u_7_segment_display_2 (
    .g(main_1_g), .f(main_1_f), .a(main_1_a), .b(main_1_b), .e(main_1_e), .d(main_1_d), .c(main_1_c));  // open: dp
endmodule
