// Logisim project expressao_soma3bit.circ as structural Verilog: 2 circuits, main circuit main
module main (
  input  a2,
  input  a1,
  input  a0,
  input  b2,
  input  b1,
  input  b0,
  output s3,
  output s2,
  output s1,
  output s0
);

  wire and_1_out, and_2_out, and_3_out, and_4_out, and_5_out, and_6_out, and_7_out, and_8_out, and_9_out,
       and_10_out, and_11_out, and_12_out, and_13_out, and_14_out, and_15_out, and_16_out, and_17_out,
       and_18_out, and_19_out, and_20_out, and_21_out, and_22_out, and_23_out, and_24_out, and_25_out,
       and_26_out, and_27_out, and_28_out, and_29_out, and_30_out, and_31_out, and_32_out, and_33_out,
       and_34_out, and_35_out, and_36_out, and_37_out, and_38_out, and_39_out, and_40_out, and_41_out,
       and_42_out, and_43_out, and_44_out, and_45_out, and_46_out, and_47_out, and_48_out, and_49_out,
       and_50_out, and_51_out, and_52_out, and_53_out, and_54_out, and_55_out, and_56_out, and_57_out,
       and_58_out, and_59_out, and_60_out, and_61_out, and_62_out, and_63_out, and_64_out, and_65_out,
       and_66_out, and_67_out, and_68_out, and_69_out, and_70_out, and_71_out, and_72_out, and_73_out,
       and_74_out, and_75_out, and_76_out, and_77_out, and_78_out, and_79_out, and_80_out, and_81_out,
       and_82_out, and_83_out, and_84_out, and_85_out, not_1_out, not_2_out, not_3_out, not_4_out, not_5_out,
       not_6_out, not_7_out, not_8_out, not_9_out, not_10_out, not_11_out, not_12_out, not_13_out,
       not_14_out, not_15_out, not_16_out, not_17_out, not_18_out, not_19_out, not_20_out, not_21_out,
       not_22_out, not_23_out, not_24_out, not_25_out, not_26_out, not_27_out, not_28_out, not_29_out,
       not_30_out, not_31_out, not_32_out, not_33_out, not_34_out, not_35_out, not_36_out, not_37_out,
       not_38_out, not_39_out, not_40_out, not_41_out, not_42_out, not_43_out, not_44_out, not_45_out,
       not_46_out, not_47_out, not_48_out, or_1_out, or_2_out, or_3_out, or_5_out, or_6_out, or_7_out,
       or_8_out, or_10_out, or_11_out, or_12_out, or_13_out, or_14_out, or_15_out, or_16_out, or_17_out,
       or_18_out, or_19_out, or_20_out, or_21_out, or_22_out, or_24_out, or_25_out, or_26_out;

  and and_1 (and_1_out, a0, b2);
  and and_2 (and_2_out, b1, b0);
  and and_3 (and_3_out, a1, b2);
  and and_4 (and_4_out, a1, a0);
  and and_5 (and_5_out, b2, b0);
  and and_6 (and_6_out, a2, a0);
  and and_7 (and_7_out, b1, b0);
  and and_8 (and_8_out, a2, a1);
  not not_1 (not_1_out, a2);
  not not_2 (not_2_out, a2);
  not not_3 (not_3_out, a1);
  not not_4 (not_4_out, a0);
  not not_5 (not_5_out, a1);
  not not_6 (not_6_out, a0);
  not not_7 (not_7_out, b1);
  not not_8 (not_8_out, a0);
  not not_9 (not_9_out, b0);
  and and_9 (and_9_out, and_1_out, and_2_out);
  and and_10 (and_10_out, and_3_out, b1);
  and and_11 (and_11_out, and_4_out, and_5_out);
  and and_12 (and_12_out, a2, b2);
  and and_13 (and_13_out, and_6_out, and_7_out);
  and and_14 (and_14_out, and_8_out, b1);
  and and_15 (and_15_out, a2, a1);
  and and_16 (and_16_out, a0, b0);
  not not_10 (not_10_out, a2);
  not not_11 (not_11_out, a1);
  not not_12 (not_12_out, a0);
  not not_13 (not_13_out, a2);
  not not_14 (not_14_out, a1);
  not not_15 (not_15_out, b1);
  not not_16 (not_16_out, a2);
  not not_17 (not_17_out, a1);
  not not_18 (not_18_out, b0);
  not not_19 (not_19_out, a2);
  not not_20 (not_20_out, a0);
  not not_21 (not_21_out, b1);
  not not_22 (not_22_out, a2);
  not not_23 (not_23_out, b1);
  not not_24 (not_24_out, b0);
  and and_17 (and_17_out, not_1_out, a0);
  not not_25 (not_25_out, b2);
  not not_26 (not_26_out, a2);
  not not_27 (not_27_out, b2);
  and and_18 (and_18_out, not_2_out, a1);
  not not_28 (not_28_out, b2);
  not not_29 (not_29_out, a1);
  not not_30 (not_30_out, a0);
  not not_31 (not_31_out, b2);
  not not_32 (not_32_out, a1);
  not not_33 (not_33_out, b2);
  not not_34 (not_34_out, b1);
  not not_35 (not_35_out, a1);
  not not_36 (not_36_out, b2);
  not not_37 (not_37_out, b0);
  not not_38 (not_38_out, a0);
  not not_39 (not_39_out, b2);
  not not_40 (not_40_out, b1);
  not not_41 (not_41_out, b2);
  not not_42 (not_42_out, b1);
  not not_43 (not_43_out, b0);
  and and_19 (and_19_out, a2, a0);
  and and_20 (and_20_out, a2, a1);
  and and_21 (and_21_out, not_3_out, not_4_out);
  and and_22 (and_22_out, not_5_out, b1);
  not not_44 (not_44_out, b0);
  not not_45 (not_45_out, a1);
  not not_46 (not_46_out, b1);
  and and_23 (and_23_out, a1, not_6_out);
  not not_47 (not_47_out, b1);
  and and_24 (and_24_out, a1, not_7_out);
  not not_48 (not_48_out, b0);
  and and_25 (and_25_out, not_8_out, b0);
  and and_26 (and_26_out, a0, not_9_out);
  or or_1 (or_1_out, and_9_out, and_10_out);
  or or_2 (or_2_out, and_11_out, and_12_out);
  or or_3 (or_3_out, and_13_out, and_14_out);
  and and_27 (and_27_out, and_15_out, and_16_out);
  and and_28 (and_28_out, not_10_out, not_11_out);
  and and_29 (and_29_out, not_12_out, b2);
  and and_30 (and_30_out, not_13_out, not_14_out);
  and and_31 (and_31_out, b2, not_15_out);
  and and_32 (and_32_out, not_16_out, not_17_out);
  and and_33 (and_33_out, b2, not_18_out);
  and and_34 (and_34_out, not_19_out, not_20_out);
  and and_35 (and_35_out, b2, not_21_out);
  and and_36 (and_36_out, not_22_out, b2);
  and and_37 (and_37_out, not_23_out, not_24_out);
  and and_38 (and_38_out, and_17_out, not_25_out);
  and and_39 (and_39_out, b1, b0);
  and and_40 (and_40_out, not_26_out, a1);
  and and_41 (and_41_out, not_27_out, b1);
  and and_42 (and_42_out, and_18_out, a0);
  and and_43 (and_43_out, not_28_out, b0);
  and and_44 (and_44_out, a2, not_29_out);
  and and_45 (and_45_out, not_30_out, not_31_out);
  and and_46 (and_46_out, a2, not_32_out);
  and and_47 (and_47_out, not_33_out, not_34_out);
  and and_48 (and_48_out, a2, not_35_out);
  and and_49 (and_49_out, not_36_out, not_37_out);
  and and_50 (and_50_out, a2, not_38_out);
  and and_51 (and_51_out, not_39_out, not_40_out);
  and and_52 (and_52_out, a2, not_41_out);
  and and_53 (and_53_out, not_42_out, not_43_out);
  and and_54 (and_54_out, and_19_out, b2);
  and and_55 (and_55_out, b1, b0);
  and and_56 (and_56_out, a2, a1);
  and and_57 (and_57_out, b2, b1);
  and and_58 (and_58_out, and_20_out, a0);
  and and_59 (and_59_out, b2, b0);
  and and_60 (and_60_out, and_21_out, b1);
  and and_61 (and_61_out, and_22_out, not_44_out);
  and and_62 (and_62_out, not_45_out, a0);
  and and_63 (and_63_out, not_46_out, b0);
  and and_64 (and_64_out, and_23_out, not_47_out);
  and and_65 (and_65_out, and_24_out, not_48_out);
  and and_66 (and_66_out, a1, a0);
  and and_67 (and_67_out, b1, b0);
  or or_4 (s0, and_25_out, and_26_out);
  or or_5 (or_5_out, or_1_out, or_2_out);
  or or_6 (or_6_out, or_3_out, and_27_out);
  and and_68 (and_68_out, and_28_out, and_29_out);
  and and_69 (and_69_out, and_30_out, and_31_out);
  and and_70 (and_70_out, and_32_out, and_33_out);
  and and_71 (and_71_out, and_34_out, and_35_out);
  and and_72 (and_72_out, and_36_out, and_37_out);
  and and_73 (and_73_out, and_38_out, and_39_out);
  and and_74 (and_74_out, and_40_out, and_41_out);
  and and_75 (and_75_out, and_42_out, and_43_out);
  and and_76 (and_76_out, and_44_out, and_45_out);
  and and_77 (and_77_out, and_46_out, and_47_out);
  and and_78 (and_78_out, and_48_out, and_49_out);
  and and_79 (and_79_out, and_50_out, and_51_out);
  and and_80 (and_80_out, and_52_out, and_53_out);
  and and_81 (and_81_out, and_54_out, and_55_out);
  and and_82 (and_82_out, and_56_out, and_57_out);
  and and_83 (and_83_out, and_58_out, and_59_out);
  or or_7 (or_7_out, and_60_out, and_61_out);
  and and_84 (and_84_out, and_62_out, and_63_out);
  or or_8 (or_8_out, and_64_out, and_65_out);
  and and_85 (and_85_out, and_66_out, and_67_out);
  or or_9 (s3, or_5_out, or_6_out);
  or or_10 (or_10_out, and_68_out, and_69_out);
  or or_11 (or_11_out, or_10_out, or_12_out);
  or or_12 (or_12_out, and_70_out, and_71_out);
  or or_13 (or_13_out, and_72_out, and_73_out);
  or or_14 (or_14_out, or_13_out, or_15_out);
  or or_15 (or_15_out, and_74_out, and_75_out);
  or or_16 (or_16_out, and_76_out, and_77_out);
  or or_17 (or_17_out, or_16_out, or_18_out);
  or or_18 (or_18_out, and_78_out, and_79_out);
  or or_19 (or_19_out, and_80_out, and_81_out);
  or or_20 (or_20_out, or_19_out, or_21_out);
  or or_21 (or_21_out, and_82_out, and_83_out);
  or or_22 (or_22_out, or_7_out, and_84_out);
  or or_23 (s1, or_22_out, or_24_out);
  or or_24 (or_24_out, or_8_out, and_85_out);
  or or_25 (or_25_out, or_11_out, or_14_out);
  or or_26 (or_26_out, or_17_out, or_20_out);
  or or_27 (s2, or_25_out, or_26_out);
endmodule

module soma (
  input  in_1,
  input  in_2,
  input  in_3,
  input  in_4,
  input  in_5,
  input  in_6,
  output out_7,
  output out_8,
  output out_9,
  output out_10
);

  main main_1 (
    .a2(in_1), .a1(in_2), .a0(in_3), .b2(in_4), .b1(in_5), .b0(in_6), .s3(out_7), .s2(out_8), .s1(out_9),
    .s0(out_10));
endmodule
