// Logisim project mux_demux.circ as structural Verilog: 2 circuits, main circuit main
module main (
  input  in_1,
  input  in_2,
  input  in_3,
  input  in_4,
  input  in_5,
  input  in_6,
  input  in_7,
  input  in_8,
  input  in_9,
  input  in_10,
  input  in_11,
  output out_12
);

  wire and_1_out, and_2_out, and_3_out, and_4_out, and_5_out, and_6_out, and_7_out, and_8_out, not_1_out,
       not_2_out, not_3_out, or_1_out, or_2_out;

  not not_1 (not_1_out, in_9);
  not not_2 (not_2_out, in_10);
  not not_3 (not_3_out, in_11);
  and and_1 (and_1_out, in_1, not_1_out, not_2_out, not_3_out);
  and and_2 (and_2_out, in_2, not_1_out, not_2_out, in_11);
  and and_3 (and_3_out, in_3, not_1_out, in_10, not_3_out);
  and and_4 (and_4_out, in_4, not_1_out, in_10, in_11);
  and and_5 (and_5_out, in_5, in_9, not_2_out, not_3_out);
  and and_6 (and_6_out, in_6, in_9, not_2_out, in_11);
  and and_7 (and_7_out, in_7, in_9, in_10, not_3_out);
  and and_8 (and_8_out, in_8, in_9, in_10, in_11);
  or or_1 (or_1_out, and_5_out, and_6_out, and_7_out, and_8_out);
  or or_2 (or_2_out, and_1_out, and_2_out, and_3_out, and_4_out);
  or or_3 (out_12, or_2_out, or_1_out);
endmodule

module demux (
  input  in_1,
  input  in_2,
  input  in_3,
  input  in_4,
  output out_5,
  output out_6,
  output out_7,
  output out_8,
  output out_9,
  output out_10,
  output out_11,
  output out_12
);

  wire not_1_out, not_2_out, not_3_out;

  not not_1 (not_1_out, in_2);
  not not_2 (not_2_out, in_3);
  not not_3 (not_3_out, in_4);
  and and_1 (out_5, in_1, not_1_out, not_2_out, not_3_out);
  and and_2 (out_6, in_1, not_1_out, not_2_out, in_4);
  and and_3 (out_7, in_1, not_1_out, in_3, not_3_out);
  and and_4 (out_8, in_1, not_1_out, in_3, in_4);
  and and_5 (out_9, in_1, in_2, not_2_out, not_3_out);
  and and_6 (out_10, in_1, in_2, not_2_out, in_4);
  and and_7 (out_11, in_1, in_2, in_3, not_3_out);
  and and_8 (out_12, in_1, in_2, in_3, in_4);
endmodule
