// Logisim project questoes_prova.circ as structural Verilog: 5 circuits, main circuit main
module main (
  input  A,
  input  B,
  input  C,
  input  D,
  output out_5
);

  wire nand_1_out, nand_2_out, nor_1_out, not_1_out, not_2_out, not_3_out, or_1_out;

  not not_1 (not_1_out, A);
  not not_2 (not_2_out, B);
  nand nand_1 (nand_1_out, not_1_out, B);
  nand nand_2 (nand_2_out, A, not_2_out);
  or or_1 (or_1_out, C, D);
  not not_3 (not_3_out, C);
  nor nor_1 (nor_1_out, nand_1_out, nand_2_out, not_3_out);
  and and_1 (out_5, nor_1_out, or_1_out);
endmodule

module segunda_questao (
  input  A,
  input  B,
  input  C,
  input  D,
  input  E,
  output out_6
);

  wire and_2_out, and_3_out, and_4_out, nand_1_out, nand_2_out, nor_1_out, not_1_out, not_2_out, not_3_out,
       not_4_out;

  not not_1 (not_1_out, A);
  not not_2 (not_2_out, D);
  // AND_Gate and_1 has open pins: in0=C, in1=D, in3=E, out=open
  nand nand_1 (nand_1_out, not_1_out, B);
  nand nand_2 (nand_2_out, C, not_2_out);
  and and_2 (and_2_out, A, not_3_out, not_4_out);
  not not_3 (not_3_out, D);
  not not_4 (not_4_out, E);
  nor nor_1 (nor_1_out, nand_1_out, nand_2_out);
  and and_3 (and_3_out, not_1_out, and_2_out);
  and and_4 (and_4_out, nor_1_out, E);
  or or_1 (out_6, and_4_out, and_3_out);
endmodule

module terceira_questao (
  input  A,
  input  B,
  input  C,
  input  D,
  output S
);

  wire and_1_out, and_2_out, not_1_out, not_2_out, not_3_out, not_4_out;

  not not_1 (not_1_out, A);
  and and_1 (and_1_out, not_1_out, B, not_2_out);
  not not_2 (not_2_out, D);
  not not_3 (not_3_out, B);
  and and_2 (and_2_out, A, not_3_out, not_4_out);
  not not_4 (not_4_out, D);
  or or_1 (S, and_1_out, and_2_out);

  // Notes on the sheet:
  //   Circuito feito após a simplificação ( ~D(~A*B+A*~B)+~D(~A*B+A*~B))
endmodule

module \quarta_questão  (
  input  I0,
  input  I1,
  input  I2,
  input  I3,
  input  I4,
  input  I5,
  input  I6,
  input  I7,
  input  in_9,
  input  in_10,
  input  in_11,
  input  in_12,
  input  in_13,
  input  in_14,
  output out_15,
  output out_16,
  output out_17,
  output out_18,
  output out_19,
  output out_20,
  output out_21,
  output out_22
);

  wire _000_out, _001_out, _010_out, _011_out, _100_out, _101_out, _110_out, _111_out, not_1_out, not_2_out,
       not_3_out, not_4_out, not_5_out, not_6_out, or_1_out;

  not not_1 (not_1_out, in_9);
  not not_2 (not_2_out, in_10);
  and _000 (_000_out, I0, not_1_out, not_2_out, not_3_out);
  and _001 (_001_out, I1, not_1_out, not_2_out, in_11);
  and _010 (_010_out, I2, not_1_out, in_10, not_3_out);
  and _011 (_011_out, I3, not_1_out, in_10, in_11);
  and _100 (_100_out, I4, in_9, not_2_out, not_3_out);
  and _101 (_101_out, I5, in_9, not_2_out, in_11);
  and _110 (_110_out, I6, in_9, in_10, not_3_out);
  and _111 (_111_out, I7, in_9, in_10, in_11);
  not not_3 (not_3_out, in_11);
  or or_1 (or_1_out, _000_out, _001_out, _010_out, _011_out, _100_out, _101_out, _110_out, _111_out);
  not not_4 (not_4_out, in_12);
  not not_5 (not_5_out, in_13);
  not not_6 (not_6_out, in_14);
  and _000_2 (out_15, or_1_out, not_4_out, not_5_out, not_6_out);
  and _001_2 (out_16, or_1_out, not_4_out, not_5_out, in_14);
  and _010_2 (out_17, or_1_out, not_4_out, in_13, not_6_out);
  and _011_2 (out_18, or_1_out, not_4_out, in_13, in_14);
  and _100_2 (out_19, or_1_out, in_12, not_5_out, not_6_out);
  and _101_2 (out_20, or_1_out, in_12, not_5_out, in_14);
  and _110_2 (out_21, or_1_out, in_12, in_13, not_6_out);
  and _111_2 (out_22, or_1_out, in_12, in_13, in_14);

  // Notes on the sheet:
  //   S
  //   E
endmodule

module \quinta_questão  (
  input  A,
  input  B,
  input  C,
  output S,
  output Ts
);

  wire and_1_out, and_2_out, and_3_out, xor_1_out;

  xor xor_1 (xor_1_out, A, B);
  and and_1 (and_1_out, B, C);
  and and_2 (and_2_out, C, A);
  and and_3 (and_3_out, B, A);
  xor xor_2 (S, xor_1_out, C);
  or or_1 (Ts, and_1_out, and_2_out, and_3_out);
endmodule
