// Logisim project tarefaC4.circ as structural Verilog: 1 circuit, main circuit main
module main (
  input  A,
  input  B,
  input  C,
  input  D,
  output S0,
  output S1
);

  or or_1 (S0, B, D);
  or or_2 (S1, C, D);
endmodule
