// Logisim project trabalho0008.circ as structural Verilog: 6 circuits, main circuit main
module main (
);

  wire and_4_out, and_6_out, and_7_out, clock_1_out, cont_7_seg_1_a, cont_7_seg_1_b, cont_7_seg_1_c,
       cont_7_seg_1_d, cont_7_seg_1_e, cont_7_seg_1_f, cont_7_seg_1_g, j_k_ff_1_q, j_k_ff_2_q, j_k_ff_3_q,
       j_k_ff_4_q, j_k_ff_4_qn, or_1_out, or_2_out, or_4_out;

  Clock clock_1 (.out(clock_1_out));
  or or_1 (or_1_out, j_k_ff_4_qn, j_k_ff_2_q);
  or or_2 (or_2_out, j_k_ff_4_qn, j_k_ff_2_q);
  J_K_Flip_Flop j_k_ff_1 (
    .J(or_1_out), .clk(clock_1_out), .K(or_2_out), .Q(j_k_ff_1_q));  // open: Qn, preset, en, reset
  // XOR_Gate xor_1 has open pins: in1=j_k_ff_1_q, out=open
  // AND_Gate and_1 has open pins: in1=j_k_ff_1_q, out=open
  // AND_Gate and_2 has open pins: in1=j_k_ff_4_q, out=open
  // OR_Gate or_3 is placed but not wired
  // AND_Gate and_3 has open pins: in1=j_k_ff_4_q, out=open
  J_K_Flip_Flop j_k_ff_2 (.clk(clock_1_out), .Q(j_k_ff_2_q));  // open: J, K, Qn, preset, en, reset
  buf and_4 (and_4_out, j_k_ff_2_q);  // AND_Gate
  buf or_4 (or_4_out, and_6_out);  // OR_Gate
  // AND_Gate and_5 has open pins: in0=j_k_ff_1_q, in1=j_k_ff_4_q, out=open
  J_K_Flip_Flop j_k_ff_3 (
    .J(and_4_out), .clk(clock_1_out), .K(or_4_out), .Q(j_k_ff_3_q));  // open: Qn, preset, en, reset
  and and_6 (and_6_out, j_k_ff_2_q, j_k_ff_1_q);
  and and_7 (and_7_out, j_k_ff_3_q, j_k_ff_1_q);
  J_K_Flip_Flop j_k_ff_4 (
    .J(and_6_out), .clk(clock_1_out), .K(and_7_out), .Q(j_k_ff_4_q), .Qn(j_k_ff_4_qn));  // open: preset, en, reset
  cont_7_seg cont_7_seg_1 (
    .d4(j_k_ff_4_q), .d3(j_k_ff_3_q), .d2(j_k_ff_2_q), .d1(j_k_ff_1_q), .a(cont_7_seg_1_a),
    .b(cont_7_seg_1_b), .c(cont_7_seg_1_c), .d(cont_7_seg_1_d), .e(cont_7_seg_1_e), .f(cont_7_seg_1_f),
    .g(cont_7_seg_1_g));
  _7_Segment_Display u_7_segment_display_1 (
    .g(cont_7_seg_1_g), .f(cont_7_seg_1_f), .a(cont_7_seg_1_a), .b(cont_7_seg_1_b), .e(cont_7_seg_1_e),
    .d(cont_7_seg_1_d), .c(cont_7_seg_1_c));  // open: dp
endmodule

module contador (
  input  q3,
  input  q2,
  input  q1,
  input  q0,
  output j4,
  output k4,
  output j3,
  output k3,
  output j2,
  output k2,
  output j1,
  output k1
);

  wire and_1_out, and_2_out;

  and and_1 (and_1_out, q2, q1);
  and and_2 (and_2_out, q2, q1);
  and and_3 (j3, q1, q0);
  and and_4 (k3, q1, q0);
  and and_5 (j4, and_1_out, q0);
  and and_6 (k4, and_2_out, q0);

  assign j1 = 1'b1;
  assign j2 = q0;
  assign k1 = 1'b1;
  assign k2 = q0;
endmodule

module B (
);

  wire clock_1_out, cont_7_seg_1_a, cont_7_seg_1_b, cont_7_seg_1_c, cont_7_seg_1_d, cont_7_seg_1_e,
       cont_7_seg_1_f, cont_7_seg_1_g, contador_1_j1, contador_1_j2, contador_1_j3, contador_1_j4,
       contador_1_k1, contador_1_k2, contador_1_k3, contador_1_k4, j_k_ff_1_q, j_k_ff_1_qn, j_k_ff_2_q,
       j_k_ff_2_qn, j_k_ff_3_q, j_k_ff_3_qn, j_k_ff_4_q, j_k_ff_4_qn;

  Clock clock_1 (.out(clock_1_out));
  J_K_Flip_Flop j_k_ff_1 (
    .J(contador_1_k1), .clk(clock_1_out), .K(contador_1_j1), .Q(j_k_ff_1_q), .Qn(j_k_ff_1_qn));  // open: preset, en, reset
  J_K_Flip_Flop j_k_ff_2 (
    .J(contador_1_k2), .clk(clock_1_out), .K(contador_1_j2), .Q(j_k_ff_2_q), .Qn(j_k_ff_2_qn));  // open: preset, en, reset
  J_K_Flip_Flop j_k_ff_3 (
    .J(contador_1_k3), .clk(clock_1_out), .K(contador_1_j3), .Q(j_k_ff_3_q), .Qn(j_k_ff_3_qn));  // open: preset, en, reset
  J_K_Flip_Flop j_k_ff_4 (
    .J(contador_1_k4), .clk(clock_1_out), .K(contador_1_j4), .Q(j_k_ff_4_q), .Qn(j_k_ff_4_qn));  // open: preset, en, reset
  contador contador_1 (
    .q3(j_k_ff_4_q), .q2(j_k_ff_3_q), .q1(j_k_ff_2_q), .q0(j_k_ff_1_q), .j4(contador_1_j4),
    .k4(contador_1_k4), .j3(contador_1_j3), .k3(contador_1_k3), .j2(contador_1_j2), .k2(contador_1_k2),
    .j1(contador_1_j1), .k1(contador_1_k1));
  cont_7_seg cont_7_seg_1 (
    .d4(j_k_ff_4_qn), .d3(j_k_ff_3_qn), .d2(j_k_ff_2_qn), .d1(j_k_ff_1_qn), .a(cont_7_seg_1_a),
    .b(cont_7_seg_1_b), .c(cont_7_seg_1_c), .d(cont_7_seg_1_d), .e(cont_7_seg_1_e), .f(cont_7_seg_1_f),
    .g(cont_7_seg_1_g));
  _7_Segment_Display u_7_segment_display_1 (
    .g(cont_7_seg_1_g), .f(cont_7_seg_1_f), .a(cont_7_seg_1_a), .b(cont_7_seg_1_b), .e(cont_7_seg_1_e),
    .d(cont_7_seg_1_d), .c(cont_7_seg_1_c));  // open: dp
endmodule

module C (
);

  wire and_1_out, clock_1_out, cont_7_seg_1_a, cont_7_seg_1_b, cont_7_seg_1_c, cont_7_seg_1_d,
       cont_7_seg_1_e, cont_7_seg_1_f, cont_7_seg_1_g, contador_1_j1, contador_1_j2, contador_1_j3,
       contador_1_j4, contador_1_k1, contador_1_k2, contador_1_k3, contador_1_k4, j_k_ff_1_q, j_k_ff_2_q,
       j_k_ff_2_qn, j_k_ff_3_q, j_k_ff_3_qn, j_k_ff_4_q;

  Clock clock_1 (.out(clock_1_out));
  J_K_Flip_Flop j_k_ff_1 (
    .J(contador_1_k1), .clk(clock_1_out), .K(contador_1_j1), .Q(j_k_ff_1_q), .reset(and_1_out));  // open: Qn, preset, en
  J_K_Flip_Flop j_k_ff_2 (
    .J(contador_1_k2), .clk(clock_1_out), .K(contador_1_j2), .Q(j_k_ff_2_q), .Qn(j_k_ff_2_qn),
    .reset(and_1_out));  // open: preset, en
  and and_1 (and_1_out, j_k_ff_1_q, j_k_ff_2_qn, j_k_ff_3_qn, j_k_ff_4_q);
  J_K_Flip_Flop j_k_ff_3 (
    .J(contador_1_k3), .clk(clock_1_out), .K(contador_1_j3), .Q(j_k_ff_3_q), .Qn(j_k_ff_3_qn),
    .reset(and_1_out));  // open: preset, en
  J_K_Flip_Flop j_k_ff_4 (
    .J(contador_1_k4), .clk(clock_1_out), .K(contador_1_j4), .Q(j_k_ff_4_q), .reset(and_1_out));  // open: Qn, preset, en
  contador contador_1 (
    .q3(j_k_ff_4_q), .q2(j_k_ff_3_q), .q1(j_k_ff_2_q), .q0(j_k_ff_1_q), .j4(contador_1_j4),
    .k4(contador_1_k4), .j3(contador_1_j3), .k3(contador_1_k3), .j2(contador_1_j2), .k2(contador_1_k2),
    .j1(contador_1_j1), .k1(contador_1_k1));
  cont_7_seg cont_7_seg_1 (
    .d4(j_k_ff_4_q), .d3(j_k_ff_3_q), .d2(j_k_ff_2_q), .d1(j_k_ff_1_q), .a(cont_7_seg_1_a),
    .b(cont_7_seg_1_b), .c(cont_7_seg_1_c), .d(cont_7_seg_1_d), .e(cont_7_seg_1_e), .f(cont_7_seg_1_f),
    .g(cont_7_seg_1_g));
  _7_Segment_Display u_7_segment_display_1 (
    .g(cont_7_seg_1_g), .f(cont_7_seg_1_f), .a(cont_7_seg_1_a), .b(cont_7_seg_1_b), .e(cont_7_seg_1_e),
    .d(cont_7_seg_1_d), .c(cont_7_seg_1_c));  // open: dp
endmodule

module D (
);

  wire and_1_out, clock_1_out, cont_7_seg_1_a, cont_7_seg_1_b, cont_7_seg_1_c, cont_7_seg_1_d,
       cont_7_seg_1_e, cont_7_seg_1_f, cont_7_seg_1_g, contador_1_j1, contador_1_j2, contador_1_j3,
       contador_1_j4, contador_1_k1, contador_1_k2, contador_1_k3, contador_1_k4, j_k_ff_1_q, j_k_ff_2_q,
       j_k_ff_2_qn, j_k_ff_3_q, j_k_ff_3_qn, j_k_ff_4_q;

  Clock clock_1 (.out(clock_1_out));
  J_K_Flip_Flop j_k_ff_1 (
    .J(contador_1_k1), .clk(clock_1_out), .K(contador_1_j1), .Q(j_k_ff_1_q), .reset(and_1_out));  // open: Qn, preset, en
  J_K_Flip_Flop j_k_ff_2 (
    .J(contador_1_k2), .clk(clock_1_out), .K(contador_1_j2), .Q(j_k_ff_2_q), .Qn(j_k_ff_2_qn),
    .reset(and_1_out));  // open: preset, en
  and and_1 (and_1_out, j_k_ff_1_q, j_k_ff_2_qn, j_k_ff_3_qn, j_k_ff_4_q);
  J_K_Flip_Flop j_k_ff_3 (
    .J(contador_1_k3), .clk(clock_1_out), .K(contador_1_j3), .Q(j_k_ff_3_q), .Qn(j_k_ff_3_qn),
    .reset(and_1_out));  // open: preset, en
  J_K_Flip_Flop j_k_ff_4 (
    .J(contador_1_k4), .clk(clock_1_out), .K(contador_1_j4), .Q(j_k_ff_4_q), .reset(and_1_out));  // open: Qn, preset, en
  contador contador_1 (
    .q3(j_k_ff_4_q), .q2(j_k_ff_3_q), .q1(j_k_ff_2_q), .q0(j_k_ff_1_q), .j4(contador_1_j4),
    .k4(contador_1_k4), .j3(contador_1_j3), .k3(contador_1_k3), .j2(contador_1_j2), .k2(contador_1_k2),
    .j1(contador_1_j1), .k1(contador_1_k1));
  cont_7_seg cont_7_seg_1 (
    .d4(j_k_ff_4_q), .d3(j_k_ff_3_q), .d2(j_k_ff_2_q), .d1(j_k_ff_1_q), .a(cont_7_seg_1_a),
    .b(cont_7_seg_1_b), .c(cont_7_seg_1_c), .d(cont_7_seg_1_d), .e(cont_7_seg_1_e), .f(cont_7_seg_1_f),
    .g(cont_7_seg_1_g));
  _7_Segment_Display u_7_segment_display_1 (
    .g(cont_7_seg_1_g), .f(cont_7_seg_1_f), .a(cont_7_seg_1_a), .b(cont_7_seg_1_b), .e(cont_7_seg_1_e),
    .d(cont_7_seg_1_d), .c(cont_7_seg_1_c));  // open: dp
endmodule

module contadorinverso (
  input  q3,
  input  q2,
  input  q1,
  input  q0,
  output j4,
  output k4,
  output j3,
  output k3,
  output j2,
  output k2,
  output j1,
  output k1
);

  wire not_1_out;

  not not_1 (not_1_out, q3);
  and and_1 (j4, q2, q0);
  and and_2 (j3, q1, q0);
  and and_3 (j2, q0, not_1_out);

  assign j1 = 1'b1;
  assign k1 = 1'b1;
  assign k2 = q0;
  assign k3 = j3;
  assign k4 = q0;
endmodule
