// Logisim project trabalho03.circ as structural Verilog: 16 circuits, main circuit main
module main (
  input  Y___25,
  input  A___1,
  input  S___19,
  input  M___13,
  input  M___13_2,
  input  I___9,
  input  N___14,
  input  E___5,
  input  [1:0] M,
  output carry,
  output A3,
  output A2,
  output A1,
  output A0
);

  wire comparador_1_a, comparador_1_b, comparador_1_c, comparador_1_carry, comparador_1_d, mascara_ligar_1_a,
       mascara_ligar_1_b, mascara_ligar_1_c, mascara_ligar_1_carry, mascara_ligar_1_d, soma_1__1, soma_1__2,
       soma_1__3, soma_1__4, soma_1_carry, subt_1__1, subt_1__2, subt_1__3, subt_1__4, subt_1_carry;

  SOMA soma_1 (
    .Y___25(Y___25), .A___1(A___1), .S___19(S___19), .M___13(M___13), .I___9(I___9), .N___14(N___14),
    .E___5(E___5), .M___13_2(M___13_2), ._4(soma_1__4), ._3(soma_1__3), ._2(soma_1__2), ._1(soma_1__1),
    .carry(soma_1_carry));
  SUBT subt_1 (
    .Y___25(Y___25), .A___1(A___1), .S___19(S___19), .M___13(M___13), .I___9(I___9), .N___14(N___14),
    .E___5(E___5), .M___13_2(M___13_2), ._4(subt_1__4), ._3(subt_1__3), ._2(subt_1__2), ._1(subt_1__1),
    .carry(subt_1_carry));
  mascara_ligar mascara_ligar_1 (
    .Y___25(Y___25), .A___1(A___1), .S___19(S___19), .M___13(M___13), .I___9(I___9), .N___14(N___14),
    .E___5(E___5), .M___13_2(M___13_2), .carry(mascara_ligar_1_carry), .a(mascara_ligar_1_a),
    .b(mascara_ligar_1_b), .c(mascara_ligar_1_c), .d(mascara_ligar_1_d));
  comparador comparador_1 (
    .Y___25(Y___25), .A___1(A___1), .S___19(S___19), .M___13(M___13), .I___9(I___9), .N___14(N___14),
    .E___5(E___5), .M___13_2(M___13_2), .d(comparador_1_d), .c(comparador_1_c), .b(comparador_1_b),
    .a(comparador_1_a), .carry(comparador_1_carry));
  Multiplexer #(.select(2)) multiplexer_1 (
    .in0(soma_1__4), .in1(subt_1__4), .in2(mascara_ligar_1_d), .in3(comparador_1_d), .out(A0), .sel(M));  // open: en
  Multiplexer #(.select(2)) multiplexer_2 (
    .in0(soma_1__3), .in1(subt_1__3), .in2(mascara_ligar_1_c), .in3(comparador_1_c), .out(A1), .sel(M));  // open: en
  Multiplexer #(.select(2)) multiplexer_3 (
    .in0(soma_1__2), .in1(subt_1__2), .in2(mascara_ligar_1_b), .in3(comparador_1_b), .out(A2), .sel(M));  // open: en
  Multiplexer #(.select(2)) multiplexer_4 (
    .in0(soma_1__1), .in1(subt_1__1), .in2(mascara_ligar_1_a), .in3(comparador_1_a), .out(A3), .sel(M));  // open: en
  Multiplexer #(.select(2)) multiplexer_5 (
    .in0(soma_1_carry), .in1(subt_1_carry), .in2(mascara_ligar_1_carry), .in3(comparador_1_carry),
    .out(carry), .sel(M));  // open: en
endmodule

module SUM (
  input  A,
  input  B,
  output S,
  output Ts
);

  wire and_2_out, and_3_out, not_1_out, not_2_out;

  not not_1 (not_1_out, A);
  not not_2 (not_2_out, B);
  and and_1 (Ts, A, B);
  and and_2 (and_2_out, not_1_out, B);
  and and_3 (and_3_out, A, not_2_out);
  or or_1 (S, and_2_out, and_3_out);
endmodule

module SUB (
  input  A,
  input  B,
  output S,
  output Ts
);

  wire and_1_out, and_2_out, not_1_out, not_2_out, not_3_out;

  not not_1 (not_1_out, A);
  not not_2 (not_2_out, B);
  not not_3 (not_3_out, A);
  and and_1 (and_1_out, not_1_out, B);
  and and_2 (and_2_out, A, not_2_out);
  and and_3 (Ts, not_3_out, B);
  or or_1 (S, and_1_out, and_2_out);
endmodule

// SUB
module SUB2 (
  input  A,
  input  B,
  input  Te,
  output S,
  output Te2
);

  wire and_1_out, and_2_out, and_3_out, and_4_out, and_5_out, and_6_out, and_7_out, and_8_out, and_9_out,
       and_10_out, and_11_out, not_1_out, not_2_out, not_3_out, not_4_out, not_5_out, not_6_out, not_7_out,
       not_8_out, or_1_out, or_2_out, or_3_out;

  not not_1 (not_1_out, A);
  not not_2 (not_2_out, B);
  not not_3 (not_3_out, A);
  not not_4 (not_4_out, B);
  not not_5 (not_5_out, A);
  not not_6 (not_6_out, A);
  and and_1 (and_1_out, not_1_out, not_2_out);
  and and_2 (and_2_out, not_3_out, B);
  not not_7 (not_7_out, Te);
  and and_3 (and_3_out, A, not_4_out);
  not not_8 (not_8_out, Te);
  and and_4 (and_4_out, A, B);
  and and_5 (and_5_out, not_5_out, Te);
  and and_6 (and_6_out, not_6_out, B);
  and and_7 (and_7_out, and_1_out, Te);
  and and_8 (and_8_out, and_2_out, not_7_out);
  and and_9 (and_9_out, and_3_out, not_8_out);
  and and_10 (and_10_out, and_4_out, Te);
  or or_1 (or_1_out, and_5_out, and_6_out);
  and and_11 (and_11_out, B, Te);
  or or_2 (or_2_out, and_7_out, and_8_out);
  or or_3 (or_3_out, and_9_out, and_10_out);
  or or_4 (Te2, or_1_out, and_11_out);
  or or_5 (S, or_2_out, or_3_out);
endmodule

// SUM
module SUM2 (
  input  A,
  input  B,
  input  Te,
  output S,
  output Ts
);

  wire and_1_out, and_2_out, and_3_out, and_4_out, and_5_out, and_6_out, and_7_out, and_8_out, and_9_out,
       and_10_out, and_11_out, not_1_out, not_2_out, not_3_out, not_4_out, not_5_out, not_6_out, or_1_out,
       or_3_out, or_4_out;

  not not_1 (not_1_out, A);
  not not_2 (not_2_out, B);
  not not_3 (not_3_out, A);
  not not_4 (not_4_out, B);
  and and_1 (and_1_out, B, Te);
  and and_2 (and_2_out, A, Te);
  and and_3 (and_3_out, not_1_out, not_2_out);
  and and_4 (and_4_out, not_3_out, B);
  not not_5 (not_5_out, Te);
  and and_5 (and_5_out, A, not_4_out);
  not not_6 (not_6_out, Te);
  and and_6 (and_6_out, A, B);
  or or_1 (or_1_out, and_1_out, and_2_out);
  and and_7 (and_7_out, A, B);
  and and_8 (and_8_out, and_3_out, Te);
  and and_9 (and_9_out, and_4_out, not_5_out);
  and and_10 (and_10_out, and_5_out, not_6_out);
  and and_11 (and_11_out, and_6_out, Te);
  or or_2 (Ts, or_1_out, and_7_out);
  or or_3 (or_3_out, and_8_out, and_9_out);
  or or_4 (or_4_out, and_10_out, and_11_out);
  or or_5 (S, or_3_out, or_4_out);
endmodule

// SUM
module SOMA (
  input  Y___25,
  input  A___1,
  input  S___19,
  input  M___13,
  input  I___9,
  input  N___14,
  input  E___5,
  input  M___13_2,
  output _4,
  output _3,
  output _2,
  output _1,
  output carry
);

  wire sum2_1_ts, sum2_2_ts, sum_1_ts;

  SUM sum_1 (.A(M___13), .B(M___13_2), .S(_4), .Ts(sum_1_ts));
  SUM2 sum2_1 (.A(S___19), .B(E___5), .Te(sum_1_ts), .S(_3), .Ts(sum2_1_ts));
  SUM2 sum2_2 (.A(A___1), .B(N___14), .Te(sum2_1_ts), .S(_2), .Ts(sum2_2_ts));
  SUM2 sum2_3 (.A(Y___25), .B(I___9), .Te(sum2_2_ts), .S(_1), .Ts(carry));
endmodule

module SUBT (
  input  Y___25,
  input  A___1,
  input  S___19,
  input  M___13,
  input  M___13_2,
  input  I___9,
  input  N___14,
  input  E___5,
  output _4,
  output _3,
  output _2,
  output _1,
  output carry
);

  wire sub2_1_te2, sub2_2_te2, sub_1_ts;

  SUB sub_1 (.A(M___13), .B(M___13_2), .S(_4), .Ts(sub_1_ts));
  SUB2 sub2_1 (.A(S___19), .B(E___5), .Te(sub_1_ts), .S(_3), .Te2(sub2_1_te2));
  SUB2 sub2_2 (.A(A___1), .B(N___14), .Te(sub2_1_te2), .S(_2), .Te2(sub2_2_te2));
  SUB2 sub2_3 (.A(Y___25), .B(I___9), .Te(sub2_2_te2), .S(_1), .Te2(carry));
endmodule

module geral (
  input  M___13,
  input  S___19,
  input  A___1,
  input  Y___25,
  input  [1:0] in_5,
  input  I___9,
  input  N___14,
  input  E___5,
  input  M___13_2,
  output overflow,
  output out_11,
  output out_12,
  output out_13,
  output out_14
);

  wire comparador_1_a, comparador_1_b, comparador_1_c, comparador_1_carry, comparador_1_d, deslocamento_1_a,
       deslocamento_1_b, deslocamento_1_c, deslocamento_1_carry, deslocamento_1_d, soma_1__1, soma_1__2,
       soma_1__3, soma_1__4, soma_1_carry, subt_1__1, subt_1__2, subt_1__3, subt_1__4, subt_1_carry;

  SOMA soma_1 (
    .Y___25(Y___25), .A___1(A___1), .S___19(S___19), .M___13(M___13), .I___9(I___9), .N___14(N___14),
    .E___5(E___5), .M___13_2(M___13_2), ._4(soma_1__4), ._3(soma_1__3), ._2(soma_1__2), ._1(soma_1__1),
    .carry(soma_1_carry));
  SUBT subt_1 (
    .Y___25(Y___25), .A___1(A___1), .S___19(S___19), .M___13(M___13), .I___9(I___9), .N___14(N___14),
    .E___5(E___5), .M___13_2(M___13_2), ._4(subt_1__4), ._3(subt_1__3), ._2(subt_1__2), ._1(subt_1__1),
    .carry(subt_1_carry));
  comparador comparador_1 (
    .Y___25(Y___25), .A___1(A___1), .S___19(S___19), .M___13(M___13), .I___9(I___9), .N___14(N___14),
    .E___5(E___5), .M___13_2(M___13_2), .d(comparador_1_d), .c(comparador_1_c), .b(comparador_1_b),
    .a(comparador_1_a), .carry(comparador_1_carry));
  deslocamento deslocamento_1 (
    .Y___25(Y___25), .A___1(A___1), .S___19(S___19), .M___13(M___13), .I___9(I___9), .N___14(N___14),
    .E___5(E___5), .M___13_2(M___13_2), .d(deslocamento_1_d), .c(deslocamento_1_c), .b(deslocamento_1_b),
    .a(deslocamento_1_a), .carry(deslocamento_1_carry));
  Multiplexer #(.select(2)) multiplexer_1 (
    .in0(soma_1_carry), .in1(subt_1_carry), .in2(comparador_1_d), .in3(deslocamento_1_carry), .out(overflow),
    .sel(in_5));  // open: en
  Multiplexer #(.select(2)) multiplexer_2 (
    .in0(soma_1__1), .in1(subt_1__1), .in2(comparador_1_c), .in3(deslocamento_1_a), .out(out_11), .sel(in_5));  // open: en
  Multiplexer #(.select(2)) multiplexer_3 (
    .in0(soma_1__2), .in1(subt_1__2), .in2(comparador_1_b), .in3(deslocamento_1_b), .out(out_12), .sel(in_5));  // open: en
  Multiplexer #(.select(2)) multiplexer_4 (
    .in0(soma_1__3), .in1(subt_1__3), .in2(comparador_1_a), .in3(deslocamento_1_c), .out(out_13), .sel(in_5));  // open: en
  Multiplexer #(.select(2)) multiplexer_5 (
    .in0(soma_1__4), .in1(subt_1__4), .in2(comparador_1_carry), .in3(deslocamento_1_d), .out(out_14),
    .sel(in_5));  // open: en
endmodule

module comparador (
  input  Y___25,
  input  A___1,
  input  S___19,
  input  M___13,
  input  M___13_2,
  input  I___9,
  input  N___14,
  input  E___5,
  output d,
  output c,
  output b,
  output a,
  output carry
);

  wire not_1_out, not_2_out, not_3_out, not_4_out, xor_1_out, xor_2_out, xor_3_out, xor_4_out;

  xor xor_1 (xor_1_out, M___13, M___13_2);
  not not_1 (not_1_out, xor_1_out);
  not not_2 (not_2_out, xor_2_out);
  xor xor_2 (xor_2_out, S___19, E___5);
  xor xor_3 (xor_3_out, A___1, N___14);
  not not_3 (not_3_out, xor_3_out);
  xor xor_4 (xor_4_out, Y___25, I___9);
  not not_4 (not_4_out, xor_4_out);
  and and_1 (d, not_1_out, not_2_out, not_3_out, not_4_out);

  assign a = 1'b0;
  assign b = 1'b0;
  assign c = 1'b0;
  assign carry = 1'b0;
endmodule

module mascara_ligar (
  input  Y___25,
  input  A___1,
  input  S___19,
  input  M___13,
  input  I___9,
  input  N___14,
  input  M___13_2,
  input  E___5,
  output carry,
  output a,
  output b,
  output c,
  output d
);

  wire and_1_out, and_2_out, and_3_out, and_4_out, not_1_out, not_2_out;

  not not_1 (not_1_out, E___5);
  not not_2 (not_2_out, M___13_2);
  and and_1 (and_1_out, E___5, M___13_2);
  and and_2 (and_2_out, E___5, not_2_out);
  and and_3 (and_3_out, not_1_out, M___13_2);
  and and_4 (and_4_out, not_1_out, not_2_out);
  or or_1 (a, Y___25, and_1_out);
  or or_2 (b, A___1, and_2_out);
  or or_3 (c, S___19, and_3_out);
  or or_4 (d, M___13, and_4_out);

  assign carry = 1'b0;
endmodule

module mascara_desligar (
  input  Y___25,
  input  A___1,
  input  S___19,
  input  M___13,
  input  M___13_2,
  input  I___9,
  input  N___14,
  input  E___5,
  output out_9,
  output out_10,
  output out_11,
  output out_12,
  output carry
);

  wire and_1_out, and_2_out, and_3_out, and_4_out, and_5_out, and_6_out, and_7_out, and_8_out, and_9_out,
       and_10_out, and_11_out, and_12_out, and_13_out, and_14_out, and_15_out, and_16_out, not_1_out,
       not_2_out, not_3_out, not_4_out;

  not not_1 (not_1_out, E___5);
  not not_2 (not_2_out, M___13_2);
  not not_3 (not_3_out, E___5);
  and and_1 (and_1_out, M___13, M___13_2);
  and and_2 (and_2_out, M___13, E___5);
  and and_3 (and_3_out, M___13, N___14);
  and and_4 (and_4_out, M___13, I___9);
  not not_4 (not_4_out, M___13_2);
  and and_5 (and_5_out, A___1, M___13_2);
  and and_6 (and_6_out, A___1, not_1_out);
  and and_7 (and_7_out, A___1, N___14);
  and and_8 (and_8_out, A___1, I___9);
  and and_9 (and_9_out, Y___25, not_2_out);
  and and_10 (and_10_out, Y___25, not_3_out);
  and and_11 (and_11_out, Y___25, N___14);
  and and_12 (and_12_out, Y___25, I___9);
  or or_1 (out_9, and_1_out, and_2_out, and_3_out, and_4_out);
  and and_13 (and_13_out, S___19, not_4_out);
  and and_14 (and_14_out, S___19, E___5);
  and and_15 (and_15_out, S___19, N___14);
  and and_16 (and_16_out, S___19, I___9);
  or or_2 (out_11, and_5_out, and_6_out, and_7_out, and_8_out);
  or or_3 (out_12, and_9_out, and_10_out, and_11_out, and_12_out);
  or or_4 (out_10, and_13_out, and_14_out, and_15_out, and_16_out);

  assign carry = 1'b0;
endmodule

module mascara_modificar (
  input  Y___25,
  input  A___1,
  input  S___19,
  input  M___13,
  input  M___13_2,
  input  I___9,
  input  N___14,
  input  E___5,
  output out_9,
  output out_10,
  output out_11,
  output out_12,
  output carry
);

  wire and_1_out, and_2_out, and_3_out, and_4_out, and_5_out, and_6_out, and_7_out, and_8_out, and_9_out,
       and_10_out, and_11_out, and_12_out, not_1_out, not_2_out, not_3_out, not_4_out, not_5_out, not_6_out;

  not not_1 (not_1_out, E___5);
  not not_2 (not_2_out, M___13_2);
  not not_3 (not_3_out, M___13);
  and and_1 (and_1_out, S___19, E___5);
  not not_4 (not_4_out, S___19);
  not not_5 (not_5_out, Y___25);
  and and_2 (and_2_out, M___13, E___5);
  and and_3 (and_3_out, M___13, M___13_2);
  and and_4 (and_4_out, not_3_out, not_1_out, not_2_out);
  and and_5 (and_5_out, S___19, not_2_out);
  and and_6 (and_6_out, A___1, M___13_2);
  and and_7 (and_7_out, A___1, not_1_out);
  not not_6 (not_6_out, A___1);
  and and_8 (and_8_out, Y___25, not_2_out);
  and and_9 (and_9_out, Y___25, not_1_out);
  and and_10 (and_10_out, not_4_out, not_1_out, M___13_2);
  and and_11 (and_11_out, not_6_out, E___5, not_2_out);
  and and_12 (and_12_out, not_5_out, E___5, M___13_2);
  or or_1 (out_9, and_2_out, and_3_out, and_4_out);
  or or_2 (out_10, and_5_out, and_1_out, and_10_out);
  or or_3 (out_11, and_6_out, and_7_out, and_11_out);
  or or_4 (out_12, and_8_out, and_9_out, and_12_out);

  assign carry = 1'b0;
endmodule

module complemento_de_2 (
  input  Y___25,
  input  A___1,
  input  S___19,
  input  M___13,
  input  M___13_2,
  input  I___9,
  input  N___14,
  input  E___5,
  output out_9,
  output out_10,
  output out_11,
  output out_12,
  output carry
);

  wire not_1_out, not_2_out, not_3_out, not_4_out, not_5_out, sum_1_ts, sum_2_ts, sum_3_ts;

  not not_1 (not_1_out, M___13_2);
  not not_2 (not_2_out, M___13);
  not not_3 (not_3_out, S___19);
  not not_4 (not_4_out, A___1);
  not not_5 (not_5_out, Y___25);
  SUM sum_1 (.A(not_2_out), .B(not_1_out), .S(out_12), .Ts(sum_1_ts));
  SUM sum_2 (.A(not_3_out), .B(sum_1_ts), .S(out_11), .Ts(sum_2_ts));
  SUM sum_3 (.A(not_4_out), .B(sum_2_ts), .S(out_10), .Ts(sum_3_ts));
  SUM sum_4 (.A(not_5_out), .B(sum_3_ts), .S(out_9), .Ts(carry));
endmodule

module deslocamento (
  input  Y___25,
  input  A___1,
  input  S___19,
  input  M___13,
  input  M___13_2,
  input  I___9,
  input  N___14,
  input  E___5,
  output d,
  output c,
  output b,
  output a,
  output carry
);

  Multiplexer multiplexer_1 (.in0(1'b0), .in1(S___19), .out(d), .sel(M___13_2));  // open: en
  Multiplexer multiplexer_2 (.in0(M___13), .in1(A___1), .out(c), .sel(M___13_2));  // open: en
  Multiplexer multiplexer_3 (.in0(S___19), .in1(Y___25), .out(b), .sel(M___13_2));  // open: en
  Multiplexer multiplexer_4 (.in0(A___1), .in1(1'b0), .out(a), .sel(M___13_2));  // open: en

  assign carry = 1'b0;
endmodule

module gerador_de_paridade (
  input  Y___25,
  input  A___1,
  input  S___19,
  input  M___13,
  input  M___13_2,
  input  I___9,
  input  N___14,
  input  E___5,
  output out_9,
  output out_10,
  output out_11,
  output out_12,
  output carry
);

  wire xor_1_out, xor_2_out;

  xor xor_1 (xor_1_out, A___1, Y___25);
  xor xor_2 (xor_2_out, M___13, S___19);
  xor xor_3 (out_9, xor_2_out, xor_1_out);

  assign carry = 1'b0;
  assign out_10 = 1'b0;
  assign out_11 = 1'b0;
  assign out_12 = 1'b0;
endmodule

module codificador_de_prioridade (
  input  Y___25,
  input  A___1,
  input  S___19,
  input  M___13,
  input  M___13_2,
  input  I___9,
  input  N___14,
  input  E___5,
  output out_9,
  output out_10,
  output out_11,
  output out_12,
  output carry
);

  wire not_1_out, not_2_out, not_3_out;

  not not_1 (not_1_out, I___9);
  not not_2 (not_2_out, N___14);
  not not_3 (not_3_out, E___5);
  and and_1 (out_9, not_1_out, not_2_out, not_3_out, M___13_2);
  and and_2 (out_10, not_1_out, not_2_out, E___5);
  and and_3 (out_11, not_1_out, N___14);

  assign carry = 1'b0;
  assign out_12 = I___9;
endmodule
