// Logisim project trabalho04.circ as structural Verilog: 2 circuits, main circuit main
module main (
  input  in_1,
  input  in_2,
  input  in_3
);

  wire bin_2_alfab_1_a_2, bin_2_alfab_1_b_2, bin_2_alfab_1_c_2, bin_2_alfab_1_d, bin_2_alfab_1_e,
       bin_2_alfab_1_f, bin_2_alfab_1_g;

  bin_2_alfab bin_2_alfab_1 (
    .a(in_1), .b(in_2), .c(in_3), .a_2(bin_2_alfab_1_a_2), .b_2(bin_2_alfab_1_b_2), .c_2(bin_2_alfab_1_c_2),
    .d(bin_2_alfab_1_d), .e(bin_2_alfab_1_e), .f(bin_2_alfab_1_f), .g(bin_2_alfab_1_g));
  _7_Segment_Display u_7_segment_display_1 (
    .g(bin_2_alfab_1_g), .f(bin_2_alfab_1_f), .a(bin_2_alfab_1_a_2), .b(bin_2_alfab_1_b_2),
    .e(bin_2_alfab_1_e), .d(bin_2_alfab_1_d), .c(bin_2_alfab_1_c_2));  // open: dp
endmodule

module bin_2_alfab (
  input  a,
  input  b,
  input  c,
  output a_2,
  output b_2,
  output c_2,
  output d,
  output e,
  output f,
  output g
);

  wire and_1_out, and_2_out, and_3_out, and_4_out, and_5_out, and_6_out, and_7_out, and_8_out, not_1_out,
       not_2_out, not_3_out, not_4_out, not_5_out, not_6_out, not_7_out, not_8_out, not_9_out, not_10_out,
       not_11_out, not_12_out, not_13_out, not_14_out, or_7_out;

  not not_1 (not_1_out, a);
  and and_1 (and_1_out, not_1_out, c);
  not not_2 (not_2_out, a);
  and and_2 (and_2_out, not_2_out, not_3_out);
  not not_3 (not_3_out, b);
  not not_4 (not_4_out, a);
  and and_3 (and_3_out, not_4_out, c);
  not not_5 (not_5_out, a);
  or or_1 (c_2, not_5_out, c);
  not not_6 (not_6_out, a);
  and and_4 (and_4_out, not_6_out, not_7_out);
  not not_7 (not_7_out, c);
  and and_5 (and_5_out, b, not_8_out);
  not not_8 (not_8_out, c);
  or or_2 (e, c, a);
  not not_9 (not_9_out, a);
  or or_3 (f, not_9_out, not_10_out);
  not not_10 (not_10_out, c);
  not not_11 (not_11_out, a);
  and and_6 (and_6_out, not_11_out, not_12_out);
  not not_12 (not_12_out, b);
  not not_13 (not_13_out, b);
  and and_7 (and_7_out, not_13_out, c);
  not not_14 (not_14_out, c);
  or or_4 (a_2, and_1_out, b);
  or or_5 (b_2, and_2_out, and_3_out);
  or or_6 (d, and_4_out, and_5_out);
  or or_7 (or_7_out, and_6_out, and_7_out);
  and and_8 (and_8_out, b, not_14_out);
  or or_8 (g, or_7_out, and_8_out);
endmodule
