// Logisim project trabalho05.circ as structural Verilog: 5 circuits, main circuit main
module main (
  input  in_1,
  input  reset,
  input  clear,
  output out_4,
  output out_5,
  output out_6,
  output out_7
);

  wire clock_1_out, display_1_a, display_1_b, display_1_c, display_1_d, display_1_e, display_1_f, display_1_g;

  Clock clock_1 (.out(clock_1_out));
  display display_1 (
    .entrada1(in_1), .clock(clock_1_out), .s4(out_4), .s3(out_5), .s2(out_6), .s1(out_7), .a(display_1_a),
    .b(display_1_b), .c(display_1_c), .d(display_1_d), .e(display_1_e), .f(display_1_f), .g(display_1_g),
    .reset(reset), .clear(clear));
  _7_Segment_Display u_7_segment_display_1 (
    .g(display_1_g), .f(display_1_f), .a(display_1_a), .b(display_1_b), .e(display_1_e), .d(display_1_d),
    .c(display_1_c));  // open: dp
endmodule

module contador (
  input  e4,
  input  e3,
  input  e2,
  input  rs4,
  input  c4,
  input  e1,
  input  rs3,
  input  c3,
  input  clock,
  input  rs2,
  input  c2,
  input  rs1,
  input  c1,
  output s4,
  output s3,
  output s2,
  output s1,
  output b1,
  output b2,
  output b3,
  output b4
);

  clock clock_1 (.PR(rs1), .J(e1), .CLOCK(clock), .K(e1), .CLR(c1), .Q(b1), .Q_(s1));
  clock clock_2 (.PR(rs2), .J(e2), .CLOCK(b1), .K(e2), .CLR(c2), .Q(b2), .Q_(s2));
  clock clock_3 (.PR(rs3), .J(e3), .CLOCK(b2), .K(e3), .CLR(c3), .Q(b3), .Q_(s3));
  clock clock_4 (.PR(rs4), .J(e4), .CLOCK(b3), .K(e4), .CLR(c4), .Q(b4), .Q_(s4));
endmodule

module clock (
  input  PR,
  input  J,
  input  CLOCK,
  input  K,
  input  CLR,
  output Q,
  output Q_
);

  wire nand_1_out, nand_2_out, nand_3_out, nand_4_out, nand_5_out, nand_6_out, not_1_out;

  nand nand_1 (nand_1_out, J, CLOCK, Q_);
  nand nand_2 (nand_2_out, Q, CLOCK, K);
  not not_1 (not_1_out, CLOCK);
  nand nand_3 (nand_3_out, nand_1_out, PR, nand_4_out);
  nand nand_4 (nand_4_out, nand_3_out, CLR, nand_2_out);
  nand nand_5 (nand_5_out, nand_3_out, not_1_out);
  nand nand_6 (nand_6_out, nand_4_out, not_1_out);
  nand nand_7 (Q, nand_5_out, PR, Q_);
  nand nand_8 (Q_, Q, CLR, nand_6_out);
endmodule

module cont_7_seg (
  input  d4,
  input  d3,
  input  d2,
  input  d1,
  output a,
  output b,
  output c,
  output d,
  output e,
  output f,
  output g
);

  wire and_1_out, and_2_out, and_3_out, and_4_out, and_5_out, and_6_out, and_7_out, and_8_out, and_9_out,
       and_10_out, and_11_out, and_12_out, and_13_out, and_14_out, and_15_out, and_16_out, and_17_out,
       and_18_out, and_19_out, and_20_out, and_21_out, and_22_out, and_23_out, and_24_out, and_25_out,
       and_26_out, and_27_out, and_28_out, and_29_out, and_30_out, and_31_out, and_32_out, and_33_out,
       and_34_out, and_35_out, and_36_out, and_37_out, and_38_out, and_39_out, and_40_out, and_41_out,
       and_42_out, and_43_out, and_44_out, and_45_out, and_46_out, not_1_out, not_2_out, not_3_out,
       not_4_out, not_5_out, not_6_out, not_7_out, not_8_out, not_9_out, not_10_out, not_11_out, not_12_out,
       not_13_out, not_14_out, not_15_out, not_16_out, not_17_out, not_18_out, not_19_out, not_20_out,
       not_21_out, not_22_out, not_23_out, not_24_out, not_25_out, not_26_out, not_27_out, not_28_out,
       not_29_out, not_30_out, not_31_out, not_32_out, not_33_out, not_34_out, not_35_out, not_36_out,
       not_37_out, not_38_out, not_39_out, not_40_out, not_41_out, not_42_out, not_43_out, or_1_out,
       or_2_out, or_3_out, or_4_out, or_5_out, or_6_out, or_7_out, or_8_out, or_9_out, or_10_out, or_12_out,
       or_13_out, or_14_out, or_15_out, or_16_out, or_17_out, or_18_out, or_20_out, or_21_out, or_22_out,
       or_23_out;

  not not_1 (not_1_out, d3);
  not not_2 (not_2_out, d1);
  not not_3 (not_3_out, d4);
  not not_4 (not_4_out, d4);
  and and_1 (and_1_out, d4, not_5_out);
  not not_5 (not_5_out, d3);
  not not_6 (not_6_out, d2);
  not not_7 (not_7_out, d4);
  not not_8 (not_8_out, d3);
  not not_9 (not_9_out, d4);
  and and_2 (and_2_out, not_9_out, not_10_out);
  not not_10 (not_10_out, d2);
  not not_11 (not_11_out, d1);
  not not_12 (not_12_out, d4);
  not not_13 (not_13_out, d2);
  not not_14 (not_14_out, d4);
  and and_3 (and_3_out, not_14_out, not_15_out);
  not not_15 (not_15_out, d2);
  not not_16 (not_16_out, d4);
  and and_4 (and_4_out, not_16_out, d1);
  not not_17 (not_17_out, d2);
  not not_18 (not_18_out, d4);
  not not_19 (not_19_out, d3);
  not not_20 (not_20_out, d4);
  and and_5 (and_5_out, not_20_out, not_21_out);
  not not_21 (not_21_out, d3);
  not not_22 (not_22_out, d1);
  not not_23 (not_23_out, d3);
  and and_6 (and_6_out, not_23_out, d2);
  not not_24 (not_24_out, d2);
  not not_25 (not_25_out, d3);
  and and_7 (and_7_out, not_25_out, not_26_out);
  not not_26 (not_26_out, d1);
  and and_8 (and_8_out, d2, not_27_out);
  not not_27 (not_27_out, d1);
  and and_9 (and_9_out, d4, d2);
  and and_10 (and_10_out, d4, d3);
  not not_28 (not_28_out, d2);
  not not_29 (not_29_out, d1);
  not not_30 (not_30_out, d4);
  and and_11 (and_11_out, not_30_out, d3);
  not not_31 (not_31_out, d2);
  not not_32 (not_32_out, d3);
  and and_12 (and_12_out, not_32_out, d2);
  and and_13 (and_13_out, d2, not_33_out);
  not not_33 (not_33_out, d1);
  not not_34 (not_34_out, d4);
  and and_14 (and_14_out, not_34_out, d3);
  not not_35 (not_35_out, d2);
  not not_36 (not_36_out, d3);
  and and_15 (and_15_out, not_1_out, not_2_out);
  and and_16 (and_16_out, not_3_out, d2);
  and and_17 (and_17_out, not_4_out, d3);
  and and_18 (and_18_out, d3, d2);
  and and_19 (and_19_out, and_1_out, not_6_out);
  not not_37 (not_37_out, d1);
  and and_20 (and_20_out, not_7_out, not_8_out);
  and and_21 (and_21_out, and_2_out, not_11_out);
  not not_38 (not_38_out, d3);
  not not_39 (not_39_out, d1);
  and and_22 (and_22_out, not_12_out, d2);
  and and_23 (and_23_out, d4, not_13_out);
  or or_1 (or_1_out, and_3_out, and_4_out);
  and and_24 (and_24_out, not_17_out, d1);
  and and_25 (and_25_out, not_18_out, d3);
  and and_26 (and_26_out, d4, not_19_out);
  and and_27 (and_27_out, and_5_out, not_22_out);
  and and_28 (and_28_out, and_6_out, d1);
  and and_29 (and_29_out, d3, not_24_out);
  and and_30 (and_30_out, d3, d2);
  not not_40 (not_40_out, d1);
  not not_41 (not_41_out, d2);
  or or_2 (or_2_out, and_7_out, and_8_out);
  or or_3 (or_3_out, and_9_out, and_10_out);
  and and_31 (and_31_out, not_28_out, not_29_out);
  and and_32 (and_32_out, and_11_out, not_31_out);
  not not_42 (not_42_out, d1);
  not not_43 (not_43_out, d3);
  or or_4 (or_4_out, and_12_out, and_13_out);
  and and_33 (and_33_out, and_14_out, not_35_out);
  and and_34 (and_34_out, d4, not_36_out);
  and and_35 (and_35_out, d4, d1);
  or or_5 (or_5_out, and_15_out, and_16_out);
  and and_36 (and_36_out, and_17_out, d1);
  or or_6 (or_6_out, and_18_out, and_19_out);
  and and_37 (and_37_out, d4, not_37_out);
  or or_7 (or_7_out, and_20_out, and_21_out);
  and and_38 (and_38_out, not_38_out, not_39_out);
  and and_39 (and_39_out, and_22_out, d1);
  and and_40 (and_40_out, and_23_out, d1);
  or or_8 (or_8_out, or_1_out, and_24_out);
  or or_9 (or_9_out, and_25_out, and_26_out);
  or or_10 (or_10_out, and_27_out, and_28_out);
  and and_41 (and_41_out, and_29_out, d1);
  and and_42 (and_42_out, and_30_out, not_40_out);
  and and_43 (and_43_out, d4, not_41_out);
  or or_11 (e, or_2_out, or_3_out);
  or or_12 (or_12_out, and_31_out, and_32_out);
  and and_44 (and_44_out, d3, not_42_out);
  and and_45 (and_45_out, d4, not_43_out);
  and and_46 (and_46_out, d4, d2);
  or or_13 (or_13_out, or_4_out, and_33_out);
  or or_14 (or_14_out, and_34_out, and_35_out);
  or or_15 (or_15_out, or_5_out, and_36_out);
  or or_16 (or_16_out, or_6_out, and_37_out);
  or or_17 (or_17_out, or_7_out, and_38_out);
  or or_18 (or_18_out, and_39_out, and_40_out);
  or or_19 (c, or_8_out, or_9_out);
  or or_20 (or_20_out, or_10_out, and_41_out);
  or or_21 (or_21_out, and_42_out, and_43_out);
  or or_22 (or_22_out, or_12_out, and_44_out);
  or or_23 (or_23_out, and_45_out, and_46_out);
  or or_24 (g, or_13_out, or_14_out);
  or or_25 (a, or_15_out, or_16_out);
  or or_26 (b, or_17_out, or_18_out);
  or or_27 (d, or_20_out, or_21_out);
  or or_28 (f, or_22_out, or_23_out);
endmodule

module display (
  input  entrada1,
  input  clock,
  input  reset,
  input  clear,
  output s4,
  output s3,
  output s2,
  output s1,
  output a,
  output b,
  output c,
  output d,
  output e,
  output f,
  output g
);

  wire contador_1_b1, contador_1_b2, contador_1_b3, contador_1_b4;

  contador contador_1 (
    .e4(entrada1), .e3(entrada1), .e2(entrada1), .e1(entrada1), .s4(s4), .s3(s3), .s2(s2), .s1(s1),
    .b1(contador_1_b1), .b2(contador_1_b2), .b3(contador_1_b3), .b4(contador_1_b4), .rs1(reset), .c1(clear),
    .rs2(reset), .c2(clear), .rs3(reset), .c3(clear), .rs4(reset), .c4(clear), .clock(clock));
  cont_7_seg cont_7_seg_1 (
    .d4(contador_1_b4), .d3(contador_1_b3), .d2(contador_1_b2), .d1(contador_1_b1), .a(a), .b(b), .c(c),
    .d(d), .e(e), .f(f), .g(g));
endmodule
