// Logisim project trabalho07.circ as structural Verilog: 17 circuits, main circuit main
module main (
  input  e1,
  input  clock,
  input  preset,
  input  clear,
  output a,
  output b,
  output c,
  output d,
  output e,
  output f,
  output g,
  output b4,
  output b3,
  output b2,
  output b1
);

  wire display_1_s4;

  DISPLAY display_1 (
    .e1(e1), .clock(clock), .s4(display_1_s4), .s3(display_1_s4), .a(a), .b(b), .c(c), .d(d), .e(e), .f(f),
    .g(g), .rs(preset), .clr(clear), .b4(b4), .b3(b3), .b2(b2), .b1(b1));  // open: s2, s1
  _7_Segment_Display u_7_segment_display_1 (.g(g), .f(f), .a(a), .b(b), .e(e), .d(d), .c(c));  // open: dp
endmodule

module ff_me_psc_t (
  input  PreSet,
  input  J,
  input  CLOCK,
  input  CLR,
  output Q,
  output Q_
);

  wire nand_1_out, nand_2_out, nand_3_out, nand_4_out, nand_5_out, nand_6_out, not_1_out;

  nand nand_1 (nand_1_out, J, CLOCK, Q_);
  nand nand_2 (nand_2_out, Q, CLOCK, J);
  not not_1 (not_1_out, CLOCK);
  nand nand_3 (nand_3_out, nand_1_out, PreSet, nand_4_out);
  nand nand_4 (nand_4_out, nand_3_out, CLR, nand_2_out);
  nand nand_5 (nand_5_out, nand_3_out, not_1_out);
  nand nand_6 (nand_6_out, nand_4_out, not_1_out);
  nand nand_7 (Q, nand_5_out, PreSet, Q_);
  nand nand_8 (Q_, Q, CLR, nand_6_out);
endmodule

module estrutura (
  input  clock,
  input  pin1,
  input  pin2,
  input  pin3,
  input  pin4,
  input  c1,
  input  c2,
  input  clr,
  output s1,
  output s2,
  output s3,
  output s4
);
endmodule

// mux
module muxd2 (
  input  _00,
  input  _01,
  input  e1,
  output saida
);

  wire and_1_out, and_2_out, not_1_out, or_1_out;

  not not_1 (not_1_out, e1);
  and and_1 (and_1_out, _00, e1);
  and and_2 (and_2_out, _01, not_1_out);
  or or_1 (or_1_out, and_1_out, and_2_out);
  not not_2 (saida, or_1_out);
endmodule

module cont_7_seg (
  input  d4,
  input  d3,
  input  d2,
  input  d1,
  output a,
  output b,
  output c,
  output d,
  output e,
  output f,
  output g
);

  wire and_1_out, and_2_out, and_3_out, and_4_out, and_5_out, and_6_out, and_7_out, and_8_out, and_9_out,
       and_10_out, and_11_out, and_12_out, and_13_out, and_14_out, and_15_out, and_16_out, and_17_out,
       and_18_out, and_19_out, and_20_out, and_21_out, and_22_out, and_23_out, and_24_out, and_25_out,
       and_26_out, and_27_out, and_28_out, and_29_out, and_30_out, and_31_out, and_32_out, and_33_out,
       and_34_out, and_35_out, and_36_out, and_37_out, and_38_out, and_39_out, and_40_out, and_41_out,
       and_42_out, and_43_out, and_44_out, and_45_out, and_46_out, not_1_out, not_2_out, not_3_out,
       not_4_out, not_5_out, not_6_out, not_7_out, not_8_out, not_9_out, not_10_out, not_11_out, not_12_out,
       not_13_out, not_14_out, not_15_out, not_16_out, not_17_out, not_18_out, not_19_out, not_20_out,
       not_21_out, not_22_out, not_23_out, not_24_out, not_25_out, not_26_out, not_27_out, not_28_out,
       not_29_out, not_30_out, not_31_out, not_32_out, not_33_out, not_34_out, not_35_out, not_36_out,
       not_37_out, not_38_out, not_39_out, not_40_out, not_41_out, not_42_out, not_43_out, or_1_out,
       or_2_out, or_3_out, or_4_out, or_5_out, or_6_out, or_7_out, or_8_out, or_9_out, or_10_out, or_12_out,
       or_13_out, or_14_out, or_15_out, or_16_out, or_17_out, or_18_out, or_20_out, or_21_out, or_22_out,
       or_23_out;

  not not_1 (not_1_out, d3);
  not not_2 (not_2_out, d1);
  not not_3 (not_3_out, d4);
  not not_4 (not_4_out, d4);
  and and_1 (and_1_out, d4, not_5_out);
  not not_5 (not_5_out, d3);
  not not_6 (not_6_out, d2);
  not not_7 (not_7_out, d4);
  not not_8 (not_8_out, d3);
  not not_9 (not_9_out, d4);
  and and_2 (and_2_out, not_9_out, not_10_out);
  not not_10 (not_10_out, d2);
  not not_11 (not_11_out, d1);
  not not_12 (not_12_out, d4);
  not not_13 (not_13_out, d2);
  not not_14 (not_14_out, d4);
  and and_3 (and_3_out, not_14_out, not_15_out);
  not not_15 (not_15_out, d2);
  not not_16 (not_16_out, d4);
  and and_4 (and_4_out, not_16_out, d1);
  not not_17 (not_17_out, d2);
  not not_18 (not_18_out, d4);
  not not_19 (not_19_out, d3);
  not not_20 (not_20_out, d4);
  and and_5 (and_5_out, not_20_out, not_21_out);
  not not_21 (not_21_out, d3);
  not not_22 (not_22_out, d1);
  not not_23 (not_23_out, d3);
  and and_6 (and_6_out, not_23_out, d2);
  not not_24 (not_24_out, d2);
  not not_25 (not_25_out, d3);
  and and_7 (and_7_out, not_25_out, not_26_out);
  not not_26 (not_26_out, d1);
  and and_8 (and_8_out, d2, not_27_out);
  not not_27 (not_27_out, d1);
  and and_9 (and_9_out, d4, d2);
  and and_10 (and_10_out, d4, d3);
  not not_28 (not_28_out, d2);
  not not_29 (not_29_out, d1);
  not not_30 (not_30_out, d4);
  and and_11 (and_11_out, not_30_out, d3);
  not not_31 (not_31_out, d2);
  not not_32 (not_32_out, d3);
  and and_12 (and_12_out, not_32_out, d2);
  and and_13 (and_13_out, d2, not_33_out);
  not not_33 (not_33_out, d1);
  not not_34 (not_34_out, d4);
  and and_14 (and_14_out, not_34_out, d3);
  not not_35 (not_35_out, d2);
  not not_36 (not_36_out, d3);
  and and_15 (and_15_out, not_1_out, not_2_out);
  and and_16 (and_16_out, not_3_out, d2);
  and and_17 (and_17_out, not_4_out, d3);
  and and_18 (and_18_out, d3, d2);
  and and_19 (and_19_out, and_1_out, not_6_out);
  not not_37 (not_37_out, d1);
  and and_20 (and_20_out, not_7_out, not_8_out);
  and and_21 (and_21_out, and_2_out, not_11_out);
  not not_38 (not_38_out, d3);
  not not_39 (not_39_out, d1);
  and and_22 (and_22_out, not_12_out, d2);
  and and_23 (and_23_out, d4, not_13_out);
  or or_1 (or_1_out, and_3_out, and_4_out);
  and and_24 (and_24_out, not_17_out, d1);
  and and_25 (and_25_out, not_18_out, d3);
  and and_26 (and_26_out, d4, not_19_out);
  and and_27 (and_27_out, and_5_out, not_22_out);
  and and_28 (and_28_out, and_6_out, d1);
  and and_29 (and_29_out, d3, not_24_out);
  and and_30 (and_30_out, d3, d2);
  not not_40 (not_40_out, d1);
  not not_41 (not_41_out, d2);
  or or_2 (or_2_out, and_7_out, and_8_out);
  or or_3 (or_3_out, and_9_out, and_10_out);
  and and_31 (and_31_out, not_28_out, not_29_out);
  and and_32 (and_32_out, and_11_out, not_31_out);
  not not_42 (not_42_out, d1);
  not not_43 (not_43_out, d3);
  or or_4 (or_4_out, and_12_out, and_13_out);
  and and_33 (and_33_out, and_14_out, not_35_out);
  and and_34 (and_34_out, d4, not_36_out);
  and and_35 (and_35_out, d4, d1);
  or or_5 (or_5_out, and_15_out, and_16_out);
  and and_36 (and_36_out, and_17_out, d1);
  or or_6 (or_6_out, and_18_out, and_19_out);
  and and_37 (and_37_out, d4, not_37_out);
  or or_7 (or_7_out, and_20_out, and_21_out);
  and and_38 (and_38_out, not_38_out, not_39_out);
  and and_39 (and_39_out, and_22_out, d1);
  and and_40 (and_40_out, and_23_out, d1);
  or or_8 (or_8_out, or_1_out, and_24_out);
  or or_9 (or_9_out, and_25_out, and_26_out);
  or or_10 (or_10_out, and_27_out, and_28_out);
  and and_41 (and_41_out, and_29_out, d1);
  and and_42 (and_42_out, and_30_out, not_40_out);
  and and_43 (and_43_out, d4, not_41_out);
  or or_11 (e, or_2_out, or_3_out);
  or or_12 (or_12_out, and_31_out, and_32_out);
  and and_44 (and_44_out, d3, not_42_out);
  and and_45 (and_45_out, d4, not_43_out);
  and and_46 (and_46_out, d4, d2);
  or or_13 (or_13_out, or_4_out, and_33_out);
  or or_14 (or_14_out, and_34_out, and_35_out);
  or or_15 (or_15_out, or_5_out, and_36_out);
  or or_16 (or_16_out, or_6_out, and_37_out);
  or or_17 (or_17_out, or_7_out, and_38_out);
  or or_18 (or_18_out, and_39_out, and_40_out);
  or or_19 (c, or_8_out, or_9_out);
  or or_20 (or_20_out, or_10_out, and_41_out);
  or or_21 (or_21_out, and_42_out, and_43_out);
  or or_22 (or_22_out, or_12_out, and_44_out);
  or or_23 (or_23_out, and_45_out, and_46_out);
  or or_24 (g, or_13_out, or_14_out);
  or or_25 (a, or_15_out, or_16_out);
  or or_26 (b, or_17_out, or_18_out);
  or or_27 (d, or_20_out, or_21_out);
  or or_28 (f, or_22_out, or_23_out);
endmodule

module contador (
  input  e4,
  input  e2,
  input  e3,
  input  rs4,
  input  c4,
  input  e1,
  input  rs3,
  input  c3,
  input  clock,
  input  rs2,
  input  c2,
  input  rs1,
  input  c1,
  output s4,
  output s3,
  output s2,
  output s1,
  output b1,
  output b2,
  output b3,
  output b4
);

  ff_me_psc_t ff_me_psc_t_1 (.PreSet(rs1), .J(e1), .CLOCK(clock), .CLR(c1), .Q(b1), .Q_(s1));
  ff_me_psc_t ff_me_psc_t_2 (.PreSet(rs2), .J(e2), .CLOCK(b1), .CLR(c2), .Q(b2), .Q_(s2));
  ff_me_psc_t ff_me_psc_t_3 (.PreSet(rs3), .J(e3), .CLOCK(b2), .CLR(c3), .Q(b3), .Q_(s3));
  ff_me_psc_t ff_me_psc_t_4 (.PreSet(rs4), .J(e4), .CLOCK(b3), .CLR(c4), .Q(b4), .Q_(s4));
endmodule

module DISPLAY (
  input  e1,
  input  clock,
  input  rs,
  input  clr,
  output s4,
  output s3,
  output s2,
  output s1,
  output b4,
  output b3,
  output b2,
  output b1,
  output a,
  output b,
  output c,
  output d,
  output e,
  output f,
  output g
);

  contador contador_1 (
    .e4(e1), .e2(e1), .e3(e1), .e1(e1), .clock(clock), .s4(s4), .s3(s3), .s2(s2), .s1(s1), .b1(b1), .b2(b2),
    .b3(b3), .b4(b4), .rs1(rs), .c1(clr), .rs2(rs), .c2(clr), .rs3(rs), .c3(clr), .rs4(rs), .c4(clr));
  cont_7_seg cont_7_seg_1 (.d4(b4), .d3(b3), .d2(b2), .d1(b1), .a(a), .b(b), .c(c), .d(d), .e(e), .f(f), .g(g));
endmodule

module Questao1_A (
  input  e1,
  input  clock,
  input  preset,
  input  clear,
  output a,
  output b,
  output c,
  output d,
  output e,
  output f,
  output g,
  output b4,
  output b3,
  output b2,
  output b1
);

  wire display_1_s4;

  DISPLAY display_1 (
    .e1(e1), .clock(clock), .s4(display_1_s4), .s3(display_1_s4), .a(a), .b(b), .c(c), .d(d), .e(e), .f(f),
    .g(g), .rs(preset), .clr(clear), .b4(b4), .b3(b3), .b2(b2), .b1(b1));  // open: s2, s1
  _7_Segment_Display u_7_segment_display_1 (.g(g), .f(f), .a(a), .b(b), .e(e), .d(d), .c(c));  // open: dp
endmodule

module Questao1_B (
  input  preset,
  input  clear,
  output b1,
  output b2,
  output b3,
  output b4
);

  wire and_1_out, clock_out, cont_7_seg_1_a, cont_7_seg_1_b, cont_7_seg_1_c, cont_7_seg_1_d, cont_7_seg_1_e,
       cont_7_seg_1_f, cont_7_seg_1_g, not_1_out, not_2_out;

  Clock clock (.out(clock_out));
  T_Flip_Flop #(.trigger("falling")) t_ff_1 (
    .clk(clock_out), .T(1'b1), .Q(b1), .preset(preset), .reset(and_1_out));  // open: Qn, en
  and and_1 (and_1_out, b1, not_1_out, not_2_out, b4);
  not not_1 (not_1_out, b2);
  T_Flip_Flop #(.trigger("falling")) t_ff_2 (
    .clk(b1), .T(1'b1), .Q(b2), .preset(preset), .reset(and_1_out));  // open: Qn, en
  not not_2 (not_2_out, b3);
  T_Flip_Flop #(.trigger("falling")) t_ff_3 (
    .clk(b2), .T(1'b1), .Q(b3), .preset(preset), .reset(and_1_out));  // open: Qn, en
  T_Flip_Flop #(.trigger("falling")) t_ff_4 (
    .clk(b3), .T(1'b1), .Q(b4), .preset(preset), .reset(and_1_out));  // open: Qn, en
  cont_7_seg cont_7_seg_1 (
    .d4(b4), .d3(b3), .d2(b2), .d1(b1), .a(cont_7_seg_1_a), .b(cont_7_seg_1_b), .c(cont_7_seg_1_c),
    .d(cont_7_seg_1_d), .e(cont_7_seg_1_e), .f(cont_7_seg_1_f), .g(cont_7_seg_1_g));
  _7_Segment_Display u_7_segment_display_1 (
    .g(cont_7_seg_1_g), .f(cont_7_seg_1_f), .a(cont_7_seg_1_a), .b(cont_7_seg_1_b), .e(cont_7_seg_1_e),
    .d(cont_7_seg_1_d), .c(cont_7_seg_1_c));  // open: dp
endmodule

module Questao1_C (
  input  preset,
  input  in_2,
  input  in_3,
  input  in_4,
  input  in_5,
  input  clear,
  output b1,
  output b2,
  output b3,
  output b4
);

  wire and_1_out, and_2_out, and_3_out, and_4_out, and_5_out, clock_out, cont_7_seg_1_a, cont_7_seg_1_b,
       cont_7_seg_1_c, cont_7_seg_1_d, cont_7_seg_1_e, cont_7_seg_1_f, cont_7_seg_1_g, cont_7_seg_2_a,
       cont_7_seg_2_b, cont_7_seg_2_c, cont_7_seg_2_d, cont_7_seg_2_e, cont_7_seg_2_f, cont_7_seg_2_g,
       not_1_out, not_2_out, or_1_out;

  Clock clock (.out(clock_out));
  T_Flip_Flop #(.trigger("falling")) t_ff_1 (
    .clk(clock_out), .T(1'b1), .Q(b1), .preset(and_1_out), .reset(or_1_out));  // open: Qn, en
  and and_1 (and_1_out, preset, in_2);
  or or_1 (or_1_out, clear, and_2_out);
  and and_2 (and_2_out, b1, not_1_out, not_2_out, b4);
  and and_3 (and_3_out, preset, in_3);
  not not_1 (not_1_out, b2);
  T_Flip_Flop #(.trigger("falling")) t_ff_2 (
    .clk(b1), .T(1'b1), .Q(b2), .preset(and_3_out), .reset(or_1_out));  // open: Qn, en
  not not_2 (not_2_out, b3);
  and and_4 (and_4_out, preset, in_4);
  T_Flip_Flop #(.trigger("falling")) t_ff_3 (
    .clk(b2), .T(1'b1), .Q(b3), .preset(and_4_out), .reset(or_1_out));  // open: Qn, en
  and and_5 (and_5_out, preset, in_5);
  cont_7_seg cont_7_seg_1 (
    .d4(in_5), .d3(in_4), .d2(in_3), .d1(in_2), .a(cont_7_seg_1_a), .b(cont_7_seg_1_b), .c(cont_7_seg_1_c),
    .d(cont_7_seg_1_d), .e(cont_7_seg_1_e), .f(cont_7_seg_1_f), .g(cont_7_seg_1_g));
  T_Flip_Flop #(.trigger("falling")) t_ff_4 (
    .clk(b3), .T(1'b1), .Q(b4), .preset(and_5_out), .reset(or_1_out));  // open: Qn, en
  _7_Segment_Display u_7_segment_display_1 (
    .g(cont_7_seg_1_g), .f(cont_7_seg_1_f), .a(cont_7_seg_1_a), .b(cont_7_seg_1_b), .e(cont_7_seg_1_e),
    .d(cont_7_seg_1_d), .c(cont_7_seg_1_c));  // open: dp
  cont_7_seg cont_7_seg_2 (
    .d4(b4), .d3(b3), .d2(b2), .d1(b1), .a(cont_7_seg_2_a), .b(cont_7_seg_2_b), .c(cont_7_seg_2_c),
    .d(cont_7_seg_2_d), .e(cont_7_seg_2_e), .f(cont_7_seg_2_f), .g(cont_7_seg_2_g));
  _7_Segment_Display u_7_segment_display_2 (
    .g(cont_7_seg_2_g), .f(cont_7_seg_2_f), .a(cont_7_seg_2_a), .b(cont_7_seg_2_b), .e(cont_7_seg_2_e),
    .d(cont_7_seg_2_d), .c(cont_7_seg_2_c));  // open: dp
endmodule

module Questao1_D (
  input  preset,
  input  in_2,
  input  in_3,
  input  in_4,
  input  in_5,
  input  clear,
  output b1,
  output b2,
  output b3,
  output b4
);

  wire and_1_out, and_2_out, and_3_out, and_4_out, and_5_out, clock_out, cont_7_seg_1_a, cont_7_seg_1_b,
       cont_7_seg_1_c, cont_7_seg_1_d, cont_7_seg_1_e, cont_7_seg_1_f, cont_7_seg_1_g, cont_7_seg_2_a,
       cont_7_seg_2_b, cont_7_seg_2_c, cont_7_seg_2_d, cont_7_seg_2_e, cont_7_seg_2_f, cont_7_seg_2_g,
       not_1_out, not_2_out, or_1_out, or_2_out;

  Clock clock (.out(clock_out));
  or or_1 (or_1_out, preset, and_2_out);
  T_Flip_Flop #(.trigger("falling")) t_ff_1 (
    .clk(clock_out), .T(1'b1), .Q(b1), .preset(and_1_out), .reset(or_2_out));  // open: Qn, en
  or or_2 (or_2_out, clear, and_2_out);
  and and_1 (and_1_out, or_1_out, in_2);
  and and_2 (and_2_out, b1, not_1_out, not_2_out, b4);
  and and_3 (and_3_out, or_1_out, in_3);
  not not_1 (not_1_out, b2);
  T_Flip_Flop #(.trigger("falling")) t_ff_2 (
    .clk(b1), .T(1'b1), .Q(b2), .preset(and_3_out), .reset(or_2_out));  // open: Qn, en
  not not_2 (not_2_out, b3);
  and and_4 (and_4_out, or_1_out, in_4);
  T_Flip_Flop #(.trigger("falling")) t_ff_3 (
    .clk(b2), .T(1'b1), .Q(b3), .preset(and_4_out), .reset(or_2_out));  // open: Qn, en
  and and_5 (and_5_out, or_1_out, in_5);
  cont_7_seg cont_7_seg_1 (
    .d4(in_5), .d3(in_4), .d2(in_3), .d1(in_2), .a(cont_7_seg_1_a), .b(cont_7_seg_1_b), .c(cont_7_seg_1_c),
    .d(cont_7_seg_1_d), .e(cont_7_seg_1_e), .f(cont_7_seg_1_f), .g(cont_7_seg_1_g));
  T_Flip_Flop #(.trigger("falling")) t_ff_4 (
    .clk(b3), .T(1'b1), .Q(b4), .preset(and_5_out), .reset(or_2_out));  // open: Qn, en
  _7_Segment_Display u_7_segment_display_1 (
    .g(cont_7_seg_1_g), .f(cont_7_seg_1_f), .a(cont_7_seg_1_a), .b(cont_7_seg_1_b), .e(cont_7_seg_1_e),
    .d(cont_7_seg_1_d), .c(cont_7_seg_1_c));  // open: dp
  cont_7_seg cont_7_seg_2 (
    .d4(b4), .d3(b3), .d2(b2), .d1(b1), .a(cont_7_seg_2_a), .b(cont_7_seg_2_b), .c(cont_7_seg_2_c),
    .d(cont_7_seg_2_d), .e(cont_7_seg_2_e), .f(cont_7_seg_2_f), .g(cont_7_seg_2_g));
  _7_Segment_Display u_7_segment_display_2 (
    .g(cont_7_seg_2_g), .f(cont_7_seg_2_f), .a(cont_7_seg_2_a), .b(cont_7_seg_2_b), .e(cont_7_seg_2_e),
    .d(cont_7_seg_2_d), .c(cont_7_seg_2_c));  // open: dp
endmodule

module Questao1_E (
  input  preset,
  input  clear,
  input  in_3,
  input  in_4,
  input  in_5,
  input  in_6,
  input  in_7,
  input  in_8,
  input  in_9,
  input  in_10,
  output b1,
  output b2,
  output b3,
  output b4
);

  wire and_1_out, and_2_out, and_3_out, and_4_out, and_5_out, clock_out, cont_7_seg_1_a, cont_7_seg_1_b,
       cont_7_seg_1_c, cont_7_seg_1_d, cont_7_seg_1_e, cont_7_seg_1_f, cont_7_seg_1_g, cont_7_seg_2_a,
       cont_7_seg_2_b, cont_7_seg_2_c, cont_7_seg_2_d, cont_7_seg_2_e, cont_7_seg_2_f, cont_7_seg_2_g,
       cont_7_seg_3_a, cont_7_seg_3_b, cont_7_seg_3_c, cont_7_seg_3_d, cont_7_seg_3_e, cont_7_seg_3_f,
       cont_7_seg_3_g, or_1_out, or_2_out, xnor_1_out, xnor_2_out, xnor_3_out, xnor_4_out;

  Clock clock (.out(clock_out));
  or or_1 (or_1_out, preset, and_4_out);
  T_Flip_Flop #(.trigger("falling")) t_ff_1 (
    .clk(clock_out), .T(1'b1), .Q(b1), .preset(and_1_out), .reset(or_2_out));  // open: Qn, en
  or or_2 (or_2_out, clear, and_4_out);
  and and_1 (and_1_out, or_1_out, in_7);
  T_Flip_Flop #(.trigger("falling")) t_ff_2 (
    .clk(b1), .T(1'b1), .Q(b2), .preset(and_2_out), .reset(or_2_out));  // open: Qn, en
  and and_2 (and_2_out, or_1_out, in_8);
  and and_3 (and_3_out, or_1_out, in_9);
  T_Flip_Flop #(.trigger("falling")) t_ff_3 (
    .clk(b2), .T(1'b1), .Q(b3), .preset(and_3_out), .reset(or_2_out));  // open: Qn, en
  and and_4 (and_4_out, xnor_1_out, xnor_2_out, xnor_3_out, xnor_4_out);
  and and_5 (and_5_out, or_1_out, in_10);
  T_Flip_Flop #(.trigger("falling")) t_ff_4 (
    .clk(b3), .T(1'b1), .Q(b4), .preset(and_5_out), .reset(or_2_out));  // open: Qn, en
  xnor xnor_1 (xnor_1_out, b1, in_3);
  xnor xnor_2 (xnor_2_out, b3, in_4);
  xnor xnor_3 (xnor_3_out, b2, in_5);
  xnor xnor_4 (xnor_4_out, b4, in_6);
  cont_7_seg cont_7_seg_1 (
    .d4(in_10), .d3(in_9), .d2(in_8), .d1(in_7), .a(cont_7_seg_1_a), .b(cont_7_seg_1_b), .c(cont_7_seg_1_c),
    .d(cont_7_seg_1_d), .e(cont_7_seg_1_e), .f(cont_7_seg_1_f), .g(cont_7_seg_1_g));
  cont_7_seg cont_7_seg_2 (
    .d4(b4), .d3(b3), .d2(b2), .d1(b1), .a(cont_7_seg_2_a), .b(cont_7_seg_2_b), .c(cont_7_seg_2_c),
    .d(cont_7_seg_2_d), .e(cont_7_seg_2_e), .f(cont_7_seg_2_f), .g(cont_7_seg_2_g));
  _7_Segment_Display u_7_segment_display_1 (
    .g(cont_7_seg_1_g), .f(cont_7_seg_1_f), .a(cont_7_seg_1_a), .b(cont_7_seg_1_b), .e(cont_7_seg_1_e),
    .d(cont_7_seg_1_d), .c(cont_7_seg_1_c));  // open: dp
  _7_Segment_Display u_7_segment_display_2 (
    .g(cont_7_seg_2_g), .f(cont_7_seg_2_f), .a(cont_7_seg_2_a), .b(cont_7_seg_2_b), .e(cont_7_seg_2_e),
    .d(cont_7_seg_2_d), .c(cont_7_seg_2_c));  // open: dp
  cont_7_seg cont_7_seg_3 (
    .d4(in_6), .d3(in_5), .d2(in_4), .d1(in_3), .a(cont_7_seg_3_a), .b(cont_7_seg_3_b), .c(cont_7_seg_3_c),
    .d(cont_7_seg_3_d), .e(cont_7_seg_3_e), .f(cont_7_seg_3_f), .g(cont_7_seg_3_g));
  _7_Segment_Display u_7_segment_display_3 (
    .g(cont_7_seg_3_g), .f(cont_7_seg_3_f), .a(cont_7_seg_3_a), .b(cont_7_seg_3_b), .e(cont_7_seg_3_e),
    .d(cont_7_seg_3_d), .c(cont_7_seg_3_c));  // open: dp
endmodule

module Questao1_F (
  input  in_1,
  input  preset,
  input  clear,
  input  in_4,
  input  in_5,
  input  in_6,
  input  in_7,
  input  in_8,
  input  in_9,
  input  in_10,
  input  in_11,
  output b1,
  output b2,
  output b3,
  output b4
);

  wire and_1_out, and_2_out, and_3_out, and_4_out, and_5_out, clock_para_crescer_out, cont_7_seg_1_a,
       cont_7_seg_1_b, cont_7_seg_1_c, cont_7_seg_1_d, cont_7_seg_1_e, cont_7_seg_1_f, cont_7_seg_1_g,
       cont_7_seg_2_a, cont_7_seg_2_b, cont_7_seg_2_c, cont_7_seg_2_d, cont_7_seg_2_e, cont_7_seg_2_f,
       cont_7_seg_2_g, cont_7_seg_3_a, cont_7_seg_3_b, cont_7_seg_3_c, cont_7_seg_3_d, cont_7_seg_3_e,
       cont_7_seg_3_f, cont_7_seg_3_g, not_1_out, or_1_out, or_2_out, t_ff_1_q, t_ff_1_qn, t_ff_2_q,
       t_ff_2_qn, t_ff_3_q, t_ff_3_qn, t_ff_4_q, t_ff_4_qn, xnor_1_out, xnor_2_out, xnor_3_out, xnor_4_out;

  Clock clock_para_crescer (.out(clock_para_crescer_out));
  not not_1 (not_1_out, clock_para_crescer_out);
  or or_1 (or_1_out, preset, and_4_out);
  T_Flip_Flop #(.trigger("falling")) t_ff_1 (
    .clk(not_1_out), .T(1'b1), .Q(t_ff_1_q), .Qn(t_ff_1_qn), .preset(and_1_out), .reset(or_2_out));  // open: en
  or or_2 (or_2_out, clear, and_4_out);
  and and_1 (and_1_out, or_1_out, in_8);
  muxd2 muxd2_1 (._00(t_ff_1_q), ._01(t_ff_1_qn), .saida(b1), .e1(in_1));
  T_Flip_Flop #(.trigger("falling")) t_ff_2 (
    .clk(b1), .T(1'b1), .Q(t_ff_2_q), .Qn(t_ff_2_qn), .preset(and_2_out), .reset(or_2_out));  // open: en
  and and_2 (and_2_out, or_1_out, in_9);
  muxd2 muxd2_2 (._00(t_ff_2_q), ._01(t_ff_2_qn), .saida(b2), .e1(in_1));
  and and_3 (and_3_out, or_1_out, in_10);
  T_Flip_Flop #(.trigger("falling")) t_ff_3 (
    .clk(b2), .T(1'b1), .Q(t_ff_3_q), .Qn(t_ff_3_qn), .preset(and_3_out), .reset(or_2_out));  // open: en
  muxd2 muxd2_3 (._00(t_ff_3_q), ._01(t_ff_3_qn), .saida(b3), .e1(in_1));
  and and_4 (and_4_out, xnor_1_out, xnor_2_out, xnor_3_out, xnor_4_out);
  xnor xnor_1 (xnor_1_out, b1, in_4);
  and and_5 (and_5_out, or_1_out, in_11);
  T_Flip_Flop #(.trigger("falling")) t_ff_4 (
    .clk(b3), .T(1'b1), .Q(t_ff_4_q), .Qn(t_ff_4_qn), .preset(and_5_out), .reset(or_2_out));  // open: en
  xnor xnor_2 (xnor_2_out, b2, in_5);
  xnor xnor_3 (xnor_3_out, b3, in_6);
  xnor xnor_4 (xnor_4_out, b4, in_7);
  cont_7_seg cont_7_seg_1 (
    .d4(in_11), .d3(in_10), .d2(in_9), .d1(in_8), .a(cont_7_seg_1_a), .b(cont_7_seg_1_b), .c(cont_7_seg_1_c),
    .d(cont_7_seg_1_d), .e(cont_7_seg_1_e), .f(cont_7_seg_1_f), .g(cont_7_seg_1_g));
  muxd2 muxd2_4 (._00(t_ff_4_q), ._01(t_ff_4_qn), .saida(b4), .e1(in_1));
  _7_Segment_Display u_7_segment_display_1 (
    .g(cont_7_seg_1_g), .f(cont_7_seg_1_f), .a(cont_7_seg_1_a), .b(cont_7_seg_1_b), .e(cont_7_seg_1_e),
    .d(cont_7_seg_1_d), .c(cont_7_seg_1_c));  // open: dp
  cont_7_seg cont_7_seg_2 (
    .d4(b4), .d3(b3), .d2(b2), .d1(b1), .a(cont_7_seg_2_a), .b(cont_7_seg_2_b), .c(cont_7_seg_2_c),
    .d(cont_7_seg_2_d), .e(cont_7_seg_2_e), .f(cont_7_seg_2_f), .g(cont_7_seg_2_g));
  cont_7_seg cont_7_seg_3 (
    .d4(in_7), .d3(in_6), .d2(in_5), .d1(in_4), .a(cont_7_seg_3_a), .b(cont_7_seg_3_b), .c(cont_7_seg_3_c),
    .d(cont_7_seg_3_d), .e(cont_7_seg_3_e), .f(cont_7_seg_3_f), .g(cont_7_seg_3_g));
  _7_Segment_Display u_7_segment_display_2 (
    .g(cont_7_seg_2_g), .f(cont_7_seg_2_f), .a(cont_7_seg_2_a), .b(cont_7_seg_2_b), .e(cont_7_seg_2_e),
    .d(cont_7_seg_2_d), .c(cont_7_seg_2_c));  // open: dp
  _7_Segment_Display u_7_segment_display_3 (
    .g(cont_7_seg_3_g), .f(cont_7_seg_3_f), .a(cont_7_seg_3_a), .b(cont_7_seg_3_b), .e(cont_7_seg_3_e),
    .d(cont_7_seg_3_d), .c(cont_7_seg_3_c));  // open: dp
endmodule

module decrescente (
  input  a0,
  input  a1,
  input  a2,
  input  a3,
  output a,
  output b,
  output c,
  output d,
  output e,
  output f,
  output g
);

  wire and_1_out, and_2_out, and_3_out, and_4_out, and_5_out, and_6_out, and_7_out, and_8_out, and_9_out,
       and_10_out, and_11_out, and_12_out, and_13_out, and_14_out, and_15_out, and_16_out, and_17_out,
       and_18_out, and_19_out, and_20_out, and_21_out, and_22_out, and_23_out, and_24_out, and_25_out,
       and_26_out, and_27_out, and_28_out, and_29_out, and_30_out, and_31_out, and_32_out, and_33_out,
       and_34_out, and_35_out, and_36_out, and_37_out, and_38_out, and_39_out, and_40_out, and_41_out,
       and_42_out, and_43_out, and_44_out, and_45_out, and_46_out, and_47_out, not_1_out, not_2_out,
       not_3_out, not_4_out, not_5_out, not_6_out, not_7_out, not_8_out, not_9_out, not_10_out, not_11_out,
       not_12_out, not_13_out, not_14_out, not_15_out, not_16_out, not_17_out, not_18_out, not_19_out,
       not_20_out, not_21_out, not_22_out, not_23_out, not_24_out, not_25_out, not_26_out, not_27_out,
       not_28_out, not_29_out, not_30_out, not_31_out, not_32_out, not_33_out, not_34_out, not_35_out,
       not_36_out, not_37_out, not_38_out, not_39_out, or_1_out, or_2_out, or_3_out, or_4_out, or_5_out,
       or_6_out, or_7_out, or_8_out, or_9_out, or_10_out, or_12_out, or_13_out, or_14_out, or_15_out,
       or_16_out, or_17_out, or_18_out, or_20_out, or_21_out, or_23_out, or_24_out;

  not not_1 (not_1_out, a1);
  not not_2 (not_2_out, a2);
  not not_3 (not_3_out, a0);
  not not_4 (not_4_out, a0);
  and and_1 (and_1_out, not_4_out, a1);
  and and_2 (and_2_out, a0, not_5_out);
  not not_5 (not_5_out, a1);
  not not_6 (not_6_out, a3);
  not not_7 (not_7_out, a0);
  and and_3 (and_3_out, not_7_out, a2);
  not not_8 (not_8_out, a3);
  not not_9 (not_9_out, a2);
  and and_4 (and_4_out, a2, not_10_out);
  not not_10 (not_10_out, a3);
  not not_11 (not_11_out, a0);
  and and_5 (and_5_out, not_11_out, a1);
  not not_12 (not_12_out, a1);
  not not_13 (not_13_out, a3);
  not not_14 (not_14_out, a1);
  and and_6 (and_6_out, not_14_out, not_15_out);
  not not_15 (not_15_out, a2);
  not not_16 (not_16_out, a0);
  not not_17 (not_17_out, a1);
  not not_18 (not_18_out, a2);
  not not_19 (not_19_out, a0);
  and and_7 (and_7_out, not_19_out, not_20_out);
  not not_20 (not_20_out, a1);
  not not_21 (not_21_out, a0);
  and and_8 (and_8_out, not_21_out, not_22_out);
  not not_22 (not_22_out, a2);
  not not_23 (not_23_out, a2);
  and and_9 (and_9_out, not_23_out, a3);
  and and_10 (and_10_out, a1, a3);
  not not_24 (not_24_out, a0);
  and and_11 (and_11_out, not_24_out, not_25_out);
  not not_25 (not_25_out, a2);
  not not_26 (not_26_out, a1);
  and and_12 (and_12_out, not_26_out, a3);
  not not_27 (not_27_out, a0);
  and and_13 (and_13_out, a0, not_28_out);
  not not_28 (not_28_out, a1);
  not not_29 (not_29_out, a0);
  not not_30 (not_30_out, a2);
  not not_31 (not_31_out, a1);
  and and_14 (and_14_out, not_31_out, a2);
  not not_32 (not_32_out, a3);
  not not_33 (not_33_out, a1);
  and and_15 (and_15_out, not_1_out, not_2_out);
  and and_16 (and_16_out, not_3_out, a3);
  and and_17 (and_17_out, and_1_out, a2);
  and and_18 (and_18_out, and_2_out, not_6_out);
  not not_34 (not_34_out, a2);
  and and_19 (and_19_out, and_3_out, not_8_out);
  and and_20 (and_20_out, a1, a3);
  and and_21 (and_21_out, a0, not_9_out);
  not not_35 (not_35_out, a3);
  and and_22 (and_22_out, a0, a2);
  or or_1 (or_1_out, and_4_out, and_5_out);
  and and_23 (and_23_out, a0, not_12_out);
  and and_24 (and_24_out, a0, not_13_out);
  and and_25 (and_25_out, a0, a2);
  and and_26 (and_26_out, and_6_out, a3);
  and and_27 (and_27_out, not_16_out, a2);
  and and_28 (and_28_out, not_17_out, a2);
  not not_36 (not_36_out, a3);
  and and_29 (and_29_out, a1, not_18_out);
  not not_37 (not_37_out, a3);
  and and_30 (and_30_out, a0, a1);
  or or_2 (or_2_out, and_7_out, and_8_out);
  or or_3 (or_3_out, and_9_out, and_10_out);
  or or_4 (or_4_out, and_11_out, and_12_out);
  and and_31 (and_31_out, a2, a3);
  and and_32 (and_32_out, not_27_out, a1);
  and and_33 (and_33_out, and_13_out, a2);
  and and_34 (and_34_out, not_29_out, not_30_out);
  and and_35 (and_35_out, and_14_out, not_32_out);
  not not_38 (not_38_out, a0);
  not not_39 (not_39_out, a2);
  and and_36 (and_36_out, a0, not_33_out);
  or or_5 (or_5_out, and_15_out, and_16_out);
  and and_37 (and_37_out, a1, a3);
  or or_6 (or_6_out, and_17_out, and_18_out);
  and and_38 (and_38_out, a0, not_34_out);
  or or_7 (or_7_out, and_19_out, and_20_out);
  and and_39 (and_39_out, and_21_out, not_35_out);
  and and_40 (and_40_out, and_22_out, a3);
  and and_41 (and_41_out, a0, a1);
  or or_8 (or_8_out, or_1_out, and_23_out);
  or or_9 (or_9_out, and_24_out, and_25_out);
  or or_10 (or_10_out, and_26_out, and_27_out);
  and and_42 (and_42_out, and_28_out, not_36_out);
  and and_43 (and_43_out, and_29_out, not_37_out);
  and and_44 (and_44_out, and_30_out, a3);
  or or_11 (e, or_2_out, or_3_out);
  or or_12 (or_12_out, or_4_out, and_31_out);
  or or_13 (or_13_out, and_32_out, and_33_out);
  or or_14 (or_14_out, and_34_out, and_35_out);
  and and_45 (and_45_out, not_38_out, a1);
  and and_46 (and_46_out, a1, not_39_out);
  and and_47 (and_47_out, and_36_out, a3);
  or or_15 (or_15_out, or_5_out, and_37_out);
  or or_16 (or_16_out, or_6_out, and_38_out);
  or or_17 (or_17_out, or_7_out, and_39_out);
  or or_18 (or_18_out, and_40_out, and_41_out);
  or or_19 (c, or_8_out, or_9_out);
  or or_20 (or_20_out, or_10_out, and_42_out);
  or or_21 (or_21_out, and_43_out, and_44_out);
  or or_22 (f, or_12_out, or_13_out);
  or or_23 (or_23_out, or_14_out, and_45_out);
  or or_24 (or_24_out, and_46_out, and_47_out);
  or or_25 (a, or_15_out, or_16_out);
  or or_26 (b, or_17_out, or_18_out);
  or or_27 (d, or_20_out, or_21_out);
  or or_28 (g, or_23_out, or_24_out);
endmodule

module Questao1_F2 (
  input  in_1,
  input  preset,
  input  clear,
  input  in_4,
  input  in_5,
  input  in_6,
  input  in_7,
  input  in_8,
  input  in_9,
  input  in_10,
  input  in_11,
  output b1,
  output b2,
  output b3,
  output b4
);

  wire and_1_out, and_2_out, and_3_out, and_4_out, and_5_out, clock_para_crescer_out, cont_7_seg_1_a,
       cont_7_seg_1_b, cont_7_seg_1_c, cont_7_seg_1_d, cont_7_seg_1_e, cont_7_seg_1_f, cont_7_seg_1_g,
       cont_7_seg_2_a, cont_7_seg_2_b, cont_7_seg_2_c, cont_7_seg_2_d, cont_7_seg_2_e, cont_7_seg_2_f,
       cont_7_seg_2_g, cont_7_seg_3_a, cont_7_seg_3_b, cont_7_seg_3_c, cont_7_seg_3_d, cont_7_seg_3_e,
       cont_7_seg_3_f, cont_7_seg_3_g, muxd2_1_saida, muxd2_2_saida, muxd2_3_saida, muxd2_4_saida, not_1_out,
       or_1_out, or_2_out, t_ff_1_qn, t_ff_2_qn, t_ff_3_qn, t_ff_4_qn, xnor_1_out, xnor_2_out, xnor_3_out,
       xnor_4_out;

  Clock clock_para_crescer (.out(clock_para_crescer_out));
  not not_1 (not_1_out, clock_para_crescer_out);
  or or_1 (or_1_out, preset, and_4_out);
  T_Flip_Flop #(.trigger("falling")) t_ff_1 (
    .clk(not_1_out), .T(1'b1), .Q(b1), .Qn(t_ff_1_qn), .preset(and_1_out), .reset(or_2_out));  // open: en
  or or_2 (or_2_out, clear, and_4_out);
  and and_1 (and_1_out, or_1_out, in_8);
  muxd2 muxd2_1 (._00(b1), ._01(t_ff_1_qn), .saida(muxd2_1_saida), .e1(in_1));
  T_Flip_Flop #(.trigger("falling")) t_ff_2 (
    .clk(muxd2_1_saida), .T(1'b1), .Q(b2), .Qn(t_ff_2_qn), .preset(and_2_out), .reset(or_2_out));  // open: en
  and and_2 (and_2_out, or_1_out, in_9);
  muxd2 muxd2_2 (._00(b2), ._01(t_ff_2_qn), .saida(muxd2_2_saida), .e1(in_1));
  and and_3 (and_3_out, or_1_out, in_10);
  T_Flip_Flop #(.trigger("falling")) t_ff_3 (
    .clk(muxd2_2_saida), .T(1'b1), .Q(b3), .Qn(t_ff_3_qn), .preset(and_3_out), .reset(or_2_out));  // open: en
  muxd2 muxd2_3 (._00(b3), ._01(t_ff_3_qn), .saida(muxd2_3_saida), .e1(in_1));
  and and_4 (and_4_out, xnor_1_out, xnor_2_out, xnor_3_out, xnor_4_out);
  xnor xnor_1 (xnor_1_out, b1, in_4);
  and and_5 (and_5_out, or_1_out, in_11);
  T_Flip_Flop #(.trigger("falling")) t_ff_4 (
    .clk(muxd2_3_saida), .T(1'b1), .Q(b4), .Qn(t_ff_4_qn), .preset(and_5_out), .reset(or_2_out));  // open: en
  xnor xnor_2 (xnor_2_out, b2, in_5);
  xnor xnor_3 (xnor_3_out, b3, in_6);
  xnor xnor_4 (xnor_4_out, muxd2_4_saida, in_7);
  cont_7_seg cont_7_seg_1 (
    .d4(in_11), .d3(in_10), .d2(in_9), .d1(in_8), .a(cont_7_seg_1_a), .b(cont_7_seg_1_b), .c(cont_7_seg_1_c),
    .d(cont_7_seg_1_d), .e(cont_7_seg_1_e), .f(cont_7_seg_1_f), .g(cont_7_seg_1_g));
  muxd2 muxd2_4 (._00(b4), ._01(t_ff_4_qn), .saida(muxd2_4_saida), .e1(in_1));
  _7_Segment_Display u_7_segment_display_1 (
    .g(cont_7_seg_1_g), .f(cont_7_seg_1_f), .a(cont_7_seg_1_a), .b(cont_7_seg_1_b), .e(cont_7_seg_1_e),
    .d(cont_7_seg_1_d), .c(cont_7_seg_1_c));  // open: dp
  cont_7_seg cont_7_seg_2 (
    .d4(b4), .d3(b3), .d2(b2), .d1(b1), .a(cont_7_seg_2_a), .b(cont_7_seg_2_b), .c(cont_7_seg_2_c),
    .d(cont_7_seg_2_d), .e(cont_7_seg_2_e), .f(cont_7_seg_2_f), .g(cont_7_seg_2_g));
  cont_7_seg cont_7_seg_3 (
    .d4(in_7), .d3(in_6), .d2(in_5), .d1(in_4), .a(cont_7_seg_3_a), .b(cont_7_seg_3_b), .c(cont_7_seg_3_c),
    .d(cont_7_seg_3_d), .e(cont_7_seg_3_e), .f(cont_7_seg_3_f), .g(cont_7_seg_3_g));
  _7_Segment_Display u_7_segment_display_2 (
    .g(cont_7_seg_2_g), .f(cont_7_seg_2_f), .a(cont_7_seg_2_a), .b(cont_7_seg_2_b), .e(cont_7_seg_2_e),
    .d(cont_7_seg_2_d), .c(cont_7_seg_2_c));  // open: dp
  _7_Segment_Display u_7_segment_display_3 (
    .g(cont_7_seg_3_g), .f(cont_7_seg_3_f), .a(cont_7_seg_3_a), .b(cont_7_seg_3_b), .e(cont_7_seg_3_e),
    .d(cont_7_seg_3_d), .c(cont_7_seg_3_c));  // open: dp
endmodule

module questaoF (
  input  in_1,
  input  in_2,
  input  in_3,
  input  in_4,
  input  Cresc_Decresc,
  input  clear,
  input  in_7,
  input  in_8,
  input  in_9,
  input  in_10,
  input  in_11,
  output b1,
  output b2,
  output b3,
  output b4
);

  wire and_1_out, and_2_out, and_3_out, and_4_out, and_5_out, and_6_out, and_7_out, and_8_out, and_9_out,
       and_10_out, clock_out, cont_7_seg_1_a, cont_7_seg_1_b, cont_7_seg_1_c, cont_7_seg_1_d, cont_7_seg_1_e,
       cont_7_seg_1_f, cont_7_seg_1_g, cont_7_seg_2_a, cont_7_seg_2_b, cont_7_seg_2_c, cont_7_seg_2_d,
       cont_7_seg_2_e, cont_7_seg_2_f, cont_7_seg_2_g, cont_7_seg_3_a, cont_7_seg_3_b, cont_7_seg_3_c,
       cont_7_seg_3_d, cont_7_seg_3_e, cont_7_seg_3_f, cont_7_seg_3_g, multiplexer_1_out, multiplexer_2_out,
       multiplexer_3_out, multiplexer_4_out, muxd2_1_saida, muxd2_2_saida, muxd2_3_saida, not_1_out,
       not_2_out, not_3_out, not_4_out, not_5_out, or_1_out, or_2_out, or_3_out, or_4_out, t_ff_1_qn,
       t_ff_2_qn, t_ff_3_qn, t_ff_4_qn;

  Clock clock (.out(clock_out));
  cont_7_seg cont_7_seg_1 (
    .d4(in_1), .d3(in_2), .d2(in_3), .d1(in_4), .a(cont_7_seg_1_a), .b(cont_7_seg_1_b), .c(cont_7_seg_1_c),
    .d(cont_7_seg_1_d), .e(cont_7_seg_1_e), .f(cont_7_seg_1_f), .g(cont_7_seg_1_g));
  not not_1 (not_1_out, clock_out);
  _7_Segment_Display u_7_segment_display_1 (
    .g(cont_7_seg_1_g), .f(cont_7_seg_1_f), .a(cont_7_seg_1_a), .b(cont_7_seg_1_b), .e(cont_7_seg_1_e),
    .d(cont_7_seg_1_d), .c(cont_7_seg_1_c));  // open: dp
  T_Flip_Flop #(.trigger("falling")) t_ff_1 (
    .clk(not_1_out), .T(1'b1), .Q(b1), .Qn(t_ff_1_qn), .preset(and_1_out), .reset(or_1_out));  // open: en
  or or_1 (or_1_out, clear, and_2_out);
  and and_1 (and_1_out, and_10_out, in_8);
  not not_2 (not_2_out, in_8);
  muxd2 muxd2_1 (._00(b1), ._01(t_ff_1_qn), .saida(muxd2_1_saida), .e1(Cresc_Decresc));
  and and_2 (and_2_out, not_2_out, and_10_out);
  Multiplexer multiplexer_1 (.in0(b1), .in1(t_ff_1_qn), .out(multiplexer_1_out), .sel(in_1));  // open: en
  or or_2 (or_2_out, clear, and_4_out);
  and and_3 (and_3_out, and_10_out, in_9);
  not not_3 (not_3_out, in_9);
  muxd2 muxd2_2 (._00(b2), ._01(t_ff_2_qn), .saida(muxd2_2_saida), .e1(Cresc_Decresc));
  T_Flip_Flop #(.trigger("falling")) t_ff_2 (
    .clk(muxd2_1_saida), .T(1'b1), .Q(b2), .Qn(t_ff_2_qn), .preset(and_3_out), .reset(or_2_out));  // open: en
  and and_4 (and_4_out, not_3_out, and_10_out);
  Multiplexer multiplexer_2 (.in0(b2), .in1(t_ff_2_qn), .out(multiplexer_2_out), .sel(in_2));  // open: en
  and and_5 (and_5_out, and_10_out, in_10);
  T_Flip_Flop #(.trigger("falling")) t_ff_3 (
    .clk(muxd2_2_saida), .T(1'b1), .Q(b3), .Qn(t_ff_3_qn), .preset(and_5_out), .reset(or_3_out));  // open: en
  muxd2 muxd2_3 (._00(b3), ._01(t_ff_3_qn), .saida(muxd2_3_saida), .e1(Cresc_Decresc));
  or or_3 (or_3_out, clear, and_6_out);
  and and_6 (and_6_out, not_4_out, and_10_out);
  not not_4 (not_4_out, in_10);
  Multiplexer multiplexer_3 (.in0(b3), .in1(t_ff_3_qn), .out(multiplexer_3_out), .sel(in_3));  // open: en
  and and_7 (and_7_out, and_10_out, in_11);
  T_Flip_Flop #(.trigger("falling")) t_ff_4 (
    .clk(muxd2_3_saida), .T(1'b1), .Q(b4), .Qn(t_ff_4_qn), .preset(and_7_out), .reset(or_4_out));  // open: en
  or or_4 (or_4_out, clear, and_8_out);
  and and_8 (and_8_out, not_5_out, and_10_out);
  not not_5 (not_5_out, in_11);
  and and_9 (and_9_out, multiplexer_1_out, multiplexer_2_out, multiplexer_3_out, multiplexer_4_out);
  Multiplexer multiplexer_4 (.in0(b4), .in1(t_ff_4_qn), .out(multiplexer_4_out), .sel(in_4));  // open: en
  and and_10 (and_10_out, and_9_out, in_7);
  cont_7_seg cont_7_seg_2 (
    .d4(in_11), .d3(in_10), .d2(in_9), .d1(in_8), .a(cont_7_seg_2_a), .b(cont_7_seg_2_b), .c(cont_7_seg_2_c),
    .d(cont_7_seg_2_d), .e(cont_7_seg_2_e), .f(cont_7_seg_2_f), .g(cont_7_seg_2_g));
  _7_Segment_Display u_7_segment_display_2 (
    .g(cont_7_seg_2_g), .f(cont_7_seg_2_f), .a(cont_7_seg_2_a), .b(cont_7_seg_2_b), .e(cont_7_seg_2_e),
    .d(cont_7_seg_2_d), .c(cont_7_seg_2_c));  // open: dp
  cont_7_seg cont_7_seg_3 (
    .d4(b4), .d3(b3), .d2(b2), .d1(b1), .a(cont_7_seg_3_a), .b(cont_7_seg_3_b), .c(cont_7_seg_3_c),
    .d(cont_7_seg_3_d), .e(cont_7_seg_3_e), .f(cont_7_seg_3_f), .g(cont_7_seg_3_g));
  _7_Segment_Display u_7_segment_display_3 (
    .g(cont_7_seg_3_g), .f(cont_7_seg_3_f), .a(cont_7_seg_3_a), .b(cont_7_seg_3_b), .e(cont_7_seg_3_e),
    .d(cont_7_seg_3_d), .c(cont_7_seg_3_c));  // open: dp
endmodule

module MUX2 (
  input  _00,
  input  _01,
  input  e1,
  output saida
);

  wire and_1_out, and_2_out, not_1_out;

  not not_1 (not_1_out, e1);
  and and_1 (and_1_out, _00, not_1_out);
  and and_2 (and_2_out, _01, e1);
  or or_1 (saida, and_1_out, and_2_out);
endmodule
