// Logisim project trabalho08.circ as structural Verilog
module QuestaoA (
);

  wire clock_1_out, cont_7_seg_1_a, cont_7_seg_1_b, cont_7_seg_1_c, cont_7_seg_1_d, cont_7_seg_1_e,
       cont_7_seg_1_f, cont_7_seg_1_g, contador_1_j0, contador_1_j1, contador_1_j2, contador_1_j3,
       contador_1_k0, contador_1_k1, contador_1_k2, contador_1_k3, j_k_ff_1_q, j_k_ff_2_q, j_k_ff_3_q,
       j_k_ff_4_q;

  Clock clock_1 (.out(clock_1_out));
  J_K_Flip_Flop j_k_ff_1 (
    .J(contador_1_j0), .clk(clock_1_out), .K(contador_1_k0), .Q(j_k_ff_1_q));  // open: Qn, preset, en, reset
  J_K_Flip_Flop j_k_ff_2 (
    .J(contador_1_j1), .clk(clock_1_out), .K(contador_1_k1), .Q(j_k_ff_2_q));  // open: Qn, preset, en, reset
  J_K_Flip_Flop j_k_ff_3 (
    .J(contador_1_j2), .clk(clock_1_out), .K(contador_1_k2), .Q(j_k_ff_3_q));  // open: Qn, preset, en, reset
  J_K_Flip_Flop j_k_ff_4 (
    .J(contador_1_j3), .clk(clock_1_out), .K(contador_1_k3), .Q(j_k_ff_4_q));  // open: Qn, preset, en, reset
  contador contador_1 (
    .q3(j_k_ff_4_q), .q2(j_k_ff_3_q), .q1(j_k_ff_2_q), .q0(j_k_ff_1_q), .j3(contador_1_j3),
    .k3(contador_1_k3), .j2(contador_1_j2), .k2(contador_1_k2), .j1(contador_1_j1), .k1(contador_1_k1),
    .j0(contador_1_j0), .k0(contador_1_k0));
  cont_7_seg cont_7_seg_1 (
    .d4(j_k_ff_4_q), .d3(j_k_ff_3_q), .d2(j_k_ff_2_q), .d1(j_k_ff_1_q), .a(cont_7_seg_1_a),
    .b(cont_7_seg_1_b), .c(cont_7_seg_1_c), .d(cont_7_seg_1_d), .e(cont_7_seg_1_e), .f(cont_7_seg_1_f),
    .g(cont_7_seg_1_g));
  _7_Segment_Display u_7_segment_display_1 (
    .g(cont_7_seg_1_g), .f(cont_7_seg_1_f), .a(cont_7_seg_1_a), .b(cont_7_seg_1_b), .e(cont_7_seg_1_e),
    .d(cont_7_seg_1_d), .c(cont_7_seg_1_c));  // open: dp
endmodule

module contador (
  input  q3,
  input  q2,
  input  q1,
  input  q0,
  output j3,
  output k3,
  output j2,
  output k2,
  output j1,
  output k1,
  output j0,
  output k0
);

  wire and_1_out, and_2_out;

  and and_1 (and_1_out, q2, q1);
  and and_2 (and_2_out, q2, q1);
  and and_3 (j2, q1, q0);
  and and_4 (k2, q1, q0);
  and and_5 (j3, and_1_out, q0);
  and and_6 (k3, and_2_out, q0);

  assign j0 = 1'b1;
  assign j1 = q0;
  assign k0 = 1'b1;
  assign k1 = q0;
endmodule

module QuestaoB (
);

  wire clock_1_out, cont_7_seg_1_a, cont_7_seg_1_b, cont_7_seg_1_c, cont_7_seg_1_d, cont_7_seg_1_e,
       cont_7_seg_1_f, cont_7_seg_1_g, contador_dec_1_j0, contador_dec_1_j1, contador_dec_1_j2,
       contador_dec_1_j3, contador_dec_1_k0, contador_dec_1_k1, contador_dec_1_k2, contador_dec_1_k3,
       j_k_ff_1_q, j_k_ff_2_q, j_k_ff_3_q, j_k_ff_4_q;

  Clock clock_1 (.out(clock_1_out));
  J_K_Flip_Flop j_k_ff_1 (
    .J(contador_dec_1_j0), .clk(clock_1_out), .K(contador_dec_1_k0), .Q(j_k_ff_1_q));  // open: Qn, preset, en, reset
  J_K_Flip_Flop j_k_ff_2 (
    .J(contador_dec_1_j1), .clk(clock_1_out), .K(contador_dec_1_k1), .Q(j_k_ff_2_q));  // open: Qn, preset, en, reset
  J_K_Flip_Flop j_k_ff_3 (
    .J(contador_dec_1_j2), .clk(clock_1_out), .K(contador_dec_1_k2), .Q(j_k_ff_3_q));  // open: Qn, preset, en, reset
  J_K_Flip_Flop j_k_ff_4 (
    .J(contador_dec_1_j3), .clk(clock_1_out), .K(contador_dec_1_k3), .Q(j_k_ff_4_q));  // open: Qn, preset, en, reset
  contador_dec contador_dec_1 (
    .q3(j_k_ff_4_q), .q2(j_k_ff_3_q), .q1(j_k_ff_2_q), .q0(j_k_ff_1_q), .j3(contador_dec_1_j3),
    .k3(contador_dec_1_k3), .j2(contador_dec_1_j2), .k2(contador_dec_1_k2), .j1(contador_dec_1_j1),
    .k1(contador_dec_1_k1), .j0(contador_dec_1_j0), .k0(contador_dec_1_k0));
  cont_7_seg cont_7_seg_1 (
    .d4(j_k_ff_4_q), .d3(j_k_ff_3_q), .d2(j_k_ff_2_q), .d1(j_k_ff_1_q), .a(cont_7_seg_1_a),
    .b(cont_7_seg_1_b), .c(cont_7_seg_1_c), .d(cont_7_seg_1_d), .e(cont_7_seg_1_e), .f(cont_7_seg_1_f),
    .g(cont_7_seg_1_g));
  _7_Segment_Display u_7_segment_display_1 (
    .g(cont_7_seg_1_g), .f(cont_7_seg_1_f), .a(cont_7_seg_1_a), .b(cont_7_seg_1_b), .e(cont_7_seg_1_e),
    .d(cont_7_seg_1_d), .c(cont_7_seg_1_c));  // open: dp
endmodule

module contador_dec (
  input  q3,
  input  q2,
  input  q1,
  input  q0,
  output j3,
  output k3,
  output j2,
  output k2,
  output j1,
  output k1,
  output j0,
  output k0
);

  wire and_1_out, and_2_out, not_1_out, not_2_out;

  not not_1 (not_1_out, q2);
  not not_2 (not_2_out, q1);
  not not_3 (j1, q0);
  and and_1 (and_1_out, not_1_out, not_2_out);
  and and_2 (and_2_out, not_1_out, not_2_out);
  and and_3 (j2, not_2_out, j1);
  and and_4 (k2, not_2_out, j1);
  and and_5 (j3, and_1_out, j1);
  and and_6 (k3, and_2_out, j1);

  assign j0 = 1'b1;
  assign k0 = 1'b1;
  assign k1 = j1;
endmodule

module QuestaoC (
);

  wire clock_1_out, cont_7_seg_1_a, cont_7_seg_1_b, cont_7_seg_1_c, cont_7_seg_1_d, cont_7_seg_1_e,
       cont_7_seg_1_f, cont_7_seg_1_g, contador0_a_9_1_j0, contador0_a_9_1_j1, contador0_a_9_1_j2,
       contador0_a_9_1_j3, contador0_a_9_1_k0, contador0_a_9_1_k1, contador0_a_9_1_k2, contador0_a_9_1_k3,
       j_k_ff_1_q, j_k_ff_2_q, j_k_ff_3_q, j_k_ff_4_q;

  Clock clock_1 (.out(clock_1_out));
  J_K_Flip_Flop j_k_ff_1 (
    .J(contador0_a_9_1_j0), .clk(clock_1_out), .K(contador0_a_9_1_k0), .Q(j_k_ff_1_q));  // open: Qn, preset, en, reset
  J_K_Flip_Flop j_k_ff_2 (
    .J(contador0_a_9_1_j1), .clk(clock_1_out), .K(contador0_a_9_1_k1), .Q(j_k_ff_2_q));  // open: Qn, preset, en, reset
  J_K_Flip_Flop j_k_ff_3 (
    .J(contador0_a_9_1_j2), .clk(clock_1_out), .K(contador0_a_9_1_k2), .Q(j_k_ff_3_q));  // open: Qn, preset, en, reset
  J_K_Flip_Flop j_k_ff_4 (
    .J(contador0_a_9_1_j3), .clk(clock_1_out), .K(contador0_a_9_1_k3), .Q(j_k_ff_4_q));  // open: Qn, preset, en, reset
  contador0_a_9 contador0_a_9_1 (
    .q3(j_k_ff_4_q), .q2(j_k_ff_3_q), .q1(j_k_ff_2_q), .q0(j_k_ff_1_q), .j3(contador0_a_9_1_j3),
    .k3(contador0_a_9_1_k3), .j2(contador0_a_9_1_j2), .k2(contador0_a_9_1_k2), .j1(contador0_a_9_1_j1),
    .k1(contador0_a_9_1_k1), .j0(contador0_a_9_1_j0), .k0(contador0_a_9_1_k0));
  cont_7_seg cont_7_seg_1 (
    .d4(j_k_ff_4_q), .d3(j_k_ff_3_q), .d2(j_k_ff_2_q), .d1(j_k_ff_1_q), .a(cont_7_seg_1_a),
    .b(cont_7_seg_1_b), .c(cont_7_seg_1_c), .d(cont_7_seg_1_d), .e(cont_7_seg_1_e), .f(cont_7_seg_1_f),
    .g(cont_7_seg_1_g));
  _7_Segment_Display u_7_segment_display_1 (
    .g(cont_7_seg_1_g), .f(cont_7_seg_1_f), .a(cont_7_seg_1_a), .b(cont_7_seg_1_b), .e(cont_7_seg_1_e),
    .d(cont_7_seg_1_d), .c(cont_7_seg_1_c));  // open: dp
endmodule

module contador_9 (
  input  q0,
  input  q1,
  input  q2,
  input  q3,
  output j0,
  output k0,
  output j1,
  output k1,
  output j2,
  output k2,
  output j3,
  output k3
);

  wire and_4_out, not_1_out;

  and and_1 (j1, q0, not_1_out);
  not not_1 (not_1_out, q3);
  and and_2 (j2, q1, q0);
  and and_3 (k2, q1, q0);
  and and_4 (and_4_out, q0, q1);
  and and_5 (j3, and_4_out, q2);

  assign j0 = 1'b1;
  assign k0 = 1'b1;
  assign k1 = q0;
  assign k3 = q0;
endmodule

module contador0_a_9 (
  input  q3,
  input  q2,
  input  q1,
  input  q0,
  output j3,
  output k3,
  output j2,
  output k2,
  output j1,
  output k1,
  output j0,
  output k0
);

  wire and_1_out, not_1_out;

  and and_1 (and_1_out, q2, q1);
  and and_2 (j2, q1, q0);
  and and_3 (k2, q1, q0);
  not not_1 (not_1_out, q3);
  and and_4 (j1, not_1_out, q0);
  and and_5 (j3, and_1_out, q0);

  assign j0 = 1'b1;
  assign k0 = 1'b1;
  assign k1 = q0;
  assign k3 = q0;
endmodule

module QuestaoD (
);

  wire clock_1_out, cont_7_seg_1_a, cont_7_seg_1_b, cont_7_seg_1_c, cont_7_seg_1_d, cont_7_seg_1_e,
       cont_7_seg_1_f, cont_7_seg_1_g, contador0a3_10_13_1_j0, contador0a3_10_13_1_j1,
       contador0a3_10_13_1_j2, contador0a3_10_13_1_j3, contador0a3_10_13_1_k0, contador0a3_10_13_1_k1,
       contador0a3_10_13_1_k2, contador0a3_10_13_1_k3, j_k_ff_1_q, j_k_ff_2_q, j_k_ff_3_q, j_k_ff_4_q;

  Clock clock_1 (.out(clock_1_out));
  J_K_Flip_Flop j_k_ff_1 (
    .J(contador0a3_10_13_1_j0), .clk(clock_1_out), .K(contador0a3_10_13_1_k0), .Q(j_k_ff_1_q));  // open: Qn, preset, en, reset
  J_K_Flip_Flop j_k_ff_2 (
    .J(contador0a3_10_13_1_j1), .clk(clock_1_out), .K(contador0a3_10_13_1_k1), .Q(j_k_ff_2_q));  // open: Qn, preset, en, reset
  J_K_Flip_Flop j_k_ff_3 (
    .J(contador0a3_10_13_1_j2), .clk(clock_1_out), .K(contador0a3_10_13_1_k2), .Q(j_k_ff_3_q));  // open: Qn, preset, en, reset
  J_K_Flip_Flop j_k_ff_4 (
    .J(contador0a3_10_13_1_j3), .clk(clock_1_out), .K(contador0a3_10_13_1_k3), .Q(j_k_ff_4_q));  // open: Qn, preset, en, reset
  contador0a3_10_13 contador0a3_10_13_1 (
    .q3(j_k_ff_4_q), .q2(j_k_ff_3_q), .q1(j_k_ff_2_q), .q0(j_k_ff_1_q), .j3(contador0a3_10_13_1_j3),
    .k3(contador0a3_10_13_1_k3), .j2(contador0a3_10_13_1_j2), .k2(contador0a3_10_13_1_k2),
    .j1(contador0a3_10_13_1_j1), .k1(contador0a3_10_13_1_k1), .j0(contador0a3_10_13_1_j0),
    .k0(contador0a3_10_13_1_k0));
  cont_7_seg cont_7_seg_1 (
    .d4(j_k_ff_4_q), .d3(j_k_ff_3_q), .d2(j_k_ff_2_q), .d1(j_k_ff_1_q), .a(cont_7_seg_1_a),
    .b(cont_7_seg_1_b), .c(cont_7_seg_1_c), .d(cont_7_seg_1_d), .e(cont_7_seg_1_e), .f(cont_7_seg_1_f),
    .g(cont_7_seg_1_g));
  _7_Segment_Display u_7_segment_display_1 (
    .g(cont_7_seg_1_g), .f(cont_7_seg_1_f), .a(cont_7_seg_1_a), .b(cont_7_seg_1_b), .e(cont_7_seg_1_e),
    .d(cont_7_seg_1_d), .c(cont_7_seg_1_c));  // open: dp
endmodule

module contador0a3_10_13 (
  input  q3,
  input  q2,
  input  q1,
  input  q0,
  output j3,
  output k3,
  output j2,
  output k2,
  output j1,
  output k1,
  output j0,
  output k0
);

  wire and_4_out, and_5_out, and_6_out, and_7_out, and_8_out, and_9_out, and_10_out, and_11_out, not_1_out,
       not_2_out, not_3_out, not_4_out, not_5_out, or_2_out, or_3_out, or_4_out;

  not not_1 (not_1_out, q0);
  and and_1 (j3, q0, q1);
  and and_2 (k3, q0, q2);
  and and_3 (j2, q3, q1);
  and and_4 (and_4_out, q0, not_2_out);
  not not_2 (not_2_out, q3);
  not not_3 (not_3_out, q2);
  and and_5 (and_5_out, not_3_out, q0);
  and and_6 (and_6_out, q2, q3);
  and and_7 (and_7_out, q1, q0);
  and and_8 (and_8_out, q3, q0);
  not not_4 (not_4_out, q2);
  not not_5 (not_5_out, q3);
  or or_1 (k2, and_7_out, and_8_out);
  or or_2 (or_2_out, and_4_out, and_5_out);
  and and_9 (and_9_out, and_6_out, not_1_out);
  and and_10 (and_10_out, q0, q2);
  and and_11 (and_11_out, not_4_out, q3);
  or or_3 (or_3_out, not_5_out, not_4_out);
  or or_4 (or_4_out, not_5_out, q1);
  or or_5 (j1, or_2_out, and_9_out);
  or or_6 (k1, and_10_out, and_11_out);
  or or_7 (j0, or_3_out, q1);
  or or_8 (k0, or_4_out, q2);
endmodule

module QuestaoE (
);

  wire clock_1_out, cont_7_seg_1_a, cont_7_seg_1_b, cont_7_seg_1_c, cont_7_seg_1_d, cont_7_seg_1_e,
       cont_7_seg_1_f, cont_7_seg_1_g, contador_018_14_15_13_76_1_j0, contador_018_14_15_13_76_1_j1,
       contador_018_14_15_13_76_1_j2, contador_018_14_15_13_76_1_j3, contador_018_14_15_13_76_1_k0,
       contador_018_14_15_13_76_1_k1, contador_018_14_15_13_76_1_k2, contador_018_14_15_13_76_1_k3,
       j_k_ff_1_q, j_k_ff_2_q, j_k_ff_3_q, j_k_ff_4_q;

  Clock clock_1 (.out(clock_1_out));
  J_K_Flip_Flop j_k_ff_1 (
    .J(contador_018_14_15_13_76_1_j0), .clk(clock_1_out), .K(contador_018_14_15_13_76_1_k0), .Q(j_k_ff_1_q));  // open: Qn, preset, en, reset
  J_K_Flip_Flop j_k_ff_2 (
    .J(contador_018_14_15_13_76_1_j1), .clk(clock_1_out), .K(contador_018_14_15_13_76_1_k1), .Q(j_k_ff_2_q));  // open: Qn, preset, en, reset
  J_K_Flip_Flop j_k_ff_3 (
    .J(contador_018_14_15_13_76_1_j2), .clk(clock_1_out), .K(contador_018_14_15_13_76_1_k2), .Q(j_k_ff_3_q));  // open: Qn, preset, en, reset
  J_K_Flip_Flop j_k_ff_4 (
    .J(contador_018_14_15_13_76_1_j3), .clk(clock_1_out), .K(contador_018_14_15_13_76_1_k3), .Q(j_k_ff_4_q));  // open: Qn, preset, en, reset
  contador_018_14_15_13_76 contador_018_14_15_13_76_1 (
    .q3(j_k_ff_4_q), .q2(j_k_ff_3_q), .j3(contador_018_14_15_13_76_1_j3), .q1(j_k_ff_2_q), .q0(j_k_ff_1_q),
    .k3(contador_018_14_15_13_76_1_k3), .j2(contador_018_14_15_13_76_1_j2),
    .k2(contador_018_14_15_13_76_1_k2), .j1(contador_018_14_15_13_76_1_j1),
    .k1(contador_018_14_15_13_76_1_k1), .j0(contador_018_14_15_13_76_1_j0), .k0(contador_018_14_15_13_76_1_k0));
  cont_7_seg cont_7_seg_1 (
    .d4(j_k_ff_4_q), .d3(j_k_ff_3_q), .d2(j_k_ff_2_q), .d1(j_k_ff_1_q), .a(cont_7_seg_1_a),
    .b(cont_7_seg_1_b), .c(cont_7_seg_1_c), .d(cont_7_seg_1_d), .e(cont_7_seg_1_e), .f(cont_7_seg_1_f),
    .g(cont_7_seg_1_g));
  _7_Segment_Display u_7_segment_display_1 (
    .g(cont_7_seg_1_g), .f(cont_7_seg_1_f), .a(cont_7_seg_1_a), .b(cont_7_seg_1_b), .e(cont_7_seg_1_e),
    .d(cont_7_seg_1_d), .c(cont_7_seg_1_c));  // open: dp
endmodule

module contador_018_14_15_13_76 (
  input  q3,
  input  q2,
  input  q1,
  input  q0,
  output j3,
  output k3,
  output j2,
  output k2,
  output j1,
  output k1,
  output j0,
  output k0
);

  wire and_1_out, and_2_out, and_3_out, and_4_out, and_5_out, and_6_out, and_7_out, and_8_out, and_9_out,
       and_10_out, and_11_out, and_12_out, and_13_out, and_14_out, and_15_out, and_16_out, and_17_out,
       and_18_out, and_19_out, and_20_out, and_21_out, and_23_out, and_24_out, and_25_out, and_26_out,
       not_1_out, not_2_out, not_3_out, not_4_out, not_5_out, not_6_out, not_7_out, not_8_out, not_9_out,
       not_10_out, not_11_out, not_12_out, not_13_out, not_14_out, not_15_out, not_16_out, not_17_out,
       not_18_out, not_19_out, not_20_out, not_21_out, not_22_out, not_23_out, not_24_out, not_25_out,
       not_26_out, not_27_out, not_28_out, not_29_out, not_30_out, not_31_out, not_32_out, or_1_out,
       or_2_out, or_3_out, or_4_out, or_5_out, or_6_out;

  not not_1 (not_1_out, q3);
  and and_1 (and_1_out, not_1_out, not_2_out);
  not not_2 (not_2_out, q2);
  not not_3 (not_3_out, q1);
  and and_2 (and_2_out, not_3_out, q0);
  and and_3 (and_3_out, q3, not_4_out);
  not not_4 (not_4_out, q2);
  not not_5 (not_5_out, q1);
  and and_4 (and_4_out, not_5_out, not_6_out);
  not not_6 (not_6_out, q0);
  not not_7 (not_7_out, q2);
  and and_5 (and_5_out, not_7_out, q0);
  not not_8 (not_8_out, q2);
  and and_6 (and_6_out, not_8_out, q1);
  not not_9 (not_9_out, q1);
  and and_7 (and_7_out, q3, not_10_out);
  not not_10 (not_10_out, q2);
  not not_11 (not_11_out, q1);
  and and_8 (and_8_out, not_11_out, not_12_out);
  not not_12 (not_12_out, q0);
  not not_13 (not_13_out, q3);
  and and_9 (and_9_out, not_13_out, not_14_out);
  not not_14 (not_14_out, q1);
  not not_15 (not_15_out, q3);
  and and_10 (and_10_out, not_15_out, not_16_out);
  not not_16 (not_16_out, q0);
  not not_17 (not_17_out, q2);
  not not_18 (not_18_out, q1);
  and and_11 (and_11_out, not_18_out, not_19_out);
  not not_19 (not_19_out, q0);
  and and_12 (and_12_out, q3, not_20_out);
  not not_20 (not_20_out, q2);
  not not_21 (not_21_out, q1);
  and and_13 (and_13_out, not_21_out, not_22_out);
  not not_22 (not_22_out, q0);
  and and_14 (and_14_out, q3, q2);
  not not_23 (not_23_out, q3);
  and and_15 (and_15_out, not_23_out, not_24_out);
  not not_24 (not_24_out, q0);
  not not_25 (not_25_out, q2);
  not not_26 (not_26_out, q1);
  and and_16 (and_16_out, q3, q0);
  not not_27 (not_27_out, q3);
  and and_17 (and_17_out, not_27_out, not_28_out);
  not not_28 (not_28_out, q2);
  not not_29 (not_29_out, q1);
  and and_18 (and_18_out, q3, q2);
  not not_30 (not_30_out, q3);
  or or_1 (or_1_out, not_30_out, not_31_out);
  not not_31 (not_31_out, q2);
  not not_32 (not_32_out, q0);
  and and_19 (and_19_out, and_1_out, and_2_out);
  and and_20 (and_20_out, and_3_out, and_4_out);
  or or_2 (or_2_out, and_5_out, and_6_out);
  and and_21 (and_21_out, q2, not_9_out);
  and and_22 (j2, and_7_out, and_8_out);
  or or_3 (or_3_out, and_9_out, and_10_out);
  or or_4 (or_4_out, not_17_out, and_11_out);
  and and_23 (and_23_out, and_12_out, and_13_out);
  and and_24 (and_24_out, and_14_out, q0);
  or or_5 (or_5_out, and_15_out, not_25_out);
  or or_6 (or_6_out, not_26_out, and_16_out);
  and and_25 (and_25_out, and_17_out, not_29_out);
  and and_26 (and_26_out, and_18_out, q1);
  or or_7 (k0, or_1_out, not_32_out);
  or or_8 (j3, and_19_out, and_20_out);
  or or_9 (k3, or_2_out, and_21_out);
  or or_10 (k2, or_3_out, or_4_out);
  or or_11 (j1, and_23_out, and_24_out);
  or or_12 (k1, or_5_out, or_6_out);
  or or_13 (j0, and_25_out, and_26_out);
endmodule
